// Logisim project F_step.circ as structural Verilog: 53 circuits, main circuit yihuomen
module huomen (
  input  in_1,
  input  in_2,
  output out_3,
  output out_4
);

  wire not_1_out, not_2_out, transistor_1_out, transistor_2_out;

  Transistor #(.\type ("n")) transistor_1 (.in(1'b1), .out(transistor_1_out), .gate(in_1));
  Transistor #(.\type ("n")) transistor_2 (.out(transistor_2_out), .gate(in_2));  // open: in
  Transistor transistor_3 (.gate(in_1));  // open: in, out
  Transistor #(.\type ("n")) transistor_4 (.gate(in_2));  // open: in, out
  // NAND_Gate nand_1 is placed but not wired
  not not_1 (not_1_out, in_1);
  not not_2 (not_2_out, in_2);
  // NOT_Gate not_3 is placed but not wired
  nand nand_2 (out_3, not_1_out, not_2_out);

  // Notes on the sheet:
  //   或门
  //   与非门
  //   非门
  //   0
  //   0
  //   1
  //   0
  //   1
  //   1
  //   0
  //   1
  //   0
  //   1
  //   1
  //   1
endmodule

module tonghuomen (
  input  in_1,
  input  in_2,
  output out_3
);

  wire and_1_out, and_2_out, not_1_out, not_2_out, or_1_out;

  not not_1 (not_1_out, in_1);
  not not_2 (not_2_out, in_2);
  and and_1 (and_1_out, not_1_out, in_2);
  and and_2 (and_2_out, in_1, not_2_out);
  or or_1 (or_1_out, and_1_out, and_2_out);
  not not_3 (out_3, or_1_out);
endmodule

module Two_4yimaqi (
  input  A0,
  input  A1,
  output Y3,
  output Y2,
  output Y1,
  output Y0
);

  wire not_1_out, not_2_out;

  not not_1 (not_1_out, A0);
  not not_2 (not_2_out, A1);
  and and_1 (Y3, A0, A1);
  and and_2 (Y2, A0, not_2_out);
  and and_3 (Y1, not_1_out, A1);
  and and_4 (Y0, not_1_out, not_2_out);
endmodule

module Three_8yimaqi_with2_4yimaqi (
  input  A0,
  input  A1,
  input  A2,
  output Y0,
  output Y1,
  output Y2,
  output Y3,
  output Y4,
  output Y5,
  output Y6,
  output Y7
);

  wire not_1_out, two_4yimaqi_1_y0, two_4yimaqi_1_y1, two_4yimaqi_1_y2, two_4yimaqi_1_y3;

  Two_4yimaqi two_4yimaqi_1 (
    .A0(A0), .A1(A1), .Y3(two_4yimaqi_1_y3), .Y2(two_4yimaqi_1_y2), .Y1(two_4yimaqi_1_y1),
    .Y0(two_4yimaqi_1_y0));
  not not_1 (not_1_out, A2);
  and and_1 (Y0, two_4yimaqi_1_y3, A2);
  and and_2 (Y1, two_4yimaqi_1_y3, not_1_out);
  and and_3 (Y2, two_4yimaqi_1_y2, A2);
  and and_4 (Y3, two_4yimaqi_1_y2, not_1_out);
  and and_5 (Y4, two_4yimaqi_1_y1, A2);
  and and_6 (Y5, two_4yimaqi_1_y1, not_1_out);
  and and_7 (Y6, two_4yimaqi_1_y0, A2);
  and and_8 (Y7, two_4yimaqi_1_y0, not_1_out);
endmodule

module yihuomen (
  input  in_1,
  input  in_2,
  output out_3
);

  wire and_1_out, and_2_out, not_1_out, not_2_out;

  not not_1 (not_1_out, in_1);
  not not_2 (not_2_out, in_2);
  and and_1 (and_1_out, not_1_out, in_2);
  and and_2 (and_2_out, in_1, not_2_out);
  or or_1 (out_3, and_1_out, and_2_out);
endmodule

module Three_8yimaqi_NO2_4yimaqi (
  input  A2,
  input  A1,
  input  A0,
  output Y0,
  output Y1,
  output Y2,
  output Y3,
  output Y4,
  output Y5,
  output Y6,
  output Y7
);

  wire not_1_out, not_2_out, not_3_out;

  not not_1 (not_1_out, A2);
  not not_2 (not_2_out, A1);
  not not_3 (not_3_out, A0);
  and and_1 (Y0, A2, A1, A0);
  and and_2 (Y1, A2, A1, not_3_out);
  and and_3 (Y2, A2, not_2_out, A0);
  and and_4 (Y3, A2, not_2_out, not_3_out);
  and and_5 (Y4, not_1_out, A1, A0);
  and and_6 (Y5, not_1_out, A1, not_3_out);
  and and_7 (Y6, not_1_out, not_2_out, A0);
  and and_8 (Y7, not_1_out, not_2_out, not_3_out);
endmodule

module test_yimaqi (
  input  in_1,
  input  in_2,
  input  in_3,
  input  in_4,
  input  in_5,
  input  in_6,
  output out_7,
  output out_8,
  output out_9,
  output out_10,
  output out_11,
  output out_12,
  output out_13,
  output out_14,
  output out_15,
  output out_16,
  output out_17,
  output out_18,
  output out_19,
  output out_20,
  output out_21,
  output out_22
);

  Three_8yimaqi_NO2_4yimaqi three_8yimaqi_no2_4yimaqi_1 (
    .A2(in_1), .A1(in_2), .A0(in_3), .Y0(out_7), .Y1(out_8), .Y2(out_9), .Y3(out_10), .Y4(out_11),
    .Y5(out_12), .Y6(out_13), .Y7(out_14));
  Three_8yimaqi_with2_4yimaqi three_8yimaqi_with2_4yimaqi_1 (
    .A0(in_4), .A1(in_5), .A2(in_6), .Y0(out_15), .Y1(out_16), .Y2(out_17), .Y3(out_18), .Y4(out_19),
    .Y5(out_20), .Y6(out_21), .Y7(out_22));
endmodule

module shumaguan_10jinzhi_qudongdianlu (
  input  in_1,
  input  in_2,
  input  in_3,
  input  in_4,
  output BBB,
  output AAA,
  output FFF,
  output GGG,
  output EEE,
  output DDD,
  output CCC,
  output HHH
);

  wire and_1_out, and_2_out, and_3_out, and_4_out, and_5_out, and_6_out, and_7_out, and_8_out, and_9_out,
       and_10_out, and_11_out, and_12_out, and_13_out, and_14_out, and_15_out, and_16_out, not_1_out,
       not_2_out, not_3_out, not_4_out, undriven, undriven_2, undriven_3, undriven_4, undriven_5, undriven_6,
       undriven_7, undriven_8;

  not not_1 (not_1_out, in_1);
  not not_2 (not_2_out, in_2);
  not not_3 (not_3_out, in_3);
  not not_4 (not_4_out, in_4);
  and and_1 (and_1_out, in_1, in_2, in_3, in_4);
  and and_2 (and_2_out, in_1, in_2, in_3, not_4_out);
  and and_3 (and_3_out, in_1, in_2, not_3_out, in_4);
  and and_4 (and_4_out, in_1, in_2, not_3_out, not_4_out);
  and and_5 (and_5_out, in_1, not_2_out, in_3, in_4);
  and and_6 (and_6_out, in_1, not_2_out, in_3, not_4_out);
  and and_7 (and_7_out, in_1, not_2_out, not_3_out, in_4);
  and and_8 (and_8_out, in_1, not_2_out, not_3_out, not_4_out);
  and and_9 (and_9_out, not_1_out, in_2, in_3, in_4);
  and and_10 (and_10_out, not_1_out, in_2, in_3, not_4_out);
  and and_11 (and_11_out, not_1_out, in_2, not_3_out, in_4);
  and and_12 (and_12_out, not_1_out, in_2, not_3_out, not_4_out);
  and and_13 (and_13_out, not_1_out, not_2_out, in_3, in_4);
  and and_14 (and_14_out, not_1_out, not_2_out, in_3, not_4_out);
  and and_15 (and_15_out, not_1_out, not_2_out, not_3_out, in_4);
  and and_16 (and_16_out, not_1_out, not_2_out, not_3_out, not_4_out);
  or a (AAA, and_7_out, and_8_out, and_9_out, and_10_out, and_11_out, and_16_out, and_13_out, and_14_out, and_16_out, and_16_out);
  or b (BBB, and_7_out, and_8_out, and_9_out, and_16_out, and_16_out, and_12_out, and_13_out, and_14_out, and_15_out, and_16_out);
  or c (CCC, and_7_out, and_8_out, and_9_out, and_10_out, and_11_out, and_12_out, and_13_out, and_16_out, and_15_out, and_16_out);
  or d (DDD, and_7_out, and_8_out, and_16_out, and_10_out, and_11_out, and_16_out, and_13_out, and_14_out, and_16_out, and_16_out);
  or e (EEE, and_16_out, and_8_out, and_16_out, and_10_out, and_16_out, and_16_out, and_16_out, and_14_out, and_16_out, and_16_out);
  or f (FFF, and_7_out, and_8_out, and_10_out, and_11_out, and_12_out, and_16_out, and_16_out, and_16_out, and_16_out, and_16_out);
  or g (GGG, and_7_out, and_8_out, and_10_out, and_10_out, and_11_out, and_12_out, and_13_out, and_14_out, and_14_out, and_14_out);
  or or_1 (HHH, and_1_out, and_2_out, and_3_out, and_4_out, and_5_out, and_6_out);
  _7_Segment_Display u_7_segment_display_1 (
    .g(undriven), .f(undriven_2), .a(undriven_5), .b(undriven_8), .e(undriven_3), .d(undriven_4),
    .c(undriven_6), .dp(undriven_7));

  // Notes on the sheet:
  //   A
  //   F
  //   G
  //   E
  //   D
  //   C
  //   B
  //   H
endmodule

module shumaguan_16jinzhi_qudongdianlu (
  input  in_1,
  input  in_2,
  input  in_3,
  input  in_4,
  output BBB,
  output AAA,
  output FFF,
  output GGG,
  output EEE,
  output DDD,
  output CCC,
  output HHH
);

  wire and_2_out, and_3_out, and_4_out, and_5_out, and_6_out, and_7_out, and_8_out, and_9_out, and_10_out,
       and_11_out, and_12_out, and_13_out, and_14_out, and_15_out, and_16_out, not_1_out, not_2_out,
       not_3_out, not_4_out, undriven, undriven_2, undriven_3, undriven_4, undriven_5, undriven_6,
       undriven_7, undriven_8;

  not not_1 (not_1_out, in_1);
  not not_2 (not_2_out, in_2);
  not not_3 (not_3_out, in_3);
  not not_4 (not_4_out, in_4);
  and and_1 (HHH, in_1, in_2, in_3, in_4);
  and and_2 (and_2_out, in_1, in_2, in_3, not_4_out);
  and and_3 (and_3_out, in_1, in_2, not_3_out, in_4);
  and and_4 (and_4_out, in_1, in_2, not_3_out, not_4_out);
  and and_5 (and_5_out, in_1, not_2_out, in_3, in_4);
  and and_6 (and_6_out, in_1, not_2_out, in_3, not_4_out);
  and and_7 (and_7_out, in_1, not_2_out, not_3_out, in_4);
  and and_8 (and_8_out, in_1, not_2_out, not_3_out, not_4_out);
  and and_9 (and_9_out, not_1_out, in_2, in_3, in_4);
  and and_10 (and_10_out, not_1_out, in_2, in_3, not_4_out);
  and and_11 (and_11_out, not_1_out, in_2, not_3_out, in_4);
  and and_12 (and_12_out, not_1_out, in_2, not_3_out, not_4_out);
  and and_13 (and_13_out, not_1_out, not_2_out, in_3, in_4);
  and and_14 (and_14_out, not_1_out, not_2_out, in_3, not_4_out);
  and and_15 (and_15_out, not_1_out, not_2_out, not_3_out, in_4);
  and and_16 (and_16_out, not_1_out, not_2_out, not_3_out, not_4_out);
  or a (AAA, HHH, and_2_out, and_6_out, and_7_out, and_8_out, and_9_out, and_10_out, and_11_out, and_13_out, and_14_out, and_16_out);
  or b (BBB, and_3_out, and_6_out, and_7_out, and_8_out, and_9_out, and_12_out, and_13_out, and_14_out, and_15_out, and_16_out);
  or c (CCC, and_3_out, and_5_out, and_6_out, and_7_out, and_8_out, and_9_out, and_10_out, and_11_out, and_12_out, and_13_out, and_15_out, and_16_out);
  or d (DDD, and_2_out, and_3_out, and_4_out, and_5_out, and_7_out, and_8_out, and_10_out, and_11_out, and_13_out, and_14_out, and_16_out);
  or e (EEE, HHH, and_2_out, and_3_out, and_4_out, and_5_out, and_6_out, and_8_out, and_10_out, and_14_out, and_16_out);
  or f (FFF, HHH, and_2_out, and_5_out, and_6_out, and_7_out, and_8_out, and_10_out, and_11_out, and_12_out, and_16_out);
  or g (GGG, HHH, and_2_out, and_3_out, and_4_out, and_5_out, and_6_out, and_7_out, and_8_out, and_10_out, and_11_out, and_12_out, and_13_out, and_14_out);
  _7_Segment_Display u_7_segment_display_1 (
    .g(undriven), .f(undriven_2), .a(undriven_5), .b(undriven_8), .e(undriven_3), .d(undriven_4),
    .c(undriven_6), .dp(undriven_7));

  // Notes on the sheet:
  //   G
  //   E
  //   F
  //   A
  //   B
  //   H
  //   D
  //   C
endmodule

module bianmaqi_with7guan (
  input  I15,
  input  I14,
  input  I13,
  input  I12,
  input  I11,
  input  I10,
  input  I9,
  input  I8,
  input  I7,
  input  I6,
  input  I5,
  input  I4,
  input  I3,
  input  I2,
  input  I1,
  input  I0
);

  wire or_1_out, or_2_out, or_3_out, or_4_out, shumaguan_16jinzhi_qudongdianlu_1_aaa,
       shumaguan_16jinzhi_qudongdianlu_1_bbb, shumaguan_16jinzhi_qudongdianlu_1_ccc,
       shumaguan_16jinzhi_qudongdianlu_1_ddd, shumaguan_16jinzhi_qudongdianlu_1_eee,
       shumaguan_16jinzhi_qudongdianlu_1_fff, shumaguan_16jinzhi_qudongdianlu_1_ggg,
       shumaguan_16jinzhi_qudongdianlu_1_hhh;

  or or_1 (or_1_out, I15, I14, I13, I12, I11, I10, I9, I8);
  or or_2 (or_2_out, I15, I14, I13, I12, I7, I6, I5, I4);
  or or_3 (or_3_out, I15, I14, I11, I10, I7, I6, I3, I2);
  or or_4 (or_4_out, I15, I13, I11, I9, I7, I5, I3, I1);
  shumaguan_16jinzhi_qudongdianlu shumaguan_16jinzhi_qudongdianlu_1 (
    .in_1(or_1_out), .in_2(or_2_out), .in_3(or_3_out), .in_4(or_4_out),
    .BBB(shumaguan_16jinzhi_qudongdianlu_1_bbb), .AAA(shumaguan_16jinzhi_qudongdianlu_1_aaa),
    .FFF(shumaguan_16jinzhi_qudongdianlu_1_fff), .GGG(shumaguan_16jinzhi_qudongdianlu_1_ggg),
    .EEE(shumaguan_16jinzhi_qudongdianlu_1_eee), .DDD(shumaguan_16jinzhi_qudongdianlu_1_ddd),
    .CCC(shumaguan_16jinzhi_qudongdianlu_1_ccc), .HHH(shumaguan_16jinzhi_qudongdianlu_1_hhh));
  _7_Segment_Display u_7_segment_display_1 (
    .g(shumaguan_16jinzhi_qudongdianlu_1_ggg), .f(shumaguan_16jinzhi_qudongdianlu_1_fff),
    .a(shumaguan_16jinzhi_qudongdianlu_1_aaa), .b(shumaguan_16jinzhi_qudongdianlu_1_bbb),
    .e(shumaguan_16jinzhi_qudongdianlu_1_eee), .d(shumaguan_16jinzhi_qudongdianlu_1_ddd),
    .c(shumaguan_16jinzhi_qudongdianlu_1_ccc), .dp(shumaguan_16jinzhi_qudongdianlu_1_hhh));

  // Notes on the sheet:
  //   Y3
  //   Y2
  //   Y1
  //   Y0
endmodule

module TEST_bianmaqi (
);

  wire bianmaqi_zidianlu_1_y0, bianmaqi_zidianlu_1_y1, bianmaqi_zidianlu_1_y2, bianmaqi_zidianlu_1_y3,
       dipswitch_1_p1, dipswitch_1_p2, dipswitch_1_p3, dipswitch_1_p4, dipswitch_1_p5, dipswitch_1_p6,
       dipswitch_1_p7, dipswitch_1_p8, dipswitch_1_p9, dipswitch_1_p10, dipswitch_1_p11, dipswitch_1_p12,
       dipswitch_1_p13, dipswitch_1_p14, dipswitch_1_p15, dipswitch_1_p16,
       shumaguan_16jinzhi_qudongdianlu_1_aaa, shumaguan_16jinzhi_qudongdianlu_1_bbb,
       shumaguan_16jinzhi_qudongdianlu_1_ccc, shumaguan_16jinzhi_qudongdianlu_1_ddd,
       shumaguan_16jinzhi_qudongdianlu_1_eee, shumaguan_16jinzhi_qudongdianlu_1_fff,
       shumaguan_16jinzhi_qudongdianlu_1_ggg, shumaguan_16jinzhi_qudongdianlu_1_hhh;

  // DipSwitch #(.number(16)) dipswitch_1: pin names not known; wires that end beside it: dipswitch_1_p1, dipswitch_1_p2, dipswitch_1_p3, dipswitch_1_p4, dipswitch_1_p5, dipswitch_1_p6, dipswitch_1_p7, dipswitch_1_p8, dipswitch_1_p9, dipswitch_1_p10, dipswitch_1_p11, dipswitch_1_p12, dipswitch_1_p13, dipswitch_1_p14, dipswitch_1_p15, dipswitch_1_p16
  bianmaqi_zidianlu bianmaqi_zidianlu_1 (
    .I15(dipswitch_1_p16), .I14(dipswitch_1_p15), .I13(dipswitch_1_p14), .I12(dipswitch_1_p13),
    .I11(dipswitch_1_p12), .I10(dipswitch_1_p11), .I9(dipswitch_1_p10), .I8(dipswitch_1_p9),
    .I7(dipswitch_1_p8), .I6(dipswitch_1_p7), .I5(dipswitch_1_p6), .I4(dipswitch_1_p5), .I3(dipswitch_1_p4),
    .I2(dipswitch_1_p3), .I1(dipswitch_1_p2), .I0(dipswitch_1_p1), .Y3(bianmaqi_zidianlu_1_y3),
    .Y2(bianmaqi_zidianlu_1_y2), .Y1(bianmaqi_zidianlu_1_y1), .Y0(bianmaqi_zidianlu_1_y0));
  shumaguan_16jinzhi_qudongdianlu shumaguan_16jinzhi_qudongdianlu_1 (
    .in_1(bianmaqi_zidianlu_1_y3), .in_2(bianmaqi_zidianlu_1_y2), .in_3(bianmaqi_zidianlu_1_y1),
    .in_4(bianmaqi_zidianlu_1_y0), .BBB(shumaguan_16jinzhi_qudongdianlu_1_bbb),
    .AAA(shumaguan_16jinzhi_qudongdianlu_1_aaa), .FFF(shumaguan_16jinzhi_qudongdianlu_1_fff),
    .GGG(shumaguan_16jinzhi_qudongdianlu_1_ggg), .EEE(shumaguan_16jinzhi_qudongdianlu_1_eee),
    .DDD(shumaguan_16jinzhi_qudongdianlu_1_ddd), .CCC(shumaguan_16jinzhi_qudongdianlu_1_ccc),
    .HHH(shumaguan_16jinzhi_qudongdianlu_1_hhh));
  _7_Segment_Display u_7_segment_display_1 (
    .g(shumaguan_16jinzhi_qudongdianlu_1_ggg), .f(shumaguan_16jinzhi_qudongdianlu_1_fff),
    .a(shumaguan_16jinzhi_qudongdianlu_1_aaa), .b(shumaguan_16jinzhi_qudongdianlu_1_bbb),
    .e(shumaguan_16jinzhi_qudongdianlu_1_eee), .d(shumaguan_16jinzhi_qudongdianlu_1_ddd),
    .c(shumaguan_16jinzhi_qudongdianlu_1_ccc), .dp(shumaguan_16jinzhi_qudongdianlu_1_hhh));
endmodule

module bianmaqi_zidianlu (
  input  I15,
  input  I14,
  input  I13,
  input  I12,
  input  I11,
  input  I10,
  input  I9,
  input  I8,
  input  I7,
  input  I6,
  input  I5,
  input  I4,
  input  I3,
  input  I2,
  input  I1,
  input  I0,
  output Y3,
  output Y2,
  output Y1,
  output Y0
);

  or or_1 (Y3, I15, I14, I13, I12, I11, I10, I9, I8);
  or or_2 (Y2, I15, I14, I13, I12, I7, I6, I5, I4);
  or or_3 (Y1, I15, I14, I11, I10, I7, I6, I3, I2);
  or or_4 (Y0, I15, I13, I11, I9, I7, I5, I3, I1);
endmodule

module four_2youxianbianmaqi (
  input  A3,
  input  A2,
  input  A1,
  input  A0,
  output Y1,
  output Y0,
  output GS
);

  wire and_1_out, and_2_out, not_1_out, not_2_out, not_3_out;

  not not_1 (not_1_out, A3);
  not not_2 (not_2_out, A3);
  not not_3 (not_3_out, A2);
  and and_1 (and_1_out, not_1_out, A2);
  and and_2 (and_2_out, not_2_out, not_3_out, A1);
  or or_1 (Y1, A3, and_1_out);
  or or_2 (Y0, A3, and_2_out);
  or or_3 (GS, A3, and_1_out, A0, A3, and_2_out);
endmodule

module shiliu_4youxianbianmaqi (
  input  in_1,
  input  in_2,
  input  in_3,
  input  in_4,
  input  in_5,
  input  in_6,
  input  in_7,
  input  in_8,
  input  in_9,
  input  in_10,
  input  in_11,
  input  in_12,
  input  in_13,
  input  in_14,
  input  in_15,
  input  in_16
);

  wire four_2youxianbianmaqi_1_gs, four_2youxianbianmaqi_1_y0, four_2youxianbianmaqi_1_y1,
       four_2youxianbianmaqi_2_gs, four_2youxianbianmaqi_2_y0, four_2youxianbianmaqi_2_y1,
       four_2youxianbianmaqi_3_gs, four_2youxianbianmaqi_3_y0, four_2youxianbianmaqi_3_y1,
       four_2youxianbianmaqi_4_gs, four_2youxianbianmaqi_4_y0, four_2youxianbianmaqi_4_y1,
       four_2youxianbianmaqi_5_y0, four_2youxianbianmaqi_5_y1, four_choose2_1_y, four_choose2_2_y,
       shumaguan_16jinzhi_qudongdianlu_1_aaa, shumaguan_16jinzhi_qudongdianlu_1_bbb,
       shumaguan_16jinzhi_qudongdianlu_1_ccc, shumaguan_16jinzhi_qudongdianlu_1_ddd,
       shumaguan_16jinzhi_qudongdianlu_1_eee, shumaguan_16jinzhi_qudongdianlu_1_fff,
       shumaguan_16jinzhi_qudongdianlu_1_ggg, shumaguan_16jinzhi_qudongdianlu_1_hhh;

  four_2youxianbianmaqi four_2youxianbianmaqi_1 (
    .A3(in_1), .A2(in_2), .A1(in_3), .A0(in_4), .Y1(four_2youxianbianmaqi_1_y1),
    .Y0(four_2youxianbianmaqi_1_y0), .GS(four_2youxianbianmaqi_1_gs));
  four_2youxianbianmaqi four_2youxianbianmaqi_2 (
    .A3(in_5), .A2(in_6), .A1(in_7), .A0(in_8), .Y1(four_2youxianbianmaqi_2_y1),
    .Y0(four_2youxianbianmaqi_2_y0), .GS(four_2youxianbianmaqi_2_gs));
  four_2youxianbianmaqi four_2youxianbianmaqi_3 (
    .A3(in_9), .A2(in_10), .A1(in_11), .A0(in_12), .Y1(four_2youxianbianmaqi_3_y1),
    .Y0(four_2youxianbianmaqi_3_y0), .GS(four_2youxianbianmaqi_3_gs));
  four_2youxianbianmaqi four_2youxianbianmaqi_4 (
    .A3(in_13), .A2(in_14), .A1(in_15), .A0(in_16), .Y1(four_2youxianbianmaqi_4_y1),
    .Y0(four_2youxianbianmaqi_4_y0), .GS(four_2youxianbianmaqi_4_gs));
  four_2youxianbianmaqi four_2youxianbianmaqi_5 (
    .A3(four_2youxianbianmaqi_1_gs), .A2(four_2youxianbianmaqi_2_gs), .A1(four_2youxianbianmaqi_3_gs),
    .A0(four_2youxianbianmaqi_4_gs), .Y1(four_2youxianbianmaqi_5_y1), .Y0(four_2youxianbianmaqi_5_y0));  // open: GS
  shumaguan_16jinzhi_qudongdianlu shumaguan_16jinzhi_qudongdianlu_1 (
    .in_1(four_2youxianbianmaqi_5_y1), .in_2(four_2youxianbianmaqi_5_y0), .in_3(four_choose2_2_y),
    .in_4(four_choose2_1_y), .BBB(shumaguan_16jinzhi_qudongdianlu_1_bbb),
    .AAA(shumaguan_16jinzhi_qudongdianlu_1_aaa), .FFF(shumaguan_16jinzhi_qudongdianlu_1_fff),
    .GGG(shumaguan_16jinzhi_qudongdianlu_1_ggg), .EEE(shumaguan_16jinzhi_qudongdianlu_1_eee),
    .DDD(shumaguan_16jinzhi_qudongdianlu_1_ddd), .CCC(shumaguan_16jinzhi_qudongdianlu_1_ccc),
    .HHH(shumaguan_16jinzhi_qudongdianlu_1_hhh));
  FOUR_choose2 four_choose2_1 (
    .A3(four_2youxianbianmaqi_1_y0), .A2(four_2youxianbianmaqi_2_y0), .A1(four_2youxianbianmaqi_3_y0),
    .A0(four_2youxianbianmaqi_4_y0), .SEL1(four_2youxianbianmaqi_5_y1), .SEL0(four_2youxianbianmaqi_5_y0),
    .Y(four_choose2_1_y));
  FOUR_choose2 four_choose2_2 (
    .A3(four_2youxianbianmaqi_1_y1), .A2(four_2youxianbianmaqi_2_y1), .A1(four_2youxianbianmaqi_3_y1),
    .A0(four_2youxianbianmaqi_4_y1), .SEL1(four_2youxianbianmaqi_5_y1), .SEL0(four_2youxianbianmaqi_5_y0),
    .Y(four_choose2_2_y));
  _7_Segment_Display u_7_segment_display_1 (
    .g(shumaguan_16jinzhi_qudongdianlu_1_ggg), .f(shumaguan_16jinzhi_qudongdianlu_1_fff),
    .a(shumaguan_16jinzhi_qudongdianlu_1_aaa), .b(shumaguan_16jinzhi_qudongdianlu_1_bbb),
    .e(shumaguan_16jinzhi_qudongdianlu_1_eee), .d(shumaguan_16jinzhi_qudongdianlu_1_ddd),
    .c(shumaguan_16jinzhi_qudongdianlu_1_ccc), .dp(shumaguan_16jinzhi_qudongdianlu_1_hhh));
endmodule

module ONE_wei2chosse1xuanzeqi (
  input  in_1,
  output out_2,
  output out_3
);

  not not_1 (out_3, in_1);

  assign out_2 = in_1;
endmodule

module TWO_choose1 (
  input  A,
  input  SEL,
  input  B,
  output Y
);

  wire and_1_out, and_2_out, not_1_out;

  not not_1 (not_1_out, SEL);
  and and_1 (and_1_out, B, not_1_out);
  and and_2 (and_2_out, A, SEL);
  or or_1 (Y, and_2_out, and_1_out);
endmodule

module FOUR_choose2 (
  input  A3,
  input  A2,
  input  A1,
  input  A0,
  input  SEL1,
  input  SEL0,
  output Y
);

  wire and_1_out, and_2_out, and_3_out, and_4_out, and_5_out, and_6_out, and_7_out, and_8_out, not_1_out,
       not_2_out;

  not not_1 (not_1_out, SEL1);
  not not_2 (not_2_out, SEL0);
  and and_1 (and_1_out, SEL1, SEL0);
  and and_2 (and_2_out, SEL1, not_2_out);
  and and_3 (and_3_out, not_1_out, SEL0);
  and and_4 (and_4_out, not_1_out, not_2_out);
  and and_5 (and_5_out, A2, and_2_out);
  and and_6 (and_6_out, A3, and_1_out);
  and and_7 (and_7_out, A1, and_3_out);
  and and_8 (and_8_out, and_4_out, A0);
  or or_1 (Y, and_6_out, and_5_out, and_7_out, and_8_out);
endmodule

module Three_4choose1 (
  input  [2:0] in_1,
  input  [2:0] in_2,
  input  [2:0] in_3,
  input  [2:0] in_4,
  input  SEL1,
  input  SEL0,
  output [2:0] out_7
);

  wire and_1_out, and_2_out, and_3_out, and_5_out, not_1_out, not_2_out;

  not not_1 (not_1_out, SEL1);
  not not_2 (not_2_out, SEL0);
  and and_1 (and_1_out, in_1[0], SEL1, SEL0);
  and and_2 (and_2_out, in_1[2], SEL1, SEL0);
  and and_3 (and_3_out, in_2[2], SEL1, not_2_out);
  and and_4 (out_7[1], in_3[1], not_1_out, SEL0);
  and and_5 (and_5_out, in_4[0], not_1_out, not_2_out);
  or or_1 (out_7[0], and_1_out, and_5_out);
  or or_2 (out_7[2], and_2_out, and_3_out);

  // Notes on the sheet:
  //   原来这个三位4选一选择器是固定输入的啊。。要改变输入中间线路也得改
endmodule

module ablechangejinwei_shumaguan (
  input  A3,
  input  A2,
  input  A1,
  input  A0,
  input  CHOOSE
);

  wire and_1_out, and_2_out, and_3_out, and_4_out, and_5_out, and_6_out, and_7_out, and_8_out, and_9_out,
       and_10_out, and_11_out, and_12_out, and_13_out, and_14_out, and_15_out, and_16_out,
       one_wei2chosse1xuanzeqi_1_out_2, one_wei2chosse1xuanzeqi_1_out_3, or_1_out, or_2_out, or_3_out,
       or_4_out, or_5_out, or_6_out, or_7_out, or_8_out, shumaguan_10jinzhi_qudongdianlu_1_aaa,
       shumaguan_10jinzhi_qudongdianlu_1_bbb, shumaguan_10jinzhi_qudongdianlu_1_ccc,
       shumaguan_10jinzhi_qudongdianlu_1_ddd, shumaguan_10jinzhi_qudongdianlu_1_eee,
       shumaguan_10jinzhi_qudongdianlu_1_fff, shumaguan_10jinzhi_qudongdianlu_1_ggg,
       shumaguan_10jinzhi_qudongdianlu_1_hhh, shumaguan_16jinzhi_qudongdianlu_1_aaa,
       shumaguan_16jinzhi_qudongdianlu_1_bbb, shumaguan_16jinzhi_qudongdianlu_1_ccc,
       shumaguan_16jinzhi_qudongdianlu_1_ddd, shumaguan_16jinzhi_qudongdianlu_1_eee,
       shumaguan_16jinzhi_qudongdianlu_1_fff, shumaguan_16jinzhi_qudongdianlu_1_ggg,
       shumaguan_16jinzhi_qudongdianlu_1_hhh;

  ONE_wei2chosse1xuanzeqi one_wei2chosse1xuanzeqi_1 (
    .in_1(CHOOSE), .out_2(one_wei2chosse1xuanzeqi_1_out_2), .out_3(one_wei2chosse1xuanzeqi_1_out_3));
  shumaguan_10jinzhi_qudongdianlu shumaguan_10jinzhi_qudongdianlu_1 (
    .in_1(A3), .in_2(A2), .in_3(A1), .in_4(A0), .BBB(shumaguan_10jinzhi_qudongdianlu_1_bbb),
    .AAA(shumaguan_10jinzhi_qudongdianlu_1_aaa), .FFF(shumaguan_10jinzhi_qudongdianlu_1_fff),
    .GGG(shumaguan_10jinzhi_qudongdianlu_1_ggg), .EEE(shumaguan_10jinzhi_qudongdianlu_1_eee),
    .DDD(shumaguan_10jinzhi_qudongdianlu_1_ddd), .CCC(shumaguan_10jinzhi_qudongdianlu_1_ccc),
    .HHH(shumaguan_10jinzhi_qudongdianlu_1_hhh));
  shumaguan_16jinzhi_qudongdianlu shumaguan_16jinzhi_qudongdianlu_1 (
    .in_1(A3), .in_2(A2), .in_3(A1), .in_4(A0), .BBB(shumaguan_16jinzhi_qudongdianlu_1_bbb),
    .AAA(shumaguan_16jinzhi_qudongdianlu_1_aaa), .FFF(shumaguan_16jinzhi_qudongdianlu_1_fff),
    .GGG(shumaguan_16jinzhi_qudongdianlu_1_ggg), .EEE(shumaguan_16jinzhi_qudongdianlu_1_eee),
    .DDD(shumaguan_16jinzhi_qudongdianlu_1_ddd), .CCC(shumaguan_16jinzhi_qudongdianlu_1_ccc),
    .HHH(shumaguan_16jinzhi_qudongdianlu_1_hhh));
  and and_1 (and_1_out, shumaguan_10jinzhi_qudongdianlu_1_bbb, one_wei2chosse1xuanzeqi_1_out_3);
  and and_2 (and_2_out, shumaguan_10jinzhi_qudongdianlu_1_aaa, one_wei2chosse1xuanzeqi_1_out_3);
  and and_3 (and_3_out, shumaguan_10jinzhi_qudongdianlu_1_fff, one_wei2chosse1xuanzeqi_1_out_3);
  and and_4 (and_4_out, shumaguan_10jinzhi_qudongdianlu_1_ggg, one_wei2chosse1xuanzeqi_1_out_3);
  and and_5 (and_5_out, shumaguan_10jinzhi_qudongdianlu_1_eee, one_wei2chosse1xuanzeqi_1_out_3);
  and and_6 (and_6_out, shumaguan_10jinzhi_qudongdianlu_1_ddd, one_wei2chosse1xuanzeqi_1_out_3);
  and and_7 (and_7_out, shumaguan_10jinzhi_qudongdianlu_1_ccc, one_wei2chosse1xuanzeqi_1_out_3);
  and and_8 (and_8_out, shumaguan_10jinzhi_qudongdianlu_1_hhh, one_wei2chosse1xuanzeqi_1_out_3);
  and and_9 (and_9_out, shumaguan_16jinzhi_qudongdianlu_1_bbb, one_wei2chosse1xuanzeqi_1_out_2);
  and and_10 (and_10_out, shumaguan_16jinzhi_qudongdianlu_1_aaa, one_wei2chosse1xuanzeqi_1_out_2);
  and and_11 (and_11_out, shumaguan_16jinzhi_qudongdianlu_1_fff, one_wei2chosse1xuanzeqi_1_out_2);
  and and_12 (and_12_out, shumaguan_16jinzhi_qudongdianlu_1_ggg, one_wei2chosse1xuanzeqi_1_out_2);
  and and_13 (and_13_out, shumaguan_16jinzhi_qudongdianlu_1_eee, one_wei2chosse1xuanzeqi_1_out_2);
  and and_14 (and_14_out, shumaguan_16jinzhi_qudongdianlu_1_ddd, one_wei2chosse1xuanzeqi_1_out_2);
  and and_15 (and_15_out, shumaguan_16jinzhi_qudongdianlu_1_ccc, one_wei2chosse1xuanzeqi_1_out_2);
  and and_16 (and_16_out, shumaguan_16jinzhi_qudongdianlu_1_hhh, one_wei2chosse1xuanzeqi_1_out_2);
  or or_1 (or_1_out, and_1_out, and_9_out);
  or or_2 (or_2_out, and_2_out, and_10_out);
  or or_3 (or_3_out, and_3_out, and_11_out);
  or or_4 (or_4_out, and_4_out, and_12_out);
  or or_5 (or_5_out, and_5_out, and_13_out);
  or or_6 (or_6_out, and_6_out, and_14_out);
  or or_7 (or_7_out, and_7_out, and_15_out);
  or or_8 (or_8_out, and_8_out, and_16_out);
  _7_Segment_Display u_7_segment_display_1 (
    .g(or_4_out), .f(or_3_out), .a(or_2_out), .b(or_1_out), .e(or_5_out), .d(or_6_out), .c(or_7_out),
    .dp(or_8_out));
endmodule

module ablechangejinwei_qudongdianlu (
  input  A3,
  input  A2,
  input  A1,
  input  A0,
  input  CHOOSE,
  output AAA,
  output BBB,
  output CCC,
  output DDD,
  output EEE,
  output FFF,
  output GGG,
  output HHH
);

  wire and_1_out, and_2_out, and_3_out, and_4_out, and_5_out, and_6_out, and_7_out, and_8_out, and_9_out,
       and_10_out, and_11_out, and_12_out, and_13_out, and_14_out, and_15_out, and_16_out,
       one_wei2chosse1xuanzeqi_1_out_2, one_wei2chosse1xuanzeqi_1_out_3,
       shumaguan_10jinzhi_qudongdianlu_1_aaa, shumaguan_10jinzhi_qudongdianlu_1_bbb,
       shumaguan_10jinzhi_qudongdianlu_1_ccc, shumaguan_10jinzhi_qudongdianlu_1_ddd,
       shumaguan_10jinzhi_qudongdianlu_1_eee, shumaguan_10jinzhi_qudongdianlu_1_fff,
       shumaguan_10jinzhi_qudongdianlu_1_ggg, shumaguan_10jinzhi_qudongdianlu_1_hhh,
       shumaguan_16jinzhi_qudongdianlu_1_aaa, shumaguan_16jinzhi_qudongdianlu_1_bbb,
       shumaguan_16jinzhi_qudongdianlu_1_ccc, shumaguan_16jinzhi_qudongdianlu_1_ddd,
       shumaguan_16jinzhi_qudongdianlu_1_eee, shumaguan_16jinzhi_qudongdianlu_1_fff,
       shumaguan_16jinzhi_qudongdianlu_1_ggg, shumaguan_16jinzhi_qudongdianlu_1_hhh;

  ONE_wei2chosse1xuanzeqi one_wei2chosse1xuanzeqi_1 (
    .in_1(CHOOSE), .out_2(one_wei2chosse1xuanzeqi_1_out_2), .out_3(one_wei2chosse1xuanzeqi_1_out_3));
  shumaguan_10jinzhi_qudongdianlu shumaguan_10jinzhi_qudongdianlu_1 (
    .in_1(A3), .in_2(A2), .in_3(A1), .in_4(A0), .BBB(shumaguan_10jinzhi_qudongdianlu_1_bbb),
    .AAA(shumaguan_10jinzhi_qudongdianlu_1_aaa), .FFF(shumaguan_10jinzhi_qudongdianlu_1_fff),
    .GGG(shumaguan_10jinzhi_qudongdianlu_1_ggg), .EEE(shumaguan_10jinzhi_qudongdianlu_1_eee),
    .DDD(shumaguan_10jinzhi_qudongdianlu_1_ddd), .CCC(shumaguan_10jinzhi_qudongdianlu_1_ccc),
    .HHH(shumaguan_10jinzhi_qudongdianlu_1_hhh));
  shumaguan_16jinzhi_qudongdianlu shumaguan_16jinzhi_qudongdianlu_1 (
    .in_1(A3), .in_2(A2), .in_3(A1), .in_4(A0), .BBB(shumaguan_16jinzhi_qudongdianlu_1_bbb),
    .AAA(shumaguan_16jinzhi_qudongdianlu_1_aaa), .FFF(shumaguan_16jinzhi_qudongdianlu_1_fff),
    .GGG(shumaguan_16jinzhi_qudongdianlu_1_ggg), .EEE(shumaguan_16jinzhi_qudongdianlu_1_eee),
    .DDD(shumaguan_16jinzhi_qudongdianlu_1_ddd), .CCC(shumaguan_16jinzhi_qudongdianlu_1_ccc),
    .HHH(shumaguan_16jinzhi_qudongdianlu_1_hhh));
  and and_1 (and_1_out, shumaguan_10jinzhi_qudongdianlu_1_bbb, one_wei2chosse1xuanzeqi_1_out_3);
  and and_2 (and_2_out, shumaguan_10jinzhi_qudongdianlu_1_aaa, one_wei2chosse1xuanzeqi_1_out_3);
  and and_3 (and_3_out, shumaguan_10jinzhi_qudongdianlu_1_fff, one_wei2chosse1xuanzeqi_1_out_3);
  and and_4 (and_4_out, shumaguan_10jinzhi_qudongdianlu_1_ggg, one_wei2chosse1xuanzeqi_1_out_3);
  and and_5 (and_5_out, shumaguan_10jinzhi_qudongdianlu_1_eee, one_wei2chosse1xuanzeqi_1_out_3);
  and and_6 (and_6_out, shumaguan_10jinzhi_qudongdianlu_1_ddd, one_wei2chosse1xuanzeqi_1_out_3);
  and and_7 (and_7_out, shumaguan_10jinzhi_qudongdianlu_1_ccc, one_wei2chosse1xuanzeqi_1_out_3);
  and and_8 (and_8_out, shumaguan_10jinzhi_qudongdianlu_1_hhh, one_wei2chosse1xuanzeqi_1_out_3);
  and and_9 (and_9_out, shumaguan_16jinzhi_qudongdianlu_1_bbb, one_wei2chosse1xuanzeqi_1_out_2);
  and and_10 (and_10_out, shumaguan_16jinzhi_qudongdianlu_1_aaa, one_wei2chosse1xuanzeqi_1_out_2);
  and and_11 (and_11_out, shumaguan_16jinzhi_qudongdianlu_1_fff, one_wei2chosse1xuanzeqi_1_out_2);
  and and_12 (and_12_out, shumaguan_16jinzhi_qudongdianlu_1_ggg, one_wei2chosse1xuanzeqi_1_out_2);
  and and_13 (and_13_out, shumaguan_16jinzhi_qudongdianlu_1_eee, one_wei2chosse1xuanzeqi_1_out_2);
  and and_14 (and_14_out, shumaguan_16jinzhi_qudongdianlu_1_ddd, one_wei2chosse1xuanzeqi_1_out_2);
  and and_15 (and_15_out, shumaguan_16jinzhi_qudongdianlu_1_ccc, one_wei2chosse1xuanzeqi_1_out_2);
  and and_16 (and_16_out, shumaguan_16jinzhi_qudongdianlu_1_hhh, one_wei2chosse1xuanzeqi_1_out_2);
  or or_1 (AAA, and_1_out, and_9_out);
  or or_2 (BBB, and_2_out, and_10_out);
  or or_3 (CCC, and_3_out, and_11_out);
  or or_4 (DDD, and_4_out, and_12_out);
  or or_5 (EEE, and_5_out, and_13_out);
  or or_6 (FFF, and_6_out, and_14_out);
  or or_7 (GGG, and_7_out, and_15_out);
  or or_8 (HHH, and_8_out, and_16_out);
endmodule

module One_4choose1 (
  input  Y3,
  input  Y2,
  input  Y1,
  input  Y0,
  input  SEL1,
  input  SEL0,
  output Y
);

  wire and_1_out, and_2_out, and_3_out, and_4_out, two_4yimaqi_1_y0, two_4yimaqi_1_y1, two_4yimaqi_1_y2,
       two_4yimaqi_1_y3;

  Two_4yimaqi two_4yimaqi_1 (
    .A0(SEL1), .A1(SEL0), .Y3(two_4yimaqi_1_y3), .Y2(two_4yimaqi_1_y2), .Y1(two_4yimaqi_1_y1),
    .Y0(two_4yimaqi_1_y0));
  and and_1 (and_1_out, Y0, two_4yimaqi_1_y0);
  and and_2 (and_2_out, Y1, two_4yimaqi_1_y1);
  and and_3 (and_3_out, Y2, two_4yimaqi_1_y2);
  and and_4 (and_4_out, Y3, two_4yimaqi_1_y3);
  or or_1 (Y, and_1_out, and_2_out, and_3_out, and_4_out);
endmodule

module FOUR_bijiaoqi (
  input  A3,
  input  B3,
  input  A2,
  input  B2,
  input  A1,
  input  B1,
  input  A0,
  input  B0,
  output Y_AdayuB,
  output Y_AdengyuB,
  output Y_AxiaoyuB
);

  wire and_2_out, and_3_out, and_4_out, and_5_out, and_6_out, and_7_out, and_8_out, and_9_out, and_10_out,
       and_11_out, and_12_out, not_1_out, not_2_out, not_3_out, not_4_out, xnor_1_out, xnor_2_out,
       xnor_3_out, xnor_4_out;

  not not_1 (not_1_out, xnor_1_out);
  not not_2 (not_2_out, xnor_2_out);
  xnor xnor_1 (xnor_1_out, A3, B3);
  xnor xnor_2 (xnor_2_out, A2, B2);
  xnor xnor_3 (xnor_3_out, A1, B1);
  xnor xnor_4 (xnor_4_out, A0, B0);
  not not_3 (not_3_out, xnor_3_out);
  not not_4 (not_4_out, xnor_4_out);
  and and_1 (Y_AdengyuB, xnor_1_out, xnor_2_out, xnor_3_out, xnor_4_out);
  and and_2 (and_2_out, xnor_1_out, not_2_out);
  and and_3 (and_3_out, xnor_1_out, xnor_2_out, not_3_out);
  and and_4 (and_4_out, xnor_1_out, xnor_2_out, xnor_2_out, not_4_out);
  and and_5 (and_5_out, A3, not_1_out);
  and and_6 (and_6_out, A2, and_2_out);
  and and_7 (and_7_out, A1, and_3_out);
  and and_8 (and_8_out, and_4_out, A0);
  and and_9 (and_9_out, B3, not_1_out);
  and and_10 (and_10_out, and_2_out, B2);
  and and_11 (and_11_out, and_3_out, B1);
  and and_12 (and_12_out, and_4_out, B0);
  or or_1 (Y_AdayuB, and_5_out, and_6_out, and_7_out, and_8_out);
  or or_2 (Y_AxiaoyuB, and_9_out, and_10_out, and_11_out, and_12_out);
  LED led_1 (.in(Y_AdayuB));
  LED led_2 (.in(Y_AdengyuB));
  LED led_3 (.in(Y_AxiaoyuB));

  // Notes on the sheet:
  //   核心在于当更高一级数据已经能比出大小的时候怎么控制次级及以下的信号，解决办法是最高级已经可以比出大小的时候（这个时候连接两个最高级的同或门信号肯定为0，非门转化后连接与门A），将大的数据位（比如A>B就选A那一条）
  //   也接在与门A，此时就是第一种情况；若最高位都相同（无论1、0），此时同或门1输出的1就用作第一位比较失败，启动第二位比较“的条件之一（”与“），后几位同理，启用第三位时比较候需要前两位相同的条件（所以要用3位数入的与门），启动第四位比较的时候需要前三者相同的条件（所以用4位输入与门）
endmodule

module Half_adder (
  input  A,
  input  B,
  output S,
  output COUT
);

  and and_1 (COUT, A, B);
  xor xor_1 (S, A, B);
endmodule

module FULL_adder (
  input  A,
  input  B,
  input  CIn,
  output S,
  output Cout
);

  wire and_1_out, and_2_out, and_3_out, and_4_out, not_1_out, or_1_out, xnor_1_out, xor_1_out;

  xor xor_1 (xor_1_out, A, B);
  and and_1 (and_1_out, A, B);
  or or_1 (or_1_out, B, A);
  not not_1 (not_1_out, CIn);
  and and_2 (and_2_out, or_1_out, CIn);
  xnor xnor_1 (xnor_1_out, B, A);
  and and_3 (and_3_out, not_1_out, xor_1_out);
  and and_4 (and_4_out, xnor_1_out, CIn);
  or or_2 (S, and_3_out, and_4_out);
  or or_3 (Cout, and_1_out, and_2_out);
endmodule

module FULL_adder_correct (
  input  A,
  input  B,
  input  CIN,
  output S,
  output COUT
);

  wire and_1_out, and_2_out, xor_1_out;

  and and_1 (and_1_out, A, B);
  xor xor_1 (xor_1_out, A, B);
  xor xor_2 (S, xor_1_out, CIN);
  and and_2 (and_2_out, xor_1_out, CIN);
  or or_1 (COUT, and_1_out, and_2_out);
endmodule

module Full_adder_withzidianlu (
  input  A,
  input  B,
  input  Cin,
  output S,
  output Cout
);

  wire half_adder_1_cout, half_adder_1_s, half_adder_2_cout;

  Half_adder half_adder_1 (.A(A), .B(B), .S(half_adder_1_s), .COUT(half_adder_1_cout));
  Half_adder half_adder_2 (.A(half_adder_1_s), .B(Cin), .S(S), .COUT(half_adder_2_cout));
  or or_1 (Cout, half_adder_2_cout, half_adder_1_cout);
endmodule

module RCA_Four_adder (
  input  A3,
  input  A2,
  input  A1,
  input  A0,
  input  B3,
  input  B2,
  input  B1,
  input  B0,
  input  C0,
  output OUT_3,
  output OUT_2,
  output OUT_1,
  output OUT_0,
  output C4
);

  wire full_adder_correct_1_cout, full_adder_correct_2_cout, full_adder_correct_3_cout,
       shumaguan_16jinzhi_qudongdianlu_1_aaa, shumaguan_16jinzhi_qudongdianlu_1_bbb,
       shumaguan_16jinzhi_qudongdianlu_1_ccc, shumaguan_16jinzhi_qudongdianlu_1_ddd,
       shumaguan_16jinzhi_qudongdianlu_1_eee, shumaguan_16jinzhi_qudongdianlu_1_fff,
       shumaguan_16jinzhi_qudongdianlu_1_ggg, shumaguan_16jinzhi_qudongdianlu_1_hhh;

  FULL_adder_correct full_adder_correct_1 (.A(A0), .B(B0), .CIN(C0), .S(OUT_0), .COUT(full_adder_correct_1_cout));
  FULL_adder_correct full_adder_correct_2 (
    .A(A1), .B(B1), .CIN(full_adder_correct_1_cout), .S(OUT_1), .COUT(full_adder_correct_2_cout));
  FULL_adder_correct full_adder_correct_3 (
    .A(A2), .B(B2), .CIN(full_adder_correct_2_cout), .S(OUT_2), .COUT(full_adder_correct_3_cout));
  FULL_adder_correct full_adder_correct_4 (.A(A3), .B(B3), .CIN(full_adder_correct_3_cout), .S(OUT_3), .COUT(C4));
  shumaguan_16jinzhi_qudongdianlu shumaguan_16jinzhi_qudongdianlu_1 (
    .in_1(OUT_3), .in_2(OUT_2), .in_3(OUT_1), .in_4(OUT_0), .BBB(shumaguan_16jinzhi_qudongdianlu_1_bbb),
    .AAA(shumaguan_16jinzhi_qudongdianlu_1_aaa), .FFF(shumaguan_16jinzhi_qudongdianlu_1_fff),
    .GGG(shumaguan_16jinzhi_qudongdianlu_1_ggg), .EEE(shumaguan_16jinzhi_qudongdianlu_1_eee),
    .DDD(shumaguan_16jinzhi_qudongdianlu_1_ddd), .CCC(shumaguan_16jinzhi_qudongdianlu_1_ccc),
    .HHH(shumaguan_16jinzhi_qudongdianlu_1_hhh));
  _7_Segment_Display u_7_segment_display_1 (
    .g(shumaguan_16jinzhi_qudongdianlu_1_ggg), .f(shumaguan_16jinzhi_qudongdianlu_1_fff),
    .a(shumaguan_16jinzhi_qudongdianlu_1_aaa), .b(shumaguan_16jinzhi_qudongdianlu_1_bbb),
    .e(shumaguan_16jinzhi_qudongdianlu_1_eee), .d(shumaguan_16jinzhi_qudongdianlu_1_ddd),
    .c(shumaguan_16jinzhi_qudongdianlu_1_ccc), .dp(shumaguan_16jinzhi_qudongdianlu_1_hhh));
endmodule

module four_jianfaqi (
  input  A3,
  input  A2,
  input  A1,
  input  A0,
  input  B3,
  input  B2,
  input  B1,
  input  B0,
  output out_3,
  output out_2,
  output out_1,
  output out_0
);

  wire not_1_out, not_2_out, not_3_out, not_4_out, rca_four_adder_1_out_0, rca_four_adder_1_out_1,
       rca_four_adder_1_out_2, rca_four_adder_1_out_3, shumaguan_16jinzhi_qudongdianlu_1_aaa,
       shumaguan_16jinzhi_qudongdianlu_1_bbb, shumaguan_16jinzhi_qudongdianlu_1_ccc,
       shumaguan_16jinzhi_qudongdianlu_1_ddd, shumaguan_16jinzhi_qudongdianlu_1_eee,
       shumaguan_16jinzhi_qudongdianlu_1_fff, shumaguan_16jinzhi_qudongdianlu_1_ggg,
       shumaguan_16jinzhi_qudongdianlu_1_hhh;

  not not_1 (not_1_out, B3);
  not not_2 (not_2_out, B2);
  not not_3 (not_3_out, B1);
  not not_4 (not_4_out, B0);
  RCA_Four_adder rca_four_adder_1 (
    .A3(not_1_out), .A2(not_2_out), .A1(not_3_out), .A0(not_4_out), .B3(1'b0), .B2(1'b0), .B1(1'b0),
    .B0(1'b1), .OUT_3(rca_four_adder_1_out_3), .OUT_2(rca_four_adder_1_out_2),
    .OUT_1(rca_four_adder_1_out_1), .OUT_0(rca_four_adder_1_out_0));  // open: C0, C4
  RCA_Four_adder rca_four_adder_2 (
    .A3(A3), .A2(A2), .A1(A1), .A0(A0), .B3(rca_four_adder_1_out_3), .B2(rca_four_adder_1_out_2),
    .B1(rca_four_adder_1_out_1), .B0(rca_four_adder_1_out_0), .OUT_3(out_3), .OUT_2(out_2), .OUT_1(out_1),
    .OUT_0(out_0));  // open: C0, C4
  shumaguan_16jinzhi_qudongdianlu shumaguan_16jinzhi_qudongdianlu_1 (
    .in_1(out_3), .in_2(out_2), .in_3(out_1), .in_4(out_0), .BBB(shumaguan_16jinzhi_qudongdianlu_1_bbb),
    .AAA(shumaguan_16jinzhi_qudongdianlu_1_aaa), .FFF(shumaguan_16jinzhi_qudongdianlu_1_fff),
    .GGG(shumaguan_16jinzhi_qudongdianlu_1_ggg), .EEE(shumaguan_16jinzhi_qudongdianlu_1_eee),
    .DDD(shumaguan_16jinzhi_qudongdianlu_1_ddd), .CCC(shumaguan_16jinzhi_qudongdianlu_1_ccc),
    .HHH(shumaguan_16jinzhi_qudongdianlu_1_hhh));
  _7_Segment_Display u_7_segment_display_1 (
    .g(shumaguan_16jinzhi_qudongdianlu_1_ggg), .f(shumaguan_16jinzhi_qudongdianlu_1_fff),
    .a(shumaguan_16jinzhi_qudongdianlu_1_aaa), .b(shumaguan_16jinzhi_qudongdianlu_1_bbb),
    .e(shumaguan_16jinzhi_qudongdianlu_1_eee), .d(shumaguan_16jinzhi_qudongdianlu_1_ddd),
    .c(shumaguan_16jinzhi_qudongdianlu_1_ccc), .dp(shumaguan_16jinzhi_qudongdianlu_1_hhh));

  // Notes on the sheet:
  //   这一块部分是一个求补模块，主要作用是将减数从原码变为补码（先逐位求反再总体加0001）
endmodule

module qiubu_mokuai (
  input  B3_in,
  input  B2_in,
  input  B1_in,
  input  B0_in,
  output B3_OUT,
  output B2_OUT,
  output BI_OUT,
  output B0_OUT
);

  wire not_1_out, not_2_out, not_3_out, not_4_out;

  not not_1 (not_1_out, B3_in);
  not not_2 (not_2_out, B2_in);
  not not_3 (not_3_out, B1_in);
  not not_4 (not_4_out, B0_in);
  RCA_Four_adder rca_four_adder_1 (
    .A3(not_1_out), .A2(not_2_out), .A1(not_3_out), .A0(not_4_out), .B3(1'b0), .B2(1'b0), .B1(1'b0),
    .B0(1'b1), .OUT_3(B3_OUT), .OUT_2(B2_OUT), .OUT_1(BI_OUT), .OUT_0(B0_OUT));  // open: C0, C4
endmodule

module yuanma_adder (
  input  A3,
  input  A2,
  input  A1,
  input  A0,
  input  B3,
  input  B2,
  input  B1,
  input  B0,
  output fuhao,
  output overflow,
  output Y2,
  output Y1,
  output Y0
);

  wire Aa_AB_out_0, Aa_AB_out_1, Aa_AB_out_2, Aa_AB_out_3, Ab_Aa_out_0, Ab_Aa_out_1, Ab_Aa_out_2,
       Ab_Aa_out_3, and_1_out, and_2_out, and_3_out, and_4_out, and_5_out, and_6_out, and_7_out, and_8_out,
       and_9_out, and_10_out, and_11_out, and_12_out, and_13_out, and_14_out, and_15_out, and_16_out,
       and_17_out, four_bijiaoqi_1_y_adayub, four_bijiaoqi_1_y_axiaoyub, not_1_out, rca_four_adder_1_out_0,
       rca_four_adder_1_out_1, rca_four_adder_1_out_2, rca_four_adder_1_out_3,
       shumaguan_16jinzhi_qudongdianlu_1_aaa, shumaguan_16jinzhi_qudongdianlu_1_bbb,
       shumaguan_16jinzhi_qudongdianlu_1_ccc, shumaguan_16jinzhi_qudongdianlu_1_ddd,
       shumaguan_16jinzhi_qudongdianlu_1_eee, shumaguan_16jinzhi_qudongdianlu_1_fff,
       shumaguan_16jinzhi_qudongdianlu_1_ggg, shumaguan_16jinzhi_qudongdianlu_1_hhh, xnor_1_out;

  xnor xnor_1 (xnor_1_out, A3, B3);
  and and_1 (and_1_out, xnor_1_out, B3, A3);
  FOUR_bijiaoqi four_bijiaoqi_1 (
    .A2(A2), .B2(B2), .A1(A1), .B1(B1), .A0(A0), .B0(B0), .Y_AdayuB(four_bijiaoqi_1_y_adayub),
    .Y_AxiaoyuB(four_bijiaoqi_1_y_axiaoyub));  // open: A3, B3, Y_AdengyuB
  RCA_Four_adder rca_four_adder_1 (
    .A2(A2), .A1(A1), .A0(A0), .B2(B2), .B1(B1), .B0(B0), .OUT_3(rca_four_adder_1_out_3),
    .OUT_2(rca_four_adder_1_out_2), .OUT_1(rca_four_adder_1_out_1), .OUT_0(rca_four_adder_1_out_0));  // open: A3, B3, C0, C4
  not not_1 (not_1_out, xnor_1_out);
  and and_2 (and_2_out, A3, not_1_out, four_bijiaoqi_1_y_adayub);
  and and_3 (and_3_out, four_bijiaoqi_1_y_axiaoyub, not_1_out, B3);
  and and_4 (and_4_out, xnor_1_out, rca_four_adder_1_out_3);
  and and_5 (and_5_out, xnor_1_out, rca_four_adder_1_out_2);
  and and_6 (and_6_out, xnor_1_out, rca_four_adder_1_out_1);
  and and_7 (and_7_out, xnor_1_out, rca_four_adder_1_out_0);
  four_jianfaqi Aa_AB (
    .A2(A2), .A1(A1), .A0(A0), .B2(B2), .B1(B1), .B0(B0), .out_3(Aa_AB_out_3), .out_2(Aa_AB_out_2),
    .out_1(Aa_AB_out_1), .out_0(Aa_AB_out_0));  // open: A3, B3
  four_jianfaqi Ab_Aa (
    .A2(B2), .A1(B1), .A0(B0), .B2(A2), .B1(A1), .B0(A0), .out_3(Ab_Aa_out_3), .out_2(Ab_Aa_out_2),
    .out_1(Ab_Aa_out_1), .out_0(Ab_Aa_out_0));  // open: A3, B3
  and and_8 (and_8_out, four_bijiaoqi_1_y_adayub, not_1_out);
  and and_9 (and_9_out, four_bijiaoqi_1_y_axiaoyub, not_1_out);
  and and_10 (and_10_out, and_8_out, Aa_AB_out_3);
  and and_11 (and_11_out, and_8_out, Aa_AB_out_2);
  and and_12 (and_12_out, and_8_out, Aa_AB_out_1);
  and and_13 (and_13_out, and_8_out, Aa_AB_out_0);
  and and_14 (and_14_out, and_9_out, Ab_Aa_out_3);
  and and_15 (and_15_out, and_9_out, Ab_Aa_out_2);
  and and_16 (and_16_out, and_9_out, Ab_Aa_out_1);
  and and_17 (and_17_out, and_9_out, Ab_Aa_out_0);
  or or_1 (overflow, and_4_out, and_10_out, and_14_out);
  or or_2 (Y2, and_5_out, and_11_out, and_15_out);
  or or_3 (Y1, and_6_out, and_12_out, and_16_out);
  or or_4 (Y0, and_7_out, and_13_out, and_17_out);
  or or_5 (fuhao, and_2_out, and_1_out, and_3_out);
  shumaguan_16jinzhi_qudongdianlu shumaguan_16jinzhi_qudongdianlu_1 (
    .in_2(Y2), .in_3(Y1), .in_4(Y0), .BBB(shumaguan_16jinzhi_qudongdianlu_1_bbb),
    .AAA(shumaguan_16jinzhi_qudongdianlu_1_aaa), .FFF(shumaguan_16jinzhi_qudongdianlu_1_fff),
    .GGG(shumaguan_16jinzhi_qudongdianlu_1_ggg), .EEE(shumaguan_16jinzhi_qudongdianlu_1_eee),
    .DDD(shumaguan_16jinzhi_qudongdianlu_1_ddd), .CCC(shumaguan_16jinzhi_qudongdianlu_1_ccc),
    .HHH(shumaguan_16jinzhi_qudongdianlu_1_hhh));  // open: in_1
  _7_Segment_Display u_7_segment_display_1 (.g(fuhao));  // open: f, a, b, e, d, c, dp
  _7_Segment_Display u_7_segment_display_2 (
    .g(shumaguan_16jinzhi_qudongdianlu_1_ggg), .f(shumaguan_16jinzhi_qudongdianlu_1_fff),
    .a(shumaguan_16jinzhi_qudongdianlu_1_aaa), .b(shumaguan_16jinzhi_qudongdianlu_1_bbb),
    .e(shumaguan_16jinzhi_qudongdianlu_1_eee), .d(shumaguan_16jinzhi_qudongdianlu_1_ddd),
    .c(shumaguan_16jinzhi_qudongdianlu_1_ccc), .dp(shumaguan_16jinzhi_qudongdianlu_1_hhh));
endmodule

module ONE_compareter (
  input  A,
  input  B,
  output OUT_DAYU,
  output OUT_XIAOYU,
  output OUT_DENGYU
);

  wire not_1_out, not_2_out;

  not not_1 (not_1_out, B);
  not not_2 (not_2_out, A);
  and and_1 (OUT_DAYU, A, not_1_out);
  and and_2 (OUT_XIAOYU, not_2_out, B);
  xnor xnor_1 (OUT_DENGYU, A, B);
endmodule

module fanma_adder (
  input  A3,
  input  A2,
  input  A1,
  input  A0,
  input  B3,
  input  B2,
  input  B1,
  input  B0,
  output out_9,
  output Y2,
  output Y1,
  output Y0
);

  wire not_1_out, not_2_out, not_3_out, rca_four_adder_1_c4, rca_four_adder_1_out_0, rca_four_adder_1_out_1,
       rca_four_adder_1_out_2, rca_four_adder_1_out_3, rca_four_adder_2_c4, rca_four_adder_2_out_0,
       rca_four_adder_2_out_1, rca_four_adder_2_out_2, rca_four_adder_2_out_3,
       shumaguan_16jinzhi_qudongdianlu_1_aaa, shumaguan_16jinzhi_qudongdianlu_1_bbb,
       shumaguan_16jinzhi_qudongdianlu_1_ccc, shumaguan_16jinzhi_qudongdianlu_1_ddd,
       shumaguan_16jinzhi_qudongdianlu_1_eee, shumaguan_16jinzhi_qudongdianlu_1_fff,
       shumaguan_16jinzhi_qudongdianlu_1_ggg, shumaguan_16jinzhi_qudongdianlu_1_hhh;

  RCA_Four_adder rca_four_adder_1 (
    .A3(A3), .A2(A2), .A1(A1), .A0(A0), .B3(B3), .B2(B2), .B1(B1), .B0(B0), .OUT_3(rca_four_adder_1_out_3),
    .OUT_2(rca_four_adder_1_out_2), .OUT_1(rca_four_adder_1_out_1), .OUT_0(rca_four_adder_1_out_0),
    .C4(rca_four_adder_1_c4));  // open: C0
  RCA_Four_adder rca_four_adder_2 (
    .A3(rca_four_adder_1_out_3), .A2(rca_four_adder_1_out_2), .A1(rca_four_adder_1_out_1),
    .A0(rca_four_adder_1_out_0), .B0(rca_four_adder_1_c4), .OUT_3(rca_four_adder_2_out_3),
    .OUT_2(rca_four_adder_2_out_2), .OUT_1(rca_four_adder_2_out_1), .OUT_0(rca_four_adder_2_out_0),
    .C4(rca_four_adder_2_c4));  // open: B3, B2, B1, C0
  not not_1 (not_1_out, rca_four_adder_2_out_2);
  not not_2 (not_2_out, rca_four_adder_2_out_1);
  not not_3 (not_3_out, rca_four_adder_2_out_0);
  TWO_choose1 two_choose1_1 (.A(not_1_out), .SEL(rca_four_adder_2_out_3), .B(rca_four_adder_2_out_2), .Y(Y2));
  TWO_choose1 two_choose1_2 (.A(not_2_out), .SEL(rca_four_adder_2_out_3), .B(rca_four_adder_2_out_1), .Y(Y1));
  TWO_choose1 two_choose1_3 (.A(not_3_out), .SEL(rca_four_adder_2_out_3), .B(rca_four_adder_2_out_0), .Y(Y0));
  shumaguan_16jinzhi_qudongdianlu shumaguan_16jinzhi_qudongdianlu_1 (
    .in_2(Y2), .in_3(Y1), .in_4(Y0), .BBB(shumaguan_16jinzhi_qudongdianlu_1_bbb),
    .AAA(shumaguan_16jinzhi_qudongdianlu_1_aaa), .FFF(shumaguan_16jinzhi_qudongdianlu_1_fff),
    .GGG(shumaguan_16jinzhi_qudongdianlu_1_ggg), .EEE(shumaguan_16jinzhi_qudongdianlu_1_eee),
    .DDD(shumaguan_16jinzhi_qudongdianlu_1_ddd), .CCC(shumaguan_16jinzhi_qudongdianlu_1_ccc),
    .HHH(shumaguan_16jinzhi_qudongdianlu_1_hhh));  // open: in_1
  _7_Segment_Display u_7_segment_display_1 (.g(rca_four_adder_2_out_3));  // open: f, a, b, e, d, c, dp
  _7_Segment_Display u_7_segment_display_2 (
    .g(shumaguan_16jinzhi_qudongdianlu_1_ggg), .f(shumaguan_16jinzhi_qudongdianlu_1_fff),
    .a(shumaguan_16jinzhi_qudongdianlu_1_aaa), .b(shumaguan_16jinzhi_qudongdianlu_1_bbb),
    .e(shumaguan_16jinzhi_qudongdianlu_1_eee), .d(shumaguan_16jinzhi_qudongdianlu_1_ddd),
    .c(shumaguan_16jinzhi_qudongdianlu_1_ccc), .dp(shumaguan_16jinzhi_qudongdianlu_1_hhh));

  // Notes on the sheet:
  //   Y3悬空即可，反正最大值为0111用不着第四位
endmodule

module fanma_adder_with_OF_detect (
  input  A3,
  input  A2,
  input  A1,
  input  A0,
  input  B3,
  input  B2,
  input  B1,
  input  B0,
  output out_9,
  output Y2,
  output Y1,
  output Y0,
  output OVERFLOW
);

  wire not_1_out, not_2_out, not_3_out, not_4_out, not_5_out, rca_four_adder_1_c4, rca_four_adder_1_out_0,
       rca_four_adder_1_out_1, rca_four_adder_1_out_2, rca_four_adder_1_out_3, rca_four_adder_2_c4,
       rca_four_adder_2_out_0, rca_four_adder_2_out_1, rca_four_adder_2_out_2, rca_four_adder_2_out_3,
       shumaguan_16jinzhi_qudongdianlu_1_aaa, shumaguan_16jinzhi_qudongdianlu_1_bbb,
       shumaguan_16jinzhi_qudongdianlu_1_ccc, shumaguan_16jinzhi_qudongdianlu_1_ddd,
       shumaguan_16jinzhi_qudongdianlu_1_eee, shumaguan_16jinzhi_qudongdianlu_1_fff,
       shumaguan_16jinzhi_qudongdianlu_1_ggg, shumaguan_16jinzhi_qudongdianlu_1_hhh;

  RCA_Four_adder rca_four_adder_1 (
    .A3(A3), .A2(A2), .A1(A1), .A0(A0), .B3(B3), .B2(B2), .B1(B1), .B0(B0), .OUT_3(rca_four_adder_1_out_3),
    .OUT_2(rca_four_adder_1_out_2), .OUT_1(rca_four_adder_1_out_1), .OUT_0(rca_four_adder_1_out_0),
    .C4(rca_four_adder_1_c4));  // open: C0
  not not_1 (not_1_out, A3);
  not not_2 (not_2_out, B3);
  NotExactlyOne xnor_1 (.out(OVERFLOW), .in0(not_1_out), .in1(not_2_out), .in2(rca_four_adder_1_out_3));
  RCA_Four_adder rca_four_adder_2 (
    .A3(rca_four_adder_1_out_3), .A2(rca_four_adder_1_out_2), .A1(rca_four_adder_1_out_1),
    .A0(rca_four_adder_1_out_0), .B0(rca_four_adder_1_c4), .OUT_3(rca_four_adder_2_out_3),
    .OUT_2(rca_four_adder_2_out_2), .OUT_1(rca_four_adder_2_out_1), .OUT_0(rca_four_adder_2_out_0),
    .C4(rca_four_adder_2_c4));  // open: B3, B2, B1, C0
  not not_3 (not_3_out, rca_four_adder_2_out_2);
  not not_4 (not_4_out, rca_four_adder_2_out_1);
  not not_5 (not_5_out, rca_four_adder_2_out_0);
  TWO_choose1 two_choose1_1 (.A(not_3_out), .SEL(rca_four_adder_2_out_3), .B(rca_four_adder_2_out_2), .Y(Y2));
  TWO_choose1 two_choose1_2 (.A(not_4_out), .SEL(rca_four_adder_2_out_3), .B(rca_four_adder_2_out_1), .Y(Y1));
  TWO_choose1 two_choose1_3 (.A(not_5_out), .SEL(rca_four_adder_2_out_3), .B(rca_four_adder_2_out_0), .Y(Y0));
  shumaguan_16jinzhi_qudongdianlu shumaguan_16jinzhi_qudongdianlu_1 (
    .in_2(Y2), .in_3(Y1), .in_4(Y0), .BBB(shumaguan_16jinzhi_qudongdianlu_1_bbb),
    .AAA(shumaguan_16jinzhi_qudongdianlu_1_aaa), .FFF(shumaguan_16jinzhi_qudongdianlu_1_fff),
    .GGG(shumaguan_16jinzhi_qudongdianlu_1_ggg), .EEE(shumaguan_16jinzhi_qudongdianlu_1_eee),
    .DDD(shumaguan_16jinzhi_qudongdianlu_1_ddd), .CCC(shumaguan_16jinzhi_qudongdianlu_1_ccc),
    .HHH(shumaguan_16jinzhi_qudongdianlu_1_hhh));  // open: in_1
  _7_Segment_Display u_7_segment_display_1 (.g(rca_four_adder_2_out_3));  // open: f, a, b, e, d, c, dp
  _7_Segment_Display u_7_segment_display_2 (
    .g(shumaguan_16jinzhi_qudongdianlu_1_ggg), .f(shumaguan_16jinzhi_qudongdianlu_1_fff),
    .a(shumaguan_16jinzhi_qudongdianlu_1_aaa), .b(shumaguan_16jinzhi_qudongdianlu_1_bbb),
    .e(shumaguan_16jinzhi_qudongdianlu_1_eee), .d(shumaguan_16jinzhi_qudongdianlu_1_ddd),
    .c(shumaguan_16jinzhi_qudongdianlu_1_ccc), .dp(shumaguan_16jinzhi_qudongdianlu_1_hhh));

  // Notes on the sheet:
  //   Y3悬空即可，反正最大值为0111用不着第四位
endmodule

module S_R_Latch_suocunqi (
  input  R,
  input  S,
  output Q,
  output Q_fan
);

  nor nor_1 (Q, R, Q_fan);
  nor nor_2 (Q_fan, Q, S);

  // Notes on the sheet:
  //   当你需要写数据的时候，SR就要一个设置成1一个设置成0
  //   当SR皆为11时，是一种奇怪的状态，再把SR调回00时就会震荡（OA）
  //   中间写了数据之后，SR都为0则为锁存状态（此时电路记住了上一刻的状态，就是记忆能力）
  //   再设成00就能锁存了
endmodule

module D_suocunqi (
  input  WE,
  input  D,
  input  RESET,
  output Q,
  output Q_fan
);

  wire and_1_out, and_2_out, and_3_out, not_1_out, not_2_out;

  not not_1 (not_1_out, RESET);
  and and_1 (and_1_out, D, not_1_out);
  not not_2 (not_2_out, and_1_out);
  and and_2 (and_2_out, and_1_out, WE);
  and and_3 (and_3_out, WE, not_2_out);
  S_R_Latch_suocunqi s_r_latch_suocunqi_1 (.R(and_2_out), .S(and_3_out), .Q(Q), .Q_fan(Q_fan));

  // Notes on the sheet:
  //   当WE为0时，D的输入被屏蔽，强行进入所锁存状态
  //   当WE开启（为1）的时候，则变为写数据状态
endmodule

module D_Flip_Flop_chufaqi (
  input  clk,
  input  D,
  input  reset,
  output Q,
  output Q_fan
);

  wire and_1_out, d_suocunqi_1_q, not_1_out, not_2_out;

  not not_1 (not_1_out, clk);
  not not_2 (not_2_out, reset);
  and and_1 (and_1_out, D, not_2_out);
  D_suocunqi d_suocunqi_1 (.WE(not_1_out), .D(and_1_out), .Q(d_suocunqi_1_q));  // open: RESET, Q_fan
  D_suocunqi d_suocunqi_2 (.WE(clk), .D(d_suocunqi_1_q), .Q(Q), .Q_fan(Q_fan));  // open: RESET

  // Notes on the sheet:
  //   现在是上升沿触发，如果想要下降沿就把非门换到这根线上就好了
  //   注意!!此复位信号为高电平有效（我看讲义上是低电平有效），是高是低只是一个非门的区别
endmodule

module D_FF_with_EN (
  input  CLK,
  input  D,
  input  EN,
  input  reset,
  output Q,
  output Q_fan
);

  wire and_1_out, and_2_out, d_suocunqi_1_q, not_1_out, not_2_out;

  and and_1 (and_1_out, D, EN);
  not not_1 (not_1_out, CLK);
  not not_2 (not_2_out, reset);
  and and_2 (and_2_out, and_1_out, not_2_out);
  D_suocunqi d_suocunqi_1 (.WE(not_1_out), .D(and_2_out), .Q(d_suocunqi_1_q));  // open: RESET, Q_fan
  D_suocunqi d_suocunqi_2 (.WE(CLK), .D(d_suocunqi_1_q), .Q(Q), .Q_fan(Q_fan));  // open: RESET

  // Notes on the sheet:
  //   现在是上升沿触发，如果想要下降沿就把非门换到这根线上就好了
  //   注意!!此复位信号为高电平有效（我看讲义上是低电平有效），是高是低只是一个非门的区别
endmodule

module FOUR_register_jicunqi (
  input  A3,
  input  A2,
  input  A1,
  input  A0,
  input  EN,
  input  CLK,
  output Y3,
  output Y2,
  output Y1,
  output Y0
);

  wire clock_1_out, shumaguan_16jinzhi_qudongdianlu_1_aaa, shumaguan_16jinzhi_qudongdianlu_1_bbb,
       shumaguan_16jinzhi_qudongdianlu_1_ccc, shumaguan_16jinzhi_qudongdianlu_1_ddd,
       shumaguan_16jinzhi_qudongdianlu_1_eee, shumaguan_16jinzhi_qudongdianlu_1_fff,
       shumaguan_16jinzhi_qudongdianlu_1_ggg, shumaguan_16jinzhi_qudongdianlu_1_hhh;

  Clock clock_1 (.out(clock_1_out));
  D_FF_with_EN THREE (.CLK(clock_1_out), .D(A3), .EN(EN), .Q(Y3));  // open: reset, Q_fan
  D_FF_with_EN TWO (.CLK(clock_1_out), .D(A2), .EN(EN), .Q(Y2));  // open: reset, Q_fan
  D_FF_with_EN ONE (.CLK(clock_1_out), .D(A1), .EN(EN), .Q(Y1));  // open: reset, Q_fan
  D_FF_with_EN ZERO (.CLK(clock_1_out), .D(A0), .EN(EN), .Q(Y0));  // open: reset, Q_fan
  shumaguan_16jinzhi_qudongdianlu shumaguan_16jinzhi_qudongdianlu_1 (
    .in_1(Y3), .in_2(Y2), .in_3(Y1), .in_4(Y0), .BBB(shumaguan_16jinzhi_qudongdianlu_1_bbb),
    .AAA(shumaguan_16jinzhi_qudongdianlu_1_aaa), .FFF(shumaguan_16jinzhi_qudongdianlu_1_fff),
    .GGG(shumaguan_16jinzhi_qudongdianlu_1_ggg), .EEE(shumaguan_16jinzhi_qudongdianlu_1_eee),
    .DDD(shumaguan_16jinzhi_qudongdianlu_1_ddd), .CCC(shumaguan_16jinzhi_qudongdianlu_1_ccc),
    .HHH(shumaguan_16jinzhi_qudongdianlu_1_hhh));
  _7_Segment_Display u_7_segment_display_1 (
    .g(shumaguan_16jinzhi_qudongdianlu_1_ggg), .f(shumaguan_16jinzhi_qudongdianlu_1_fff),
    .a(shumaguan_16jinzhi_qudongdianlu_1_aaa), .b(shumaguan_16jinzhi_qudongdianlu_1_bbb),
    .e(shumaguan_16jinzhi_qudongdianlu_1_eee), .d(shumaguan_16jinzhi_qudongdianlu_1_ddd),
    .c(shumaguan_16jinzhi_qudongdianlu_1_ccc), .dp(shumaguan_16jinzhi_qudongdianlu_1_hhh));
endmodule

module FOUR_counter (
  input  EN,
  input  CLK,
  output Y3,
  output Y2,
  output Y1,
  output Y0
);

  wire clock_1_out, rca_four_adder_1_out_0, rca_four_adder_1_out_1, rca_four_adder_1_out_2,
       rca_four_adder_1_out_3, shumaguan_16jinzhi_qudongdianlu_1_aaa, shumaguan_16jinzhi_qudongdianlu_1_bbb,
       shumaguan_16jinzhi_qudongdianlu_1_ccc, shumaguan_16jinzhi_qudongdianlu_1_ddd,
       shumaguan_16jinzhi_qudongdianlu_1_eee, shumaguan_16jinzhi_qudongdianlu_1_fff,
       shumaguan_16jinzhi_qudongdianlu_1_ggg, shumaguan_16jinzhi_qudongdianlu_1_hhh;

  Clock clock_1 (.out(clock_1_out));
  RCA_Four_adder rca_four_adder_1 (
    .A3(Y3), .A2(Y2), .A1(Y1), .A0(Y0), .B0(1'b1), .OUT_3(rca_four_adder_1_out_3),
    .OUT_2(rca_four_adder_1_out_2), .OUT_1(rca_four_adder_1_out_1), .OUT_0(rca_four_adder_1_out_0));  // open: B3, B2, B1, C0, C4
  FOUR_register_jicunqi four_register_jicunqi_1 (
    .A3(rca_four_adder_1_out_3), .A2(rca_four_adder_1_out_2), .A1(rca_four_adder_1_out_1),
    .A0(rca_four_adder_1_out_0), .EN(EN), .CLK(clock_1_out), .Y3(Y3), .Y2(Y2), .Y1(Y1), .Y0(Y0));
  shumaguan_16jinzhi_qudongdianlu shumaguan_16jinzhi_qudongdianlu_1 (
    .in_1(Y3), .in_2(Y2), .in_3(Y1), .in_4(Y0), .BBB(shumaguan_16jinzhi_qudongdianlu_1_bbb),
    .AAA(shumaguan_16jinzhi_qudongdianlu_1_aaa), .FFF(shumaguan_16jinzhi_qudongdianlu_1_fff),
    .GGG(shumaguan_16jinzhi_qudongdianlu_1_ggg), .EEE(shumaguan_16jinzhi_qudongdianlu_1_eee),
    .DDD(shumaguan_16jinzhi_qudongdianlu_1_ddd), .CCC(shumaguan_16jinzhi_qudongdianlu_1_ccc),
    .HHH(shumaguan_16jinzhi_qudongdianlu_1_hhh));
  _7_Segment_Display u_7_segment_display_1 (
    .g(shumaguan_16jinzhi_qudongdianlu_1_ggg), .f(shumaguan_16jinzhi_qudongdianlu_1_fff),
    .a(shumaguan_16jinzhi_qudongdianlu_1_aaa), .b(shumaguan_16jinzhi_qudongdianlu_1_bbb),
    .e(shumaguan_16jinzhi_qudongdianlu_1_eee), .d(shumaguan_16jinzhi_qudongdianlu_1_ddd),
    .c(shumaguan_16jinzhi_qudongdianlu_1_ccc), .dp(shumaguan_16jinzhi_qudongdianlu_1_hhh));
endmodule

module Eight_register (
  input  A7,
  input  A6,
  input  A5,
  input  A4,
  input  A3,
  input  A2,
  input  A1,
  input  A0,
  input  EN,
  input  CLK,
  output Y7,
  output Y6,
  output Y5,
  output Y4,
  output Y3,
  output Y2,
  output Y1,
  output Y0
);

  wire clock_1_out, shumaguan_16jinzhi_qudongdianlu_1_aaa, shumaguan_16jinzhi_qudongdianlu_1_bbb,
       shumaguan_16jinzhi_qudongdianlu_1_ccc, shumaguan_16jinzhi_qudongdianlu_1_ddd,
       shumaguan_16jinzhi_qudongdianlu_1_eee, shumaguan_16jinzhi_qudongdianlu_1_fff,
       shumaguan_16jinzhi_qudongdianlu_1_ggg, shumaguan_16jinzhi_qudongdianlu_1_hhh,
       shumaguan_16jinzhi_qudongdianlu_2_aaa, shumaguan_16jinzhi_qudongdianlu_2_bbb,
       shumaguan_16jinzhi_qudongdianlu_2_ccc, shumaguan_16jinzhi_qudongdianlu_2_ddd,
       shumaguan_16jinzhi_qudongdianlu_2_eee, shumaguan_16jinzhi_qudongdianlu_2_fff,
       shumaguan_16jinzhi_qudongdianlu_2_ggg, shumaguan_16jinzhi_qudongdianlu_2_hhh;

  Clock clock_1 (.out(clock_1_out));
  D_FF_with_EN THREE (.CLK(clock_1_out), .D(A7), .EN(EN), .Q(Y7));  // open: reset, Q_fan
  D_FF_with_EN TWO (.CLK(clock_1_out), .D(A6), .EN(EN), .Q(Y6));  // open: reset, Q_fan
  D_FF_with_EN ONE (.CLK(clock_1_out), .D(A5), .EN(EN), .Q(Y5));  // open: reset, Q_fan
  D_FF_with_EN ZERO (.CLK(clock_1_out), .D(A4), .EN(EN), .Q(Y4));  // open: reset, Q_fan
  D_FF_with_EN d_ff_with_en_1 (.CLK(clock_1_out), .D(A3), .EN(EN), .Q(Y3));  // open: reset, Q_fan
  D_FF_with_EN d_ff_with_en_2 (.CLK(clock_1_out), .D(A2), .EN(EN), .Q(Y2));  // open: reset, Q_fan
  shumaguan_16jinzhi_qudongdianlu shumaguan_16jinzhi_qudongdianlu_1 (
    .in_1(Y7), .in_2(Y6), .in_3(Y5), .in_4(Y4), .BBB(shumaguan_16jinzhi_qudongdianlu_1_bbb),
    .AAA(shumaguan_16jinzhi_qudongdianlu_1_aaa), .FFF(shumaguan_16jinzhi_qudongdianlu_1_fff),
    .GGG(shumaguan_16jinzhi_qudongdianlu_1_ggg), .EEE(shumaguan_16jinzhi_qudongdianlu_1_eee),
    .DDD(shumaguan_16jinzhi_qudongdianlu_1_ddd), .CCC(shumaguan_16jinzhi_qudongdianlu_1_ccc),
    .HHH(shumaguan_16jinzhi_qudongdianlu_1_hhh));
  _7_Segment_Display u_7_segment_display_1 (
    .g(shumaguan_16jinzhi_qudongdianlu_1_ggg), .f(shumaguan_16jinzhi_qudongdianlu_1_fff),
    .a(shumaguan_16jinzhi_qudongdianlu_1_aaa), .b(shumaguan_16jinzhi_qudongdianlu_1_bbb),
    .e(shumaguan_16jinzhi_qudongdianlu_1_eee), .d(shumaguan_16jinzhi_qudongdianlu_1_ddd),
    .c(shumaguan_16jinzhi_qudongdianlu_1_ccc), .dp(shumaguan_16jinzhi_qudongdianlu_1_hhh));
  D_FF_with_EN d_ff_with_en_3 (.CLK(clock_1_out), .D(A1), .EN(EN), .Q(Y1));  // open: reset, Q_fan
  D_FF_with_EN d_ff_with_en_4 (.CLK(clock_1_out), .D(A0), .EN(EN), .Q(Y0));  // open: reset, Q_fan
  shumaguan_16jinzhi_qudongdianlu shumaguan_16jinzhi_qudongdianlu_2 (
    .in_1(Y3), .in_2(Y2), .in_3(Y1), .in_4(Y0), .BBB(shumaguan_16jinzhi_qudongdianlu_2_bbb),
    .AAA(shumaguan_16jinzhi_qudongdianlu_2_aaa), .FFF(shumaguan_16jinzhi_qudongdianlu_2_fff),
    .GGG(shumaguan_16jinzhi_qudongdianlu_2_ggg), .EEE(shumaguan_16jinzhi_qudongdianlu_2_eee),
    .DDD(shumaguan_16jinzhi_qudongdianlu_2_ddd), .CCC(shumaguan_16jinzhi_qudongdianlu_2_ccc),
    .HHH(shumaguan_16jinzhi_qudongdianlu_2_hhh));
  _7_Segment_Display u_7_segment_display_2 (
    .g(shumaguan_16jinzhi_qudongdianlu_2_ggg), .f(shumaguan_16jinzhi_qudongdianlu_2_fff),
    .a(shumaguan_16jinzhi_qudongdianlu_2_aaa), .b(shumaguan_16jinzhi_qudongdianlu_2_bbb),
    .e(shumaguan_16jinzhi_qudongdianlu_2_eee), .d(shumaguan_16jinzhi_qudongdianlu_2_ddd),
    .c(shumaguan_16jinzhi_qudongdianlu_2_ccc), .dp(shumaguan_16jinzhi_qudongdianlu_2_hhh));
endmodule

module eight_adder (
  input  A7,
  input  A6,
  input  A5,
  input  A4,
  input  A3,
  input  A2,
  input  A1,
  input  A0,
  input  B7,
  input  B6,
  input  B5,
  input  B4,
  input  B3,
  input  B2,
  input  B1,
  input  B0,
  input  C0,
  output Y0,
  output Y1,
  output Y2,
  output Y3,
  output Y4,
  output Y5,
  output Y6,
  output Y7
);

  wire full_adder_correct_1_cout, full_adder_correct_2_cout, full_adder_correct_3_cout,
       full_adder_correct_4_cout, full_adder_correct_5_cout, full_adder_correct_6_cout,
       full_adder_correct_7_cout;

  FULL_adder_correct full_adder_correct_1 (.A(A0), .B(B0), .CIN(C0), .S(Y0), .COUT(full_adder_correct_1_cout));
  FULL_adder_correct full_adder_correct_2 (
    .A(A1), .B(B1), .CIN(full_adder_correct_1_cout), .S(Y1), .COUT(full_adder_correct_2_cout));
  FULL_adder_correct full_adder_correct_3 (
    .A(A2), .B(B2), .CIN(full_adder_correct_2_cout), .S(Y2), .COUT(full_adder_correct_3_cout));
  FULL_adder_correct full_adder_correct_4 (
    .A(A3), .B(B3), .CIN(full_adder_correct_3_cout), .S(Y3), .COUT(full_adder_correct_4_cout));
  FULL_adder_correct full_adder_correct_5 (
    .A(A4), .B(B4), .CIN(full_adder_correct_4_cout), .S(Y4), .COUT(full_adder_correct_5_cout));
  FULL_adder_correct full_adder_correct_6 (
    .A(A5), .B(B5), .CIN(full_adder_correct_5_cout), .S(Y5), .COUT(full_adder_correct_6_cout));
  FULL_adder_correct full_adder_correct_7 (
    .A(A6), .B(B6), .CIN(full_adder_correct_6_cout), .S(Y6), .COUT(full_adder_correct_7_cout));
  FULL_adder_correct full_adder_correct_8 (.A(A7), .B(B7), .CIN(full_adder_correct_7_cout), .S(Y7));  // open: COUT
endmodule

module SUM_1to10 (
  input  in_1
);

  wire clock_1_out, eight_adder_1_y0, eight_adder_1_y1, eight_adder_1_y2, eight_adder_1_y3, eight_adder_1_y4,
       eight_adder_1_y5, eight_adder_1_y6, eight_adder_1_y7, eight_adder_2_y0, eight_adder_2_y1,
       eight_adder_2_y2, eight_adder_2_y3, eight_adder_2_y4, eight_adder_2_y5, eight_adder_2_y6,
       eight_adder_2_y7, eight_register_1_y0, eight_register_1_y1, eight_register_1_y2, eight_register_1_y3,
       eight_register_1_y4, eight_register_1_y5, eight_register_1_y6, eight_register_1_y7,
       eight_register_2_y0, eight_register_2_y1, eight_register_2_y2, eight_register_2_y3,
       eight_register_2_y4, eight_register_2_y5, eight_register_2_y6, eight_register_2_y7,
       shumaguan_16jinzhi_qudongdianlu_1_aaa, shumaguan_16jinzhi_qudongdianlu_1_bbb,
       shumaguan_16jinzhi_qudongdianlu_1_ccc, shumaguan_16jinzhi_qudongdianlu_1_ddd,
       shumaguan_16jinzhi_qudongdianlu_1_eee, shumaguan_16jinzhi_qudongdianlu_1_fff,
       shumaguan_16jinzhi_qudongdianlu_1_ggg, shumaguan_16jinzhi_qudongdianlu_1_hhh,
       shumaguan_16jinzhi_qudongdianlu_2_aaa, shumaguan_16jinzhi_qudongdianlu_2_bbb,
       shumaguan_16jinzhi_qudongdianlu_2_ccc, shumaguan_16jinzhi_qudongdianlu_2_ddd,
       shumaguan_16jinzhi_qudongdianlu_2_eee, shumaguan_16jinzhi_qudongdianlu_2_fff,
       shumaguan_16jinzhi_qudongdianlu_2_ggg, shumaguan_16jinzhi_qudongdianlu_2_hhh;

  Clock clock_1 (.out(clock_1_out));
  Eight_register eight_register_1 (
    .A7(eight_adder_1_y7), .A6(eight_adder_1_y6), .A5(eight_adder_1_y5), .A4(eight_adder_1_y4),
    .A3(eight_adder_1_y3), .A2(eight_adder_1_y2), .A1(eight_adder_1_y1), .A0(eight_adder_1_y0), .EN(in_1),
    .CLK(clock_1_out), .Y7(eight_register_1_y7), .Y6(eight_register_1_y6), .Y5(eight_register_1_y5),
    .Y4(eight_register_1_y4), .Y3(eight_register_1_y3), .Y2(eight_register_1_y2), .Y1(eight_register_1_y1),
    .Y0(eight_register_1_y0));
  eight_adder eight_adder_1 (
    .A7(eight_register_1_y7), .A6(eight_register_1_y6), .A5(eight_register_1_y5), .A4(eight_register_1_y4),
    .A3(eight_register_1_y3), .A2(eight_register_1_y2), .A1(eight_register_1_y1), .A0(eight_register_1_y0),
    .B0(in_1), .Y0(eight_adder_1_y0), .Y1(eight_adder_1_y1), .Y2(eight_adder_1_y2), .Y3(eight_adder_1_y3),
    .Y4(eight_adder_1_y4), .Y5(eight_adder_1_y5), .Y6(eight_adder_1_y6), .Y7(eight_adder_1_y7));  // open: B7, B6, B5, B4, B3, B2, B1, C0
  Eight_register eight_register_2 (
    .A7(eight_adder_2_y7), .A6(eight_adder_2_y6), .A5(eight_adder_2_y5), .A4(eight_adder_2_y4),
    .A3(eight_adder_2_y3), .A2(eight_adder_2_y2), .A1(eight_adder_2_y1), .A0(eight_adder_2_y0), .EN(in_1),
    .CLK(clock_1_out), .Y7(eight_register_2_y7), .Y6(eight_register_2_y6), .Y5(eight_register_2_y5),
    .Y4(eight_register_2_y4), .Y3(eight_register_2_y3), .Y2(eight_register_2_y2), .Y1(eight_register_2_y1),
    .Y0(eight_register_2_y0));
  eight_adder eight_adder_2 (
    .A7(eight_adder_1_y7), .A6(eight_adder_1_y6), .A5(eight_adder_1_y5), .A4(eight_adder_1_y4),
    .A3(eight_adder_1_y3), .A2(eight_adder_1_y2), .A1(eight_adder_1_y1), .A0(eight_adder_1_y0),
    .B7(eight_register_2_y7), .B6(eight_register_2_y6), .B5(eight_register_2_y5), .B4(eight_register_2_y4),
    .B3(eight_register_2_y3), .B2(eight_register_2_y2), .B1(eight_register_2_y1), .B0(eight_register_2_y0),
    .Y0(eight_adder_2_y0), .Y1(eight_adder_2_y1), .Y2(eight_adder_2_y2), .Y3(eight_adder_2_y3),
    .Y4(eight_adder_2_y4), .Y5(eight_adder_2_y5), .Y6(eight_adder_2_y6), .Y7(eight_adder_2_y7));  // open: C0
  shumaguan_16jinzhi_qudongdianlu shumaguan_16jinzhi_qudongdianlu_1 (
    .in_1(eight_register_2_y7), .in_2(eight_register_2_y6), .in_3(eight_register_2_y5),
    .in_4(eight_register_2_y4), .BBB(shumaguan_16jinzhi_qudongdianlu_1_bbb),
    .AAA(shumaguan_16jinzhi_qudongdianlu_1_aaa), .FFF(shumaguan_16jinzhi_qudongdianlu_1_fff),
    .GGG(shumaguan_16jinzhi_qudongdianlu_1_ggg), .EEE(shumaguan_16jinzhi_qudongdianlu_1_eee),
    .DDD(shumaguan_16jinzhi_qudongdianlu_1_ddd), .CCC(shumaguan_16jinzhi_qudongdianlu_1_ccc),
    .HHH(shumaguan_16jinzhi_qudongdianlu_1_hhh));
  shumaguan_16jinzhi_qudongdianlu shumaguan_16jinzhi_qudongdianlu_2 (
    .in_1(eight_register_2_y3), .in_2(eight_register_2_y2), .in_3(eight_register_2_y1),
    .in_4(eight_register_2_y0), .BBB(shumaguan_16jinzhi_qudongdianlu_2_bbb),
    .AAA(shumaguan_16jinzhi_qudongdianlu_2_aaa), .FFF(shumaguan_16jinzhi_qudongdianlu_2_fff),
    .GGG(shumaguan_16jinzhi_qudongdianlu_2_ggg), .EEE(shumaguan_16jinzhi_qudongdianlu_2_eee),
    .DDD(shumaguan_16jinzhi_qudongdianlu_2_ddd), .CCC(shumaguan_16jinzhi_qudongdianlu_2_ccc),
    .HHH(shumaguan_16jinzhi_qudongdianlu_2_hhh));
  _7_Segment_Display u_7_segment_display_1 (
    .g(shumaguan_16jinzhi_qudongdianlu_1_ggg), .f(shumaguan_16jinzhi_qudongdianlu_1_fff),
    .a(shumaguan_16jinzhi_qudongdianlu_1_aaa), .b(shumaguan_16jinzhi_qudongdianlu_1_bbb),
    .e(shumaguan_16jinzhi_qudongdianlu_1_eee), .d(shumaguan_16jinzhi_qudongdianlu_1_ddd),
    .c(shumaguan_16jinzhi_qudongdianlu_1_ccc), .dp(shumaguan_16jinzhi_qudongdianlu_1_hhh));
  _7_Segment_Display u_7_segment_display_2 (
    .g(shumaguan_16jinzhi_qudongdianlu_2_ggg), .f(shumaguan_16jinzhi_qudongdianlu_2_fff),
    .a(shumaguan_16jinzhi_qudongdianlu_2_aaa), .b(shumaguan_16jinzhi_qudongdianlu_2_bbb),
    .e(shumaguan_16jinzhi_qudongdianlu_2_eee), .d(shumaguan_16jinzhi_qudongdianlu_2_ddd),
    .c(shumaguan_16jinzhi_qudongdianlu_2_ccc), .dp(shumaguan_16jinzhi_qudongdianlu_2_hhh));
endmodule

module Timer (
  input  EN
);

  wire and_1_out, and_2_out, and_3_out, and_4_out, and_5_out, and_6_out, and_7_out, and_8_out, and_9_out,
       and_10_out, and_11_out, and_12_out, and_13_out, and_14_out, and_15_out, and_16_out, and_17_out,
       and_18_out, and_19_out, and_20_out, and_21_out, and_22_out, and_23_out, and_24_out, and_25_out,
       and_26_out, and_27_out, and_28_out, and_29_out, CLK_out, four_register_jicunqi_1_y0,
       four_register_jicunqi_1_y1, four_register_jicunqi_1_y2, four_register_jicunqi_1_y3,
       four_register_jicunqi_2_y0, four_register_jicunqi_2_y1, four_register_jicunqi_2_y2,
       four_register_jicunqi_2_y3, four_register_jicunqi_3_y0, four_register_jicunqi_3_y1,
       four_register_jicunqi_3_y2, four_register_jicunqi_3_y3, four_register_jicunqi_4_y0,
       four_register_jicunqi_4_y1, four_register_jicunqi_4_y2, four_register_jicunqi_4_y3, min_gewei_aaa,
       min_gewei_bbb, min_gewei_ccc, min_gewei_ddd, min_gewei_eee, min_gewei_fff, min_gewei_ggg,
       min_gewei_hhh, min_shiwei_aaa, min_shiwei_bbb, min_shiwei_ccc, min_shiwei_ddd, min_shiwei_eee,
       min_shiwei_fff, min_shiwei_ggg, min_shiwei_hhh, not_1_out, not_2_out, not_3_out, not_4_out, not_5_out,
       not_6_out, not_7_out, not_8_out, not_9_out, not_10_out, not_11_out, not_12_out, not_13_out,
       not_14_out, not_15_out, not_16_out, not_17_out, not_18_out, not_19_out, not_20_out, not_21_out,
       not_22_out, not_23_out, not_24_out, not_25_out, not_26_out, not_27_out, not_28_out, not_29_out,
       not_30_out, not_31_out, not_32_out, not_33_out, not_34_out, not_35_out, not_36_out,
       rca_four_adder_1_out_0, rca_four_adder_1_out_1, rca_four_adder_1_out_2, rca_four_adder_1_out_3,
       rca_four_adder_2_out_0, rca_four_adder_2_out_1, rca_four_adder_2_out_2, rca_four_adder_2_out_3,
       rca_four_adder_3_out_0, rca_four_adder_3_out_1, rca_four_adder_3_out_2, rca_four_adder_3_out_3,
       rca_four_adder_4_out_0, rca_four_adder_4_out_1, rca_four_adder_4_out_2, rca_four_adder_4_out_3,
       sec_gewei_aaa, sec_gewei_bbb, sec_gewei_ccc, sec_gewei_ddd, sec_gewei_eee, sec_gewei_fff,
       sec_gewei_ggg, sec_gewei_hhh, sec_shiwei_aaa, sec_shiwei_bbb, sec_shiwei_ccc, sec_shiwei_ddd,
       sec_shiwei_eee, sec_shiwei_fff, sec_shiwei_ggg, sec_shiwei_hhh;

  Clock CLK (.out(CLK_out));
  RCA_Four_adder rca_four_adder_1 (
    .A3(four_register_jicunqi_1_y3), .A2(four_register_jicunqi_1_y2), .A1(four_register_jicunqi_1_y1),
    .A0(four_register_jicunqi_1_y0), .B0(and_6_out), .OUT_3(rca_four_adder_1_out_3),
    .OUT_2(rca_four_adder_1_out_2), .OUT_1(rca_four_adder_1_out_1), .OUT_0(rca_four_adder_1_out_0));  // open: B3, B2, B1, C0, C4
  not not_1 (not_1_out, and_1_out);
  not not_2 (not_2_out, and_1_out);
  not not_3 (not_3_out, and_1_out);
  not not_4 (not_4_out, and_1_out);
  and and_1 (and_1_out, and_7_out, and_8_out, and_9_out, and_10_out);
  RCA_Four_adder rca_four_adder_2 (
    .A3(four_register_jicunqi_2_y3), .A2(four_register_jicunqi_2_y2), .A1(four_register_jicunqi_2_y1),
    .A0(four_register_jicunqi_2_y0), .B0(and_18_out), .OUT_3(rca_four_adder_2_out_3),
    .OUT_2(rca_four_adder_2_out_2), .OUT_1(rca_four_adder_2_out_1), .OUT_0(rca_four_adder_2_out_0));  // open: B3, B2, B1, C0, C4
  and and_2 (and_2_out, rca_four_adder_1_out_3, not_1_out);
  and and_3 (and_3_out, rca_four_adder_1_out_2, not_2_out);
  and and_4 (and_4_out, rca_four_adder_1_out_1, not_3_out);
  and and_5 (and_5_out, rca_four_adder_1_out_0, not_4_out);
  not not_5 (not_5_out, and_6_out);
  not not_6 (not_6_out, and_6_out);
  not not_7 (not_7_out, and_6_out);
  not not_8 (not_8_out, and_6_out);
  and and_6 (and_6_out, and_16_out, and_15_out, and_17_out);
  and and_7 (and_7_out, not_9_out, four_register_jicunqi_1_y2, not_10_out, four_register_jicunqi_1_y0);
  and and_8 (and_8_out, four_register_jicunqi_2_y3, not_11_out, not_12_out, four_register_jicunqi_2_y0);
  and and_9 (and_9_out, four_register_jicunqi_4_y3, not_13_out, not_14_out, four_register_jicunqi_4_y0);
  and and_10 (and_10_out, not_15_out, four_register_jicunqi_3_y2, not_16_out, four_register_jicunqi_3_y0);
  and and_11 (and_11_out, rca_four_adder_2_out_3, not_5_out);
  and and_12 (and_12_out, rca_four_adder_2_out_2, not_6_out);
  and and_13 (and_13_out, rca_four_adder_2_out_1, not_7_out);
  and and_14 (and_14_out, rca_four_adder_2_out_0, not_8_out);
  not not_9 (not_9_out, four_register_jicunqi_1_y3);
  not not_10 (not_10_out, four_register_jicunqi_1_y1);
  not not_11 (not_11_out, four_register_jicunqi_2_y2);
  not not_12 (not_12_out, four_register_jicunqi_2_y1);
  not not_13 (not_13_out, four_register_jicunqi_4_y2);
  not not_14 (not_14_out, four_register_jicunqi_4_y1);
  and and_15 (and_15_out, not_21_out, four_register_jicunqi_3_y2, not_22_out, four_register_jicunqi_3_y0);
  and and_16 (and_16_out, four_register_jicunqi_4_y3, not_17_out, not_18_out, four_register_jicunqi_4_y0);
  and and_17 (and_17_out, four_register_jicunqi_2_y3, not_19_out, not_20_out, four_register_jicunqi_2_y0);
  not not_15 (not_15_out, four_register_jicunqi_3_y3);
  not not_16 (not_16_out, four_register_jicunqi_3_y1);
  not not_17 (not_17_out, four_register_jicunqi_4_y2);
  not not_18 (not_18_out, four_register_jicunqi_4_y1);
  not not_19 (not_19_out, four_register_jicunqi_2_y2);
  not not_20 (not_20_out, four_register_jicunqi_2_y1);
  FOUR_register_jicunqi four_register_jicunqi_1 (
    .A3(and_2_out), .A2(and_3_out), .A1(and_4_out), .A0(and_5_out), .EN(EN), .CLK(CLK_out),
    .Y3(four_register_jicunqi_1_y3), .Y2(four_register_jicunqi_1_y2), .Y1(four_register_jicunqi_1_y1),
    .Y0(four_register_jicunqi_1_y0));
  not not_21 (not_21_out, four_register_jicunqi_3_y3);
  not not_22 (not_22_out, four_register_jicunqi_3_y1);
  FOUR_register_jicunqi four_register_jicunqi_2 (
    .A3(and_11_out), .A2(and_12_out), .A1(and_13_out), .A0(and_14_out), .EN(EN), .CLK(CLK_out),
    .Y3(four_register_jicunqi_2_y3), .Y2(four_register_jicunqi_2_y2), .Y1(four_register_jicunqi_2_y1),
    .Y0(four_register_jicunqi_2_y0));
  RCA_Four_adder rca_four_adder_3 (
    .A3(four_register_jicunqi_3_y3), .A2(four_register_jicunqi_3_y2), .A1(four_register_jicunqi_3_y1),
    .A0(four_register_jicunqi_3_y0), .B0(and_29_out), .OUT_3(rca_four_adder_3_out_3),
    .OUT_2(rca_four_adder_3_out_2), .OUT_1(rca_four_adder_3_out_1), .OUT_0(rca_four_adder_3_out_0));  // open: B3, B2, B1, C0, C4
  not not_23 (not_23_out, and_18_out);
  not not_24 (not_24_out, and_18_out);
  not not_25 (not_25_out, and_18_out);
  not not_26 (not_26_out, and_18_out);
  and and_18 (and_18_out, and_23_out, and_24_out);
  and and_19 (and_19_out, rca_four_adder_3_out_3, not_23_out);
  and and_20 (and_20_out, rca_four_adder_3_out_2, not_24_out);
  and and_21 (and_21_out, rca_four_adder_3_out_1, not_25_out);
  and and_22 (and_22_out, rca_four_adder_3_out_0, not_26_out);
  and and_23 (and_23_out, not_27_out, four_register_jicunqi_3_y2, not_28_out, four_register_jicunqi_3_y0);
  and and_24 (and_24_out, four_register_jicunqi_4_y3, not_29_out, not_30_out, four_register_jicunqi_4_y0);
  not not_27 (not_27_out, four_register_jicunqi_3_y3);
  not not_28 (not_28_out, four_register_jicunqi_3_y1);
  not not_29 (not_29_out, four_register_jicunqi_4_y2);
  not not_30 (not_30_out, four_register_jicunqi_4_y1);
  FOUR_register_jicunqi four_register_jicunqi_3 (
    .A3(and_19_out), .A2(and_20_out), .A1(and_21_out), .A0(and_22_out), .EN(EN), .CLK(CLK_out),
    .Y3(four_register_jicunqi_3_y3), .Y2(four_register_jicunqi_3_y2), .Y1(four_register_jicunqi_3_y1),
    .Y0(four_register_jicunqi_3_y0));
  RCA_Four_adder rca_four_adder_4 (
    .A3(four_register_jicunqi_4_y3), .A2(four_register_jicunqi_4_y2), .A1(four_register_jicunqi_4_y1),
    .A0(four_register_jicunqi_4_y0), .B0(EN), .OUT_3(rca_four_adder_4_out_3), .OUT_2(rca_four_adder_4_out_2),
    .OUT_1(rca_four_adder_4_out_1), .OUT_0(rca_four_adder_4_out_0));  // open: B3, B2, B1, C0, C4
  and and_25 (and_25_out, rca_four_adder_4_out_3, not_31_out);
  not not_31 (not_31_out, and_29_out);
  and and_26 (and_26_out, rca_four_adder_4_out_2, not_32_out);
  not not_32 (not_32_out, and_29_out);
  and and_27 (and_27_out, rca_four_adder_4_out_1, not_33_out);
  not not_33 (not_33_out, and_29_out);
  and and_28 (and_28_out, rca_four_adder_4_out_0, not_34_out);
  not not_34 (not_34_out, and_29_out);
  and and_29 (and_29_out, four_register_jicunqi_4_y3, not_35_out, not_36_out, four_register_jicunqi_4_y0);
  shumaguan_10jinzhi_qudongdianlu min_shiwei (
    .in_1(four_register_jicunqi_1_y3), .in_2(four_register_jicunqi_1_y2), .in_3(four_register_jicunqi_1_y1),
    .in_4(four_register_jicunqi_1_y0), .BBB(min_shiwei_bbb), .AAA(min_shiwei_aaa), .FFF(min_shiwei_fff),
    .GGG(min_shiwei_ggg), .EEE(min_shiwei_eee), .DDD(min_shiwei_ddd), .CCC(min_shiwei_ccc),
    .HHH(min_shiwei_hhh));
  shumaguan_10jinzhi_qudongdianlu min_gewei (
    .in_1(four_register_jicunqi_2_y3), .in_2(four_register_jicunqi_2_y2), .in_3(four_register_jicunqi_2_y1),
    .in_4(four_register_jicunqi_2_y0), .BBB(min_gewei_bbb), .AAA(min_gewei_aaa), .FFF(min_gewei_fff),
    .GGG(min_gewei_ggg), .EEE(min_gewei_eee), .DDD(min_gewei_ddd), .CCC(min_gewei_ccc), .HHH(min_gewei_hhh));
  not not_35 (not_35_out, four_register_jicunqi_4_y2);
  not not_36 (not_36_out, four_register_jicunqi_4_y1);
  _7_Segment_Display u_7_segment_display_1 (
    .g(min_shiwei_ggg), .f(min_shiwei_fff), .a(min_shiwei_aaa), .b(min_shiwei_bbb), .e(min_shiwei_eee),
    .d(min_shiwei_ddd), .c(min_shiwei_ccc), .dp(min_shiwei_hhh));
  FOUR_register_jicunqi four_register_jicunqi_4 (
    .A3(and_25_out), .A2(and_26_out), .A1(and_27_out), .A0(and_28_out), .EN(EN), .CLK(CLK_out),
    .Y3(four_register_jicunqi_4_y3), .Y2(four_register_jicunqi_4_y2), .Y1(four_register_jicunqi_4_y1),
    .Y0(four_register_jicunqi_4_y0));
  _7_Segment_Display u_7_segment_display_2 (
    .g(min_gewei_ggg), .f(min_gewei_fff), .a(min_gewei_aaa), .b(min_gewei_bbb), .e(min_gewei_eee),
    .d(min_gewei_ddd), .c(min_gewei_ccc), .dp(min_gewei_hhh));
  shumaguan_10jinzhi_qudongdianlu sec_shiwei (
    .in_1(four_register_jicunqi_3_y3), .in_2(four_register_jicunqi_3_y2), .in_3(four_register_jicunqi_3_y1),
    .in_4(four_register_jicunqi_3_y0), .BBB(sec_shiwei_bbb), .AAA(sec_shiwei_aaa), .FFF(sec_shiwei_fff),
    .GGG(sec_shiwei_ggg), .EEE(sec_shiwei_eee), .DDD(sec_shiwei_ddd), .CCC(sec_shiwei_ccc),
    .HHH(sec_shiwei_hhh));
  shumaguan_10jinzhi_qudongdianlu sec_gewei (
    .in_1(four_register_jicunqi_4_y3), .in_2(four_register_jicunqi_4_y2), .in_3(four_register_jicunqi_4_y1),
    .in_4(four_register_jicunqi_4_y0), .BBB(sec_gewei_bbb), .AAA(sec_gewei_aaa), .FFF(sec_gewei_fff),
    .GGG(sec_gewei_ggg), .EEE(sec_gewei_eee), .DDD(sec_gewei_ddd), .CCC(sec_gewei_ccc), .HHH(sec_gewei_hhh));
  _7_Segment_Display u_7_segment_display_3 (
    .g(sec_shiwei_ggg), .f(sec_shiwei_fff), .a(sec_shiwei_aaa), .b(sec_shiwei_bbb), .e(sec_shiwei_eee),
    .d(sec_shiwei_ddd), .c(sec_shiwei_ccc), .dp(sec_shiwei_hhh));
  _7_Segment_Display u_7_segment_display_4 (
    .g(sec_gewei_ggg), .f(sec_gewei_fff), .a(sec_gewei_aaa), .b(sec_gewei_bbb), .e(sec_gewei_eee),
    .d(sec_gewei_ddd), .c(sec_gewei_ccc), .dp(sec_gewei_hhh));

  // Notes on the sheet:
  //   这一部分是复位信号C，有四个条件：分的十位为5，个位为9，秒为“5”和“9”时写入0000
  //   这一部分是复位信号C，有三个条件（还有一个 与门在上面），为分的个位为9，秒为“5”和“9”时写入0000，并且作为进位信号传给分的十位进行一次加1
  //   这一部分为复位信号B，条件为秒的十位为5个位为9时写入0000，并且作为进位信号传给分的个位进行一次加1
  //   这一部分是复位信号A，条件为当（秒）个位为9需要写入数据0000，同时作为进位信号传给秒的十位进行一次加1
endmodule

module ROM_fetch (
  input  [2:0] in_1,
  output Y7,
  output Y6,
  output Y5,
  output Y0,
  output Y4,
  output Y3,
  output Y2,
  output Y1
);

  wire and_1_out, and_2_out, and_3_out, and_4_out, and_5_out, and_6_out, and_7_out, and_8_out, and_9_out,
       and_10_out, and_11_out, and_12_out, and_13_out, and_14_out, and_15_out, and_16_out, and_17_out,
       and_18_out, and_19_out, and_20_out, and_21_out, and_22_out, and_23_out, and_24_out, and_25_out,
       and_26_out, and_27_out, and_28_out, and_29_out, and_30_out, and_31_out, and_32_out, and_33_out,
       and_34_out, and_35_out, and_36_out, and_37_out, and_38_out, and_39_out, and_40_out, and_41_out,
       and_42_out, and_43_out, and_44_out, and_45_out, and_46_out, and_47_out, and_48_out, and_49_out,
       and_50_out, and_51_out, and_52_out, and_53_out, and_54_out, and_55_out, and_56_out, and_57_out,
       and_58_out, and_59_out, and_60_out, and_61_out, and_62_out, and_63_out, and_64_out,
       three_8yimaqi_no2_4yimaqi_1_y0, three_8yimaqi_no2_4yimaqi_1_y1, three_8yimaqi_no2_4yimaqi_1_y2,
       three_8yimaqi_no2_4yimaqi_1_y3, three_8yimaqi_no2_4yimaqi_1_y4, three_8yimaqi_no2_4yimaqi_1_y5,
       three_8yimaqi_no2_4yimaqi_1_y6, three_8yimaqi_no2_4yimaqi_1_y7;

  Three_8yimaqi_NO2_4yimaqi three_8yimaqi_no2_4yimaqi_1 (
    .A2(in_1[2]), .A1(in_1[1]), .A0(in_1[0]), .Y0(three_8yimaqi_no2_4yimaqi_1_y0),
    .Y1(three_8yimaqi_no2_4yimaqi_1_y1), .Y2(three_8yimaqi_no2_4yimaqi_1_y2),
    .Y3(three_8yimaqi_no2_4yimaqi_1_y3), .Y4(three_8yimaqi_no2_4yimaqi_1_y4),
    .Y5(three_8yimaqi_no2_4yimaqi_1_y5), .Y6(three_8yimaqi_no2_4yimaqi_1_y6),
    .Y7(three_8yimaqi_no2_4yimaqi_1_y7));
  and and_1 (and_1_out, three_8yimaqi_no2_4yimaqi_1_y0, 1'b1);
  and and_2 (and_2_out, three_8yimaqi_no2_4yimaqi_1_y1, 1'b1);
  and and_3 (and_3_out, three_8yimaqi_no2_4yimaqi_1_y2, 1'b0);
  and and_4 (and_4_out, three_8yimaqi_no2_4yimaqi_1_y3, 1'b0);
  and and_5 (and_5_out, three_8yimaqi_no2_4yimaqi_1_y4, 1'b1);
  and and_6 (and_6_out, three_8yimaqi_no2_4yimaqi_1_y5, 1'b1);
  and and_7 (and_7_out, three_8yimaqi_no2_4yimaqi_1_y6, 1'b1);
  and and_8 (and_8_out, three_8yimaqi_no2_4yimaqi_1_y7, 1'b1);
  or or_1 (Y7, and_8_out, and_7_out, and_6_out, and_5_out, and_4_out, and_3_out, and_2_out, and_1_out);
  and and_9 (and_9_out, three_8yimaqi_no2_4yimaqi_1_y0, 1'b1);
  and and_10 (and_10_out, three_8yimaqi_no2_4yimaqi_1_y1, 1'b1);
  and and_11 (and_11_out, three_8yimaqi_no2_4yimaqi_1_y2, 1'b0);
  and and_12 (and_12_out, three_8yimaqi_no2_4yimaqi_1_y3, 1'b0);
  and and_13 (and_13_out, three_8yimaqi_no2_4yimaqi_1_y4, 1'b0);
  and and_14 (and_14_out, three_8yimaqi_no2_4yimaqi_1_y5, 1'b0);
  and and_15 (and_15_out, three_8yimaqi_no2_4yimaqi_1_y6, 1'b0);
  and and_16 (and_16_out, three_8yimaqi_no2_4yimaqi_1_y7, 1'b0);
  or or_2 (Y6, and_16_out, and_15_out, and_14_out, and_13_out, and_12_out, and_11_out, and_10_out, and_9_out);
  and and_17 (and_17_out, three_8yimaqi_no2_4yimaqi_1_y0, 1'b0);
  and and_18 (and_18_out, three_8yimaqi_no2_4yimaqi_1_y1, 1'b0);
  and and_19 (and_19_out, three_8yimaqi_no2_4yimaqi_1_y2, 1'b1);
  and and_20 (and_20_out, three_8yimaqi_no2_4yimaqi_1_y3, 1'b0);
  and and_21 (and_21_out, three_8yimaqi_no2_4yimaqi_1_y4, 1'b1);
  and and_22 (and_22_out, three_8yimaqi_no2_4yimaqi_1_y5, 1'b1);
  and and_23 (and_23_out, three_8yimaqi_no2_4yimaqi_1_y6, 1'b0);
  and and_24 (and_24_out, three_8yimaqi_no2_4yimaqi_1_y7, 1'b0);
  or or_3 (Y5, and_24_out, and_23_out, and_22_out, and_21_out, and_20_out, and_19_out, and_18_out, and_17_out);
  and and_25 (and_25_out, three_8yimaqi_no2_4yimaqi_1_y0, 1'b1);
  and and_26 (and_26_out, three_8yimaqi_no2_4yimaqi_1_y1, 1'b1);
  and and_27 (and_27_out, three_8yimaqi_no2_4yimaqi_1_y2, 1'b0);
  and and_28 (and_28_out, three_8yimaqi_no2_4yimaqi_1_y3, 1'b1);
  and and_29 (and_29_out, three_8yimaqi_no2_4yimaqi_1_y4, 1'b1);
  and and_30 (and_30_out, three_8yimaqi_no2_4yimaqi_1_y5, 1'b0);
  and and_31 (and_31_out, three_8yimaqi_no2_4yimaqi_1_y6, 1'b1);
  and and_32 (and_32_out, three_8yimaqi_no2_4yimaqi_1_y7, 1'b0);
  or or_4 (Y4, and_32_out, and_31_out, and_30_out, and_29_out, and_28_out, and_27_out, and_26_out, and_25_out);
  and and_33 (and_33_out, three_8yimaqi_no2_4yimaqi_1_y0, 1'b1);
  and and_34 (and_34_out, three_8yimaqi_no2_4yimaqi_1_y1, 1'b0);
  and and_35 (and_35_out, three_8yimaqi_no2_4yimaqi_1_y2, 1'b1);
  and and_36 (and_36_out, three_8yimaqi_no2_4yimaqi_1_y3, 1'b0);
  and and_37 (and_37_out, three_8yimaqi_no2_4yimaqi_1_y4, 1'b0);
  and and_38 (and_38_out, three_8yimaqi_no2_4yimaqi_1_y5, 1'b0);
  and and_39 (and_39_out, three_8yimaqi_no2_4yimaqi_1_y6, 1'b0);
  and and_40 (and_40_out, three_8yimaqi_no2_4yimaqi_1_y7, 1'b1);
  or or_5 (Y3, and_40_out, and_39_out, and_38_out, and_37_out, and_36_out, and_35_out, and_34_out, and_33_out);
  and and_41 (and_41_out, three_8yimaqi_no2_4yimaqi_1_y0, 1'b1);
  and and_42 (and_42_out, three_8yimaqi_no2_4yimaqi_1_y1, 1'b0);
  and and_43 (and_43_out, three_8yimaqi_no2_4yimaqi_1_y2, 1'b0);
  and and_44 (and_44_out, three_8yimaqi_no2_4yimaqi_1_y3, 1'b1);
  and and_45 (and_45_out, three_8yimaqi_no2_4yimaqi_1_y4, 1'b0);
  and and_46 (and_46_out, three_8yimaqi_no2_4yimaqi_1_y5, 1'b0);
  and and_47 (and_47_out, three_8yimaqi_no2_4yimaqi_1_y6, 1'b0);
  and and_48 (and_48_out, three_8yimaqi_no2_4yimaqi_1_y7, 1'b0);
  or or_6 (Y2, and_48_out, and_47_out, and_46_out, and_45_out, and_44_out, and_43_out, and_42_out, and_41_out);
  and and_49 (and_49_out, three_8yimaqi_no2_4yimaqi_1_y0, 1'b1);
  and and_50 (and_50_out, three_8yimaqi_no2_4yimaqi_1_y1, 1'b0);
  and and_51 (and_51_out, three_8yimaqi_no2_4yimaqi_1_y2, 1'b0);
  and and_52 (and_52_out, three_8yimaqi_no2_4yimaqi_1_y3, 1'b1);
  and and_53 (and_53_out, three_8yimaqi_no2_4yimaqi_1_y4, 1'b0);
  and and_54 (and_54_out, three_8yimaqi_no2_4yimaqi_1_y5, 1'b0);
  and and_55 (and_55_out, three_8yimaqi_no2_4yimaqi_1_y6, 1'b0);
  and and_56 (and_56_out, three_8yimaqi_no2_4yimaqi_1_y7, 1'b1);
  or or_7 (Y1, and_56_out, and_55_out, and_54_out, and_53_out, and_52_out, and_51_out, and_50_out, and_49_out);
  and and_57 (and_57_out, three_8yimaqi_no2_4yimaqi_1_y0, 1'b1);
  and and_58 (and_58_out, three_8yimaqi_no2_4yimaqi_1_y1, 1'b1);
  and and_59 (and_59_out, three_8yimaqi_no2_4yimaqi_1_y2, 1'b1);
  and and_60 (and_60_out, three_8yimaqi_no2_4yimaqi_1_y3, 1'b1);
  and and_61 (and_61_out, three_8yimaqi_no2_4yimaqi_1_y4, 1'b1);
  and and_62 (and_62_out, three_8yimaqi_no2_4yimaqi_1_y5, 1'b0);
  and and_63 (and_63_out, three_8yimaqi_no2_4yimaqi_1_y6, 1'b0);
  and and_64 (and_64_out, three_8yimaqi_no2_4yimaqi_1_y7, 1'b0);
  or or_8 (Y0, and_64_out, and_63_out, and_62_out, and_61_out, and_60_out, and_59_out, and_58_out, and_57_out);

  // Notes on the sheet:
  //   10001010    # 0: li r0, 10 10010000    # 1: li r1, 0 10100000    # 2: li r2, 0 10110001    # 3: li r3, 1 00010111    # 4: add r1, r1, r3 00101001    # 5: add r2, r2, r1 11010001    # 6: bner0 r1, 4 11011111    # 7: bner0 r3, 7
  //   指令存储顺序为从下往上
endmodule

module ROM_MUX (
  input  [7:0] in_1,
  input  [7:0] in_2,
  input  [7:0] in_3,
  input  [7:0] in_4,
  input  [7:0] in_5,
  input  [7:0] in_6,
  input  [7:0] in_7,
  input  [7:0] in_8,
  input  in_9,
  input  RESET,
  output [7:0] Y
);

  wire and_1_out, and_2_out, and_3_out, and_4_out, and_5_out, clock_1_out, four_jianfaqi_1_out_0,
       four_jianfaqi_1_out_1, four_jianfaqi_1_out_2, not_1_out, not_2_out, not_3_out, not_4_out, or_1_out,
       rca_four_adder_1_out_0, rca_four_adder_1_out_1, rca_four_adder_1_out_2, two_choose1_1_y,
       two_choose1_2_y, two_choose1_3_y;
  wire [2:0] four_register_jicunqi_1_y0;

  RCA_Four_adder rca_four_adder_1 (
    .A2(four_register_jicunqi_1_y0[2]), .A1(four_register_jicunqi_1_y0[1]),
    .A0(four_register_jicunqi_1_y0[0]), .B0(and_1_out), .OUT_2(rca_four_adder_1_out_2),
    .OUT_1(rca_four_adder_1_out_1), .OUT_0(rca_four_adder_1_out_0));  // open: A3, B3, B2, B1, C0, OUT_3, C4
  four_jianfaqi four_jianfaqi_1 (
    .A2(four_register_jicunqi_1_y0[2]), .A1(four_register_jicunqi_1_y0[1]),
    .A0(four_register_jicunqi_1_y0[0]), .B1(and_2_out), .B0(and_2_out), .out_2(four_jianfaqi_1_out_2),
    .out_1(four_jianfaqi_1_out_1), .out_0(four_jianfaqi_1_out_0));  // open: A3, B3, B2, out_3
  not not_1 (not_1_out, and_2_out);
  and and_1 (and_1_out, or_1_out, not_1_out);
  or or_1 (or_1_out, Y[0], Y[1], Y[2], Y[3], Y[4], Y[5], Y[6], Y[7]);
  Multiplexer #(.select(3), .width(8)) multiplexer_1 (
    .in0(in_1), .in1(in_2), .in2(in_3), .in3(in_4), .in4(in_5), .in5(in_6), .in6(in_7), .in7(in_8), .out(Y),
    .sel(four_register_jicunqi_1_y0));
  TWO_choose1 two_choose1_1 (
    .A(rca_four_adder_1_out_2), .SEL(and_1_out), .B(four_jianfaqi_1_out_2), .Y(two_choose1_1_y));
  TWO_choose1 two_choose1_2 (
    .A(rca_four_adder_1_out_1), .SEL(and_1_out), .B(four_jianfaqi_1_out_1), .Y(two_choose1_2_y));
  TWO_choose1 two_choose1_3 (
    .A(rca_four_adder_1_out_0), .SEL(and_1_out), .B(four_jianfaqi_1_out_0), .Y(two_choose1_3_y));
  and and_2 (and_2_out, Y[7], Y[6]);
  and and_3 (and_3_out, two_choose1_1_y, not_2_out);
  not not_2 (not_2_out, RESET);
  and and_4 (and_4_out, two_choose1_2_y, not_3_out);
  not not_3 (not_3_out, RESET);
  and and_5 (and_5_out, two_choose1_3_y, not_4_out);
  not not_4 (not_4_out, RESET);
  Clock clock_1 (.out(clock_1_out));
  FOUR_register_jicunqi four_register_jicunqi_1 (
    .A2(and_3_out), .A1(and_4_out), .A0(and_5_out), .EN(in_9), .CLK(clock_1_out),
    .Y2(four_register_jicunqi_1_y0[2]), .Y1(four_register_jicunqi_1_y0[1]), .Y0(four_register_jicunqi_1_y0[0]));  // open: A3, Y3

  // Notes on the sheet:
  //   bner0信号成立，减3得到PC=4然后存入寄存器
  //   指令顺序为从上到下
  //   与门为1说明bner0信号要来了！
endmodule

module ROM_MUXX (
  input  [7:0] in_1,
  input  [7:0] in_2,
  input  [7:0] in_3,
  input  [7:0] in_4,
  input  [7:0] in_5,
  input  [7:0] in_6,
  input  [7:0] in_7,
  input  [7:0] in_8,
  input  EN,
  output [7:0] Y
);

  wire clock_1_out;
  wire [2:0] four_counter_1_y2;

  Clock clock_1 (.out(clock_1_out));
  Multiplexer #(.select(3), .width(8)) multiplexer_1 (
    .in0(in_1), .in1(in_2), .in2(in_3), .in3(in_4), .in4(in_5), .in5(in_6), .in6(in_7), .in7(in_8), .out(Y),
    .sel(four_counter_1_y2));
  FOUR_counter four_counter_1 (
    .EN(EN), .CLK(clock_1_out), .Y2(four_counter_1_y2[0]), .Y1(four_counter_1_y2[1]),
    .Y0(four_counter_1_y2[2]));  // open: Y3
endmodule
module RAM_GPRwriting (
  input  D7,
  input  D6,
  input  D5,
  input  D4,
  input  D3,
  input  D2,
  input  D1,
  input  D0,
  input  addr_2,
  input  addr_1,
  input  addr_0,
  input  Write_EN,
  input  clkk,
  output Y7,
  output Y6,
  output Y5,
  output Y4,
  output Y3,
  output Y2,
  output Y1,
  output Y0
);

  wire and_1_out, and_2_out, and_3_out, and_4_out, and_5_out, and_6_out, and_7_out, and_8_out, and_9_out,
       and_10_out, and_11_out, and_12_out, and_13_out, and_14_out, and_15_out, and_16_out, and_17_out,
       and_18_out, and_19_out, and_20_out, and_21_out, and_22_out, and_23_out, and_24_out, and_25_out,
       and_26_out, and_27_out, and_28_out, and_29_out, and_30_out, and_31_out, and_32_out, and_33_out,
       and_34_out, and_35_out, and_36_out, and_37_out, and_38_out, and_39_out, and_40_out, and_41_out,
       and_42_out, and_43_out, and_44_out, and_45_out, and_46_out, and_47_out, and_48_out, and_49_out,
       and_50_out, and_51_out, and_52_out, and_53_out, and_54_out, and_55_out, and_56_out, and_57_out,
       and_58_out, and_59_out, and_60_out, and_61_out, and_62_out, and_63_out, and_64_out, and_65_out,
       and_66_out, and_67_out, and_68_out, and_69_out, and_70_out, and_71_out, and_72_out, d_ff_with_en_1_q,
       d_ff_with_en_2_q, d_ff_with_en_3_q, d_ff_with_en_4_q, d_ff_with_en_5_q, d_ff_with_en_6_q,
       d_ff_with_en_7_q, d_ff_with_en_8_q, d_ff_with_en_8_q_fan, d_ff_with_en_9_q, d_ff_with_en_10_q,
       d_ff_with_en_11_q, d_ff_with_en_12_q, d_ff_with_en_13_q, d_ff_with_en_14_q, d_ff_with_en_15_q,
       d_ff_with_en_16_q, d_ff_with_en_17_q, d_ff_with_en_18_q, d_ff_with_en_19_q, d_ff_with_en_20_q,
       d_ff_with_en_21_q, d_ff_with_en_22_q, d_ff_with_en_23_q, d_ff_with_en_24_q, d_ff_with_en_24_q_fan,
       d_ff_with_en_25_q, d_ff_with_en_26_q, d_ff_with_en_27_q, d_ff_with_en_28_q, d_ff_with_en_29_q,
       d_ff_with_en_30_q, d_ff_with_en_31_q, d_ff_with_en_32_q, d_ff_with_en_32_q_fan, d_ff_with_en_33_q,
       d_ff_with_en_34_q, d_ff_with_en_35_q, d_ff_with_en_36_q, d_ff_with_en_37_q, d_ff_with_en_38_q,
       d_ff_with_en_39_q, d_ff_with_en_40_q, d_ff_with_en_40_q_fan, d_ff_with_en_41_q, d_ff_with_en_42_q,
       d_ff_with_en_43_q, d_ff_with_en_44_q, d_ff_with_en_45_q, d_ff_with_en_46_q, d_ff_with_en_47_q,
       d_ff_with_en_48_q, d_ff_with_en_48_q_fan, d_ff_with_en_49_q, d_ff_with_en_50_q, d_ff_with_en_51_q,
       d_ff_with_en_52_q, d_ff_with_en_53_q, d_ff_with_en_54_q, d_ff_with_en_55_q, d_ff_with_en_56_q,
       d_ff_with_en_56_q_fan, d_ff_with_en_57_q, d_ff_with_en_58_q, d_ff_with_en_59_q, d_ff_with_en_60_q,
       d_ff_with_en_61_q, d_ff_with_en_62_q, d_ff_with_en_63_q, d_ff_with_en_64_q, d_ff_with_en_64_q_fan,
       three_8yimaqi_no2_4yimaqi_1_y0, three_8yimaqi_no2_4yimaqi_1_y1, three_8yimaqi_no2_4yimaqi_1_y2,
       three_8yimaqi_no2_4yimaqi_1_y3, three_8yimaqi_no2_4yimaqi_1_y4, three_8yimaqi_no2_4yimaqi_1_y5,
       three_8yimaqi_no2_4yimaqi_1_y6, three_8yimaqi_no2_4yimaqi_1_y7;

  Clock CLK ();  // open: out
  Three_8yimaqi_NO2_4yimaqi three_8yimaqi_no2_4yimaqi_1 (
    .A2(addr_2), .A1(addr_1), .A0(addr_0), .Y0(three_8yimaqi_no2_4yimaqi_1_y0),
    .Y1(three_8yimaqi_no2_4yimaqi_1_y1), .Y2(three_8yimaqi_no2_4yimaqi_1_y2),
    .Y3(three_8yimaqi_no2_4yimaqi_1_y3), .Y4(three_8yimaqi_no2_4yimaqi_1_y4),
    .Y5(three_8yimaqi_no2_4yimaqi_1_y5), .Y6(three_8yimaqi_no2_4yimaqi_1_y6),
    .Y7(three_8yimaqi_no2_4yimaqi_1_y7));
  and and_1 (and_1_out, three_8yimaqi_no2_4yimaqi_1_y0, Write_EN);
  and and_2 (and_2_out, three_8yimaqi_no2_4yimaqi_1_y1, Write_EN);
  and and_3 (and_3_out, three_8yimaqi_no2_4yimaqi_1_y2, Write_EN);
  and and_4 (and_4_out, three_8yimaqi_no2_4yimaqi_1_y3, Write_EN);
  and and_5 (and_5_out, three_8yimaqi_no2_4yimaqi_1_y4, Write_EN);
  and and_6 (and_6_out, three_8yimaqi_no2_4yimaqi_1_y5, Write_EN);
  and and_7 (and_7_out, three_8yimaqi_no2_4yimaqi_1_y6, Write_EN);
  and and_8 (and_8_out, three_8yimaqi_no2_4yimaqi_1_y7, Write_EN);
  D_FF_with_EN d_ff_with_en_1 (.CLK(clkk), .D(D7), .EN(and_1_out), .Q(d_ff_with_en_1_q));  // open: reset, Q_fan
  D_FF_with_EN d_ff_with_en_2 (.CLK(clkk), .D(D7), .EN(and_2_out), .Q(d_ff_with_en_2_q));  // open: reset, Q_fan
  D_FF_with_EN d_ff_with_en_3 (.CLK(clkk), .D(D7), .EN(and_3_out), .Q(d_ff_with_en_3_q));  // open: reset, Q_fan
  D_FF_with_EN d_ff_with_en_4 (.CLK(clkk), .D(D7), .EN(and_4_out), .Q(d_ff_with_en_4_q));  // open: reset, Q_fan
  D_FF_with_EN d_ff_with_en_5 (.CLK(clkk), .D(D7), .EN(and_5_out), .Q(d_ff_with_en_5_q));  // open: reset, Q_fan
  D_FF_with_EN d_ff_with_en_6 (.CLK(clkk), .D(D7), .EN(and_6_out), .Q(d_ff_with_en_6_q));  // open: reset, Q_fan
  D_FF_with_EN d_ff_with_en_7 (.CLK(clkk), .D(D7), .EN(and_7_out), .Q(d_ff_with_en_7_q));  // open: reset, Q_fan
  D_FF_with_EN d_ff_with_en_8 (
    .CLK(clkk), .D(D7), .EN(and_8_out), .Q(d_ff_with_en_8_q), .Q_fan(d_ff_with_en_8_q_fan));  // open: reset
  and and_9 (and_9_out, and_5_out, d_ff_with_en_5_q);
  and and_10 (and_10_out, and_6_out, d_ff_with_en_6_q);
  and and_11 (and_11_out, and_7_out, d_ff_with_en_7_q);
  and and_12 (and_12_out, and_8_out, d_ff_with_en_8_q);
  and and_13 (and_13_out, three_8yimaqi_no2_4yimaqi_1_y0, d_ff_with_en_1_q);
  and and_14 (and_14_out, and_2_out, d_ff_with_en_2_q);
  and and_15 (and_15_out, and_3_out, d_ff_with_en_3_q);
  and and_16 (and_16_out, and_4_out, d_ff_with_en_4_q);
  or or_1 (Y7, and_12_out, and_11_out, and_10_out, and_9_out, and_16_out, and_15_out, and_14_out, and_13_out);
  D_FF_with_EN d_ff_with_en_9 (.CLK(clkk), .D(D6), .EN(and_1_out), .Q(d_ff_with_en_9_q));  // open: reset, Q_fan
  D_FF_with_EN d_ff_with_en_10 (.CLK(clkk), .D(D6), .EN(and_2_out), .Q(d_ff_with_en_10_q));  // open: reset, Q_fan
  D_FF_with_EN d_ff_with_en_11 (.CLK(clkk), .D(D6), .EN(and_3_out), .Q(d_ff_with_en_11_q));  // open: reset, Q_fan
  D_FF_with_EN d_ff_with_en_12 (.CLK(clkk), .D(D6), .EN(and_4_out), .Q(d_ff_with_en_12_q));  // open: reset, Q_fan
  D_FF_with_EN d_ff_with_en_13 (.CLK(clkk), .D(D6), .EN(and_5_out), .Q(d_ff_with_en_13_q));  // open: reset, Q_fan
  D_FF_with_EN d_ff_with_en_14 (.CLK(clkk), .D(D6), .EN(and_6_out), .Q(d_ff_with_en_14_q));  // open: reset, Q_fan
  D_FF_with_EN d_ff_with_en_15 (.CLK(clkk), .D(D6), .EN(and_7_out), .Q(d_ff_with_en_15_q));  // open: reset, Q_fan
  D_FF_with_EN d_ff_with_en_16 (.CLK(clkk), .D(D6), .EN(and_8_out), .Q(d_ff_with_en_16_q));  // open: reset, Q_fan
  and and_17 (and_17_out, and_5_out, d_ff_with_en_13_q);
  and and_18 (and_18_out, and_6_out, d_ff_with_en_14_q);
  and and_19 (and_19_out, and_7_out, d_ff_with_en_15_q);
  and and_20 (and_20_out, and_8_out, d_ff_with_en_16_q);
  and and_21 (and_21_out, three_8yimaqi_no2_4yimaqi_1_y0, d_ff_with_en_9_q);
  and and_22 (and_22_out, and_2_out, d_ff_with_en_10_q);
  and and_23 (and_23_out, and_3_out, d_ff_with_en_11_q);
  and and_24 (and_24_out, and_4_out, d_ff_with_en_12_q);
  or or_2 (Y6, and_20_out, and_19_out, and_18_out, and_17_out, and_24_out, and_23_out, and_22_out, and_21_out);
  D_FF_with_EN d_ff_with_en_17 (.CLK(clkk), .D(D5), .EN(and_1_out), .Q(d_ff_with_en_17_q));  // open: reset, Q_fan
  D_FF_with_EN d_ff_with_en_18 (.CLK(clkk), .D(D5), .EN(and_2_out), .Q(d_ff_with_en_18_q));  // open: reset, Q_fan
  D_FF_with_EN d_ff_with_en_19 (.CLK(clkk), .D(D5), .EN(and_3_out), .Q(d_ff_with_en_19_q));  // open: reset, Q_fan
  D_FF_with_EN d_ff_with_en_20 (.CLK(clkk), .D(D5), .EN(and_4_out), .Q(d_ff_with_en_20_q));  // open: reset, Q_fan
  D_FF_with_EN d_ff_with_en_21 (.CLK(clkk), .D(D5), .EN(and_5_out), .Q(d_ff_with_en_21_q));  // open: reset, Q_fan
  D_FF_with_EN d_ff_with_en_22 (.CLK(clkk), .D(D5), .EN(and_6_out), .Q(d_ff_with_en_22_q));  // open: reset, Q_fan
  D_FF_with_EN d_ff_with_en_23 (.CLK(clkk), .D(D5), .EN(and_7_out), .Q(d_ff_with_en_23_q));  // open: reset, Q_fan
  D_FF_with_EN d_ff_with_en_24 (
    .CLK(clkk), .D(D5), .EN(and_8_out), .Q(d_ff_with_en_24_q), .Q_fan(d_ff_with_en_24_q_fan));  // open: reset
  and and_25 (and_25_out, and_5_out, d_ff_with_en_21_q);
  and and_26 (and_26_out, and_6_out, d_ff_with_en_22_q);
  and and_27 (and_27_out, and_7_out, d_ff_with_en_23_q);
  and and_28 (and_28_out, and_8_out, d_ff_with_en_24_q);
  and and_29 (and_29_out, three_8yimaqi_no2_4yimaqi_1_y0, d_ff_with_en_17_q);
  and and_30 (and_30_out, and_2_out, d_ff_with_en_18_q);
  and and_31 (and_31_out, and_3_out, d_ff_with_en_19_q);
  and and_32 (and_32_out, and_4_out, d_ff_with_en_20_q);
  or or_3 (Y5, and_28_out, and_27_out, and_26_out, and_25_out, and_32_out, and_31_out, and_30_out, and_29_out);
  D_FF_with_EN d_ff_with_en_25 (.CLK(clkk), .D(D4), .EN(and_1_out), .Q(d_ff_with_en_25_q));  // open: reset, Q_fan
  D_FF_with_EN d_ff_with_en_26 (.CLK(clkk), .D(D4), .EN(and_2_out), .Q(d_ff_with_en_26_q));  // open: reset, Q_fan
  D_FF_with_EN d_ff_with_en_27 (.CLK(clkk), .D(D4), .EN(and_3_out), .Q(d_ff_with_en_27_q));  // open: reset, Q_fan
  D_FF_with_EN d_ff_with_en_28 (.CLK(clkk), .D(D4), .EN(and_4_out), .Q(d_ff_with_en_28_q));  // open: reset, Q_fan
  D_FF_with_EN d_ff_with_en_29 (.CLK(clkk), .D(D4), .EN(and_5_out), .Q(d_ff_with_en_29_q));  // open: reset, Q_fan
  D_FF_with_EN d_ff_with_en_30 (.CLK(clkk), .D(D4), .EN(and_6_out), .Q(d_ff_with_en_30_q));  // open: reset, Q_fan
  D_FF_with_EN d_ff_with_en_31 (.CLK(clkk), .D(D4), .EN(and_7_out), .Q(d_ff_with_en_31_q));  // open: reset, Q_fan
  D_FF_with_EN d_ff_with_en_32 (
    .CLK(clkk), .D(D4), .EN(and_8_out), .Q(d_ff_with_en_32_q), .Q_fan(d_ff_with_en_32_q_fan));  // open: reset
  and and_33 (and_33_out, and_5_out, d_ff_with_en_29_q);
  and and_34 (and_34_out, and_6_out, d_ff_with_en_30_q);
  and and_35 (and_35_out, and_7_out, d_ff_with_en_31_q);
  and and_36 (and_36_out, and_8_out, d_ff_with_en_32_q);
  and and_37 (and_37_out, three_8yimaqi_no2_4yimaqi_1_y0, d_ff_with_en_25_q);
  and and_38 (and_38_out, and_2_out, d_ff_with_en_26_q);
  and and_39 (and_39_out, and_3_out, d_ff_with_en_27_q);
  and and_40 (and_40_out, and_4_out, d_ff_with_en_28_q);
  or or_4 (Y4, and_36_out, and_35_out, and_34_out, and_33_out, and_40_out, and_39_out, and_38_out, and_37_out);
  D_FF_with_EN d_ff_with_en_33 (.CLK(clkk), .D(D3), .EN(and_1_out), .Q(d_ff_with_en_33_q));  // open: reset, Q_fan
  D_FF_with_EN d_ff_with_en_34 (.CLK(clkk), .D(D3), .EN(and_2_out), .Q(d_ff_with_en_34_q));  // open: reset, Q_fan
  D_FF_with_EN d_ff_with_en_35 (.CLK(clkk), .D(D3), .EN(and_3_out), .Q(d_ff_with_en_35_q));  // open: reset, Q_fan
  D_FF_with_EN d_ff_with_en_36 (.CLK(clkk), .D(D3), .EN(and_4_out), .Q(d_ff_with_en_36_q));  // open: reset, Q_fan
  D_FF_with_EN d_ff_with_en_37 (.CLK(clkk), .D(D3), .EN(and_5_out), .Q(d_ff_with_en_37_q));  // open: reset, Q_fan
  D_FF_with_EN d_ff_with_en_38 (.CLK(clkk), .D(D3), .EN(and_6_out), .Q(d_ff_with_en_38_q));  // open: reset, Q_fan
  D_FF_with_EN d_ff_with_en_39 (.CLK(clkk), .D(D3), .EN(and_7_out), .Q(d_ff_with_en_39_q));  // open: reset, Q_fan
  D_FF_with_EN d_ff_with_en_40 (
    .CLK(clkk), .D(D3), .EN(and_8_out), .Q(d_ff_with_en_40_q), .Q_fan(d_ff_with_en_40_q_fan));  // open: reset
  and and_41 (and_41_out, and_5_out, d_ff_with_en_37_q);
  and and_42 (and_42_out, and_6_out, d_ff_with_en_38_q);
  and and_43 (and_43_out, and_7_out, d_ff_with_en_39_q);
  and and_44 (and_44_out, and_8_out, d_ff_with_en_40_q);
  and and_45 (and_45_out, three_8yimaqi_no2_4yimaqi_1_y0, d_ff_with_en_33_q);
  and and_46 (and_46_out, and_2_out, d_ff_with_en_34_q);
  and and_47 (and_47_out, and_3_out, d_ff_with_en_35_q);
  and and_48 (and_48_out, and_4_out, d_ff_with_en_36_q);
  or or_5 (Y3, and_44_out, and_43_out, and_42_out, and_41_out, and_48_out, and_47_out, and_46_out, and_45_out);
  D_FF_with_EN d_ff_with_en_41 (.CLK(clkk), .D(D2), .EN(and_1_out), .Q(d_ff_with_en_41_q));  // open: reset, Q_fan
  D_FF_with_EN d_ff_with_en_42 (.CLK(clkk), .D(D2), .EN(and_2_out), .Q(d_ff_with_en_42_q));  // open: reset, Q_fan
  D_FF_with_EN d_ff_with_en_43 (.CLK(clkk), .D(D2), .EN(and_3_out), .Q(d_ff_with_en_43_q));  // open: reset, Q_fan
  D_FF_with_EN d_ff_with_en_44 (.CLK(clkk), .D(D2), .EN(and_4_out), .Q(d_ff_with_en_44_q));  // open: reset, Q_fan
  D_FF_with_EN d_ff_with_en_45 (.CLK(clkk), .D(D2), .EN(and_5_out), .Q(d_ff_with_en_45_q));  // open: reset, Q_fan
  D_FF_with_EN d_ff_with_en_46 (.CLK(clkk), .D(D2), .EN(and_6_out), .Q(d_ff_with_en_46_q));  // open: reset, Q_fan
  D_FF_with_EN d_ff_with_en_47 (.CLK(clkk), .D(D2), .EN(and_7_out), .Q(d_ff_with_en_47_q));  // open: reset, Q_fan
  D_FF_with_EN d_ff_with_en_48 (
    .CLK(clkk), .D(D2), .EN(and_8_out), .Q(d_ff_with_en_48_q), .Q_fan(d_ff_with_en_48_q_fan));  // open: reset
  and and_49 (and_49_out, and_4_out, d_ff_with_en_44_q);
  and and_50 (and_50_out, and_5_out, d_ff_with_en_45_q);
  and and_51 (and_51_out, and_6_out, d_ff_with_en_46_q);
  and and_52 (and_52_out, and_7_out, d_ff_with_en_47_q);
  and and_53 (and_53_out, and_8_out, d_ff_with_en_48_q);
  or or_6 (Y2, and_53_out, and_52_out, and_51_out, and_50_out, and_49_out, and_56_out, and_55_out, and_54_out);
  and and_54 (and_54_out, three_8yimaqi_no2_4yimaqi_1_y0, d_ff_with_en_41_q);
  and and_55 (and_55_out, and_2_out, d_ff_with_en_42_q);
  and and_56 (and_56_out, and_3_out, d_ff_with_en_43_q);
  D_FF_with_EN d_ff_with_en_49 (.CLK(clkk), .D(D1), .EN(and_1_out), .Q(d_ff_with_en_49_q));  // open: reset, Q_fan
  D_FF_with_EN d_ff_with_en_50 (.CLK(clkk), .D(D1), .EN(and_2_out), .Q(d_ff_with_en_50_q));  // open: reset, Q_fan
  D_FF_with_EN d_ff_with_en_51 (.CLK(clkk), .D(D1), .EN(and_3_out), .Q(d_ff_with_en_51_q));  // open: reset, Q_fan
  D_FF_with_EN d_ff_with_en_52 (.CLK(clkk), .D(D1), .EN(and_4_out), .Q(d_ff_with_en_52_q));  // open: reset, Q_fan
  D_FF_with_EN d_ff_with_en_53 (.CLK(clkk), .D(D1), .EN(and_5_out), .Q(d_ff_with_en_53_q));  // open: reset, Q_fan
  D_FF_with_EN d_ff_with_en_54 (.CLK(clkk), .D(D1), .EN(and_6_out), .Q(d_ff_with_en_54_q));  // open: reset, Q_fan
  D_FF_with_EN d_ff_with_en_55 (.CLK(clkk), .D(D1), .EN(and_7_out), .Q(d_ff_with_en_55_q));  // open: reset, Q_fan
  D_FF_with_EN d_ff_with_en_56 (
    .CLK(clkk), .D(D1), .EN(and_8_out), .Q(d_ff_with_en_56_q), .Q_fan(d_ff_with_en_56_q_fan));  // open: reset
  and and_57 (and_57_out, and_7_out, d_ff_with_en_55_q);
  and and_58 (and_58_out, and_8_out, d_ff_with_en_56_q);
  and and_59 (and_59_out, three_8yimaqi_no2_4yimaqi_1_y0, d_ff_with_en_49_q);
  and and_60 (and_60_out, and_2_out, d_ff_with_en_50_q);
  and and_61 (and_61_out, and_3_out, d_ff_with_en_51_q);
  and and_62 (and_62_out, and_4_out, d_ff_with_en_52_q);
  and and_63 (and_63_out, and_5_out, d_ff_with_en_53_q);
  and and_64 (and_64_out, and_6_out, d_ff_with_en_54_q);
  or or_7 (Y1, and_58_out, and_57_out, and_64_out, and_63_out, and_62_out, and_61_out, and_60_out, and_59_out);
  D_FF_with_EN d_ff_with_en_57 (.CLK(clkk), .D(D0), .EN(and_1_out), .Q(d_ff_with_en_57_q));  // open: reset, Q_fan
  D_FF_with_EN d_ff_with_en_58 (.CLK(clkk), .D(D0), .EN(and_2_out), .Q(d_ff_with_en_58_q));  // open: reset, Q_fan
  D_FF_with_EN d_ff_with_en_59 (.CLK(clkk), .D(D0), .EN(and_3_out), .Q(d_ff_with_en_59_q));  // open: reset, Q_fan
  D_FF_with_EN d_ff_with_en_60 (.CLK(clkk), .D(D0), .EN(and_4_out), .Q(d_ff_with_en_60_q));  // open: reset, Q_fan
  D_FF_with_EN d_ff_with_en_61 (.CLK(clkk), .D(D0), .EN(and_5_out), .Q(d_ff_with_en_61_q));  // open: reset, Q_fan
  D_FF_with_EN d_ff_with_en_62 (.CLK(clkk), .D(D0), .EN(and_6_out), .Q(d_ff_with_en_62_q));  // open: reset, Q_fan
  D_FF_with_EN d_ff_with_en_63 (.CLK(clkk), .D(D0), .EN(and_7_out), .Q(d_ff_with_en_63_q));  // open: reset, Q_fan
  D_FF_with_EN d_ff_with_en_64 (
    .CLK(clkk), .D(D0), .EN(and_8_out), .Q(d_ff_with_en_64_q), .Q_fan(d_ff_with_en_64_q_fan));  // open: reset
  and and_65 (and_65_out, and_7_out, d_ff_with_en_63_q);
  and and_66 (and_66_out, and_8_out, d_ff_with_en_64_q);
  and and_67 (and_67_out, three_8yimaqi_no2_4yimaqi_1_y0, d_ff_with_en_57_q);
  and and_68 (and_68_out, and_2_out, d_ff_with_en_58_q);
  and and_69 (and_69_out, and_3_out, d_ff_with_en_59_q);
  and and_70 (and_70_out, and_4_out, d_ff_with_en_60_q);
  and and_71 (and_71_out, and_5_out, d_ff_with_en_61_q);
  and and_72 (and_72_out, and_6_out, d_ff_with_en_62_q);
  or or_8 (Y0, and_66_out, and_65_out, and_72_out, and_71_out, and_70_out, and_69_out, and_68_out, and_67_out);

  // Notes on the sheet:
  //   指令存储顺序为从下往上
endmodule

module sCPU_only_li (
);

  wire and_1_out, and_2_out, and_3_out, and_4_out, CLK, decoder_1_out0, decoder_1_out2, decoder_2_out0,
       decoder_2_out1, decoder_2_out2, decoder_2_out3;
  wire [1:0] opcode, rd;
  wire [3:0] data, g0, g1, g2, g3, PCOUT, register_1_q;

  ROM #(.addrWidth(4)) rom_1 (.addr(PCOUT), .data({opcode, rd, data}));
  Clock clock_1 (.out(CLK));
  Register #(.width(4)) register_1 (.D(PCOUT), .en(1'b1), .clk(CLK), .Q(register_1_q));  // open: clr
  Decoder #(.select(2)) decoder_1 (
    .out0(decoder_1_out0), .out2(decoder_1_out2), .sel(opcode), .en(1'b1));  // open: out1, out3
  Decoder #(.select(2)) decoder_2 (
    .out0(decoder_2_out0), .out1(decoder_2_out1), .out2(decoder_2_out2), .out3(decoder_2_out3), .sel(rd),
    .en(1'b1));
  and and_1 (and_1_out, decoder_2_out0, decoder_1_out2);
  and and_2 (and_2_out, decoder_2_out1, decoder_1_out2);
  and and_3 (and_3_out, decoder_2_out2, decoder_1_out2);
  and and_4 (and_4_out, decoder_2_out3, decoder_1_out2);
  Adder #(.width(4)) adder_1 (.a(register_1_q), .b(4'b0001), .out(PCOUT));  // open: cin, cout
  Register #(.width(4)) R0 (.D(data), .en(and_1_out), .clk(CLK), .Q(g0));  // open: clr
  Register #(.width(4)) r1 (.D(data), .en(and_2_out), .clk(CLK), .Q(g1));  // open: clr
  Register #(.width(4)) r2 (.D(data), .en(and_3_out), .clk(CLK), .Q(g2));  // open: clr
  Register #(.width(4)) r3 (.D(data), .en(and_4_out), .clk(CLK), .Q(g3));  // open: clr

  // Other names for the same wires on the sheet: rs2[1:0] = data[1:0]; rs1[1:0] = data[3:2]

  // Notes on the sheet:
  //   contents of rom_1 (hex, n*v repeats v):
  //   8a 90 a0 b1
  //   仅仅支持li指令的sCPU，故只有四条指令
  //   译码器用于识别指令类型，10为li，00为add
  //   PC寄存器
  //   将写入数据拼凑成4位
  //   GPR
endmodule

module sCPU_li_and_add (
);

  wire and_1_out, and_2_out, and_3_out, and_4_out, CLK, decoder_1_out0, decoder_1_out2, decoder_2_out0,
       decoder_2_out1, decoder_2_out2, decoder_2_out3, or_1_out;
  wire [1:0] opcode, rd;
  wire [3:0] adder_output, data, g0, g1, g2, g3, multiplexer_1_out, multiplexer_2_out, multiplexer_3_out,
       multiplexer_4_out, PCOUT, register_1_q, rs1_result, rs2_result;

  ROM #(.addrWidth(4)) rom_1 (.addr(PCOUT), .data({opcode, rd, data}));
  Clock clock_1 (.out(CLK));
  Decoder #(.select(2)) decoder_1 (
    .out0(decoder_1_out0), .out2(decoder_1_out2), .sel(opcode), .en(1'b1));  // open: out1, out3
  Register #(.width(4)) register_1 (.D(PCOUT), .en(1'b1), .clk(CLK), .Q(register_1_q));  // open: clr
  Decoder #(.select(2)) decoder_2 (
    .out0(decoder_2_out0), .out1(decoder_2_out1), .out2(decoder_2_out2), .out3(decoder_2_out3), .sel(rd),
    .en(1'b1));
  or or_1 (or_1_out, decoder_1_out0, decoder_1_out2);
  and and_1 (and_1_out, decoder_2_out0, or_1_out);
  and and_2 (and_2_out, decoder_2_out1, or_1_out);
  and and_3 (and_3_out, decoder_2_out2, or_1_out);
  and and_4 (and_4_out, decoder_2_out3, or_1_out);
  Adder #(.width(4)) adder_1 (.a(register_1_q), .b(4'b0001), .out(PCOUT));  // open: cin, cout
  Multiplexer #(.select(2), .width(4)) multiplexer_1 (
    .in0(adder_output), .in2(data), .out(multiplexer_1_out), .sel(opcode));  // open: in1, in3
  Multiplexer #(.select(2), .width(4)) multiplexer_2 (
    .in0(adder_output), .in2(data), .out(multiplexer_2_out), .sel(opcode));  // open: in1, in3
  Multiplexer #(.select(2), .width(4)) multiplexer_3 (
    .in0(adder_output), .in2(data), .out(multiplexer_3_out), .sel(opcode));  // open: in1, in3
  Multiplexer #(.select(2), .width(4)) multiplexer_4 (
    .in0(adder_output), .in2(data), .out(multiplexer_4_out), .sel(opcode));  // open: in1, in3
  Register #(.width(4)) R0 (.D(multiplexer_1_out), .en(and_1_out), .clk(CLK), .Q(g0));  // open: clr
  Register #(.width(4)) r1 (.D(multiplexer_2_out), .en(and_2_out), .clk(CLK), .Q(g1));  // open: clr
  Register #(.width(4)) r2 (.D(multiplexer_3_out), .en(and_3_out), .clk(CLK), .Q(g2));  // open: clr
  Register #(.width(4)) r3 (.D(multiplexer_4_out), .en(and_4_out), .clk(CLK), .Q(g3));  // open: clr
  Multiplexer #(.select(2), .width(4)) multiplexer_5 (
    .in0(g0), .in1(g1), .in2(g2), .in3(g3), .out(rs1_result), .sel(data[3:2]));
  Multiplexer #(.select(2), .width(4)) multiplexer_6 (
    .in0(g0), .in1(g1), .in2(g2), .in3(g3), .out(rs2_result), .sel(data[1:0]));
  Adder #(.width(4)) adder_2 (.a(rs1_result), .b(rs2_result), .out(adder_output), .cin(1'b0));  // open: cout

  // Other names for the same wires on the sheet: rs2[1:0] = data[1:0]; rs1[1:0] = data[3:2]

  // Notes on the sheet:
  //   contents of rom_1 (hex, n*v repeats v):
  //   8a 90 a0 b1 17 29
  //   GPR部分数据位宽应该全部改为8位，但是主播太懒了就懒得搞了
  //   add和li需要写使能
  //   PC寄存器
  //   译码器用于识别指令类型，10为li，00为add
  //   将写入数据拼凑成4位
  //   GPR
  //   先进行rs1，rs2的选择
endmodule

module sCPU_final (
  input  [1:0] in_1,
  input  [1:0] in_2,
  input  [1:0] in_3
);

  wire and_1_out, and_2_out, and_3_out, and_4_out, bner0, bner0need, CLK, comparator_1_eq, decoder_1_out0,
       decoder_1_out2, decoder_2_out0, decoder_2_out1, decoder_2_out2, decoder_2_out3, not_1_out, or_1_out,
       outchengli;
  wire [1:0] data, opcode, rs1_afterchoose;
  wire [3:0] adder_1_out, bner0tiaozhuandizhi, PCIN, PCOUT;
  wire [7:0] adder_output, DATA_FINAL, g0, g1, g2, g3, rs1_result, rs2_result;

  Clock clock_1 (.out(CLK));
  ROM #(.addrWidth(4)) rom_1 (.addr(PCOUT), .data({opcode, bner0tiaozhuandizhi, data}));
  Adder #(.width(4)) adder_1 (.a(PCOUT), .b(4'b0001), .out(adder_1_out), .cin(1'b0));  // open: cout
  Multiplexer #(.width(4)) multiplexer_1 (.in0(adder_1_out), .in1(bner0tiaozhuandizhi), .out(PCIN), .sel(bner0need));
  Decoder #(.select(2)) decoder_1 (
    .out0(decoder_1_out0), .out1(outchengli), .out2(decoder_1_out2), .out3(bner0), .sel(opcode), .en(1'b1));
  Register #(.width(4)) register_1 (.D(PCIN), .en(1'b1), .clk(CLK), .Q(PCOUT));  // open: clr
  Hex_Digit_Display hex_digit_display_1 (.value(g2[7:4]));  // open: dp
  Decoder #(.select(2)) decoder_2 (
    .out0(decoder_2_out0), .out1(decoder_2_out1), .out2(decoder_2_out2), .out3(decoder_2_out3),
    .sel(bner0tiaozhuandizhi[3:2]), .en(1'b1));
  or or_1 (or_1_out, decoder_1_out0, decoder_1_out2);
  Hex_Digit_Display hex_digit_display_2 (.value(g2[3:0]));  // open: dp
  Hex_Digit_Display hex_digit_display_3 (.value(rs2_result[7:4]));  // open: dp
  Hex_Digit_Display hex_digit_display_4 (.value(rs2_result[3:0]));  // open: dp
  and and_1 (and_1_out, decoder_2_out0, or_1_out);
  and and_2 (and_2_out, decoder_2_out1, or_1_out);
  and and_3 (and_3_out, decoder_2_out2, or_1_out);
  and and_4 (and_4_out, decoder_2_out3, or_1_out);
  Multiplexer #(.select(2), .width(8)) multiplexer_2 (
    .in0(adder_output), .in2({in_1, in_2, bner0tiaozhuandizhi[1:0], data}), .out(DATA_FINAL), .sel(opcode));  // open: in1, in3
  Register R0 (.D(DATA_FINAL), .en(and_1_out), .clk(CLK), .Q(g0));  // open: clr
  Register r1 (.D(DATA_FINAL), .en(and_2_out), .clk(CLK), .Q(g1));  // open: clr
  Register r2 (.D(DATA_FINAL), .en(and_3_out), .clk(CLK), .Q(g2));  // open: clr
  Register r3 (.D(DATA_FINAL), .en(and_4_out), .clk(CLK), .Q(g3));  // open: clr
  Multiplexer #(.select(2), .width(8)) multiplexer_3 (
    .in0(g0), .in1(g1), .in2(g2), .in3(g3), .out(rs1_result), .sel(rs1_afterchoose));
  Multiplexer #(.width(2)) multiplexer_4 (
    .in0(bner0tiaozhuandizhi[1:0]), .in1(in_3), .out(rs1_afterchoose), .sel(bner0));
  Multiplexer #(.select(2), .width(8)) multiplexer_5 (
    .in0(g0), .in1(g1), .in2(g2), .in3(g3), .out(rs2_result), .sel(data));
  Adder adder_2 (.a(rs1_result), .b(rs2_result), .out(adder_output), .cin(1'b0));  // open: cout
  Comparator #(.mode("unsigned")) comparator_1 (.a(rs1_result), .b(rs2_result), .eq(comparator_1_eq));  // open: gt, lt
  not not_1 (not_1_out, comparator_1_eq);
  and and_5 (bner0need, not_1_out, bner0);

  // Other names for the same wires on the sheet: data[7:2] = {in_1, in_2, bner0tiaozhuandizhi[1:0]};
  //   rs1[1:0] = bner0tiaozhuandizhi[1:0]; rd[1:0] = bner0tiaozhuandizhi[3:2]; rs2[1:0] = data

  // Notes on the sheet:
  //   contents of rom_1 (hex, n*v repeats v):
  //   8a 90 a0 b1 17 29 d1 df
  //   译码器用于识别指令类型，10为li，00为add
  //   add和li需要写使能
  //   PC寄存器
  //   out指令成立时，输出rs的内容，我自定义的编码格式是opcode：01，中间四位舍弃（无意义），最后两位为rs
  //   将写入数据拼凑成8位
  //   将写入数据拼凑成4位
  //   先进行rs1，rs2的选择
  //   若bner0信号来了，则固定选择地址为00的r0寄存器
  //   加法运算
  //   bner0指令下，比较r0与其它GPR部分，值不同则返回
endmodule

module minirv_addi_jalr (
);

  wire addichengli, and_4_out, CLK, funct3is000, jalrchengli, multiplexer_2_out, not_1_out, not_2_out,
       not_3_out, not_4_out, not_5_out, not_6_out, not_7_out, not_8_out, not_9_out, not_10_out, rd_is_x0;
  wire [2:0] funct3;
  wire [3:0] GPR0_3, GPR4_7, GPR8_11, GPR12_15;
  wire [4:0] rd, rs1;
  wire [6:0] opcode;
  wire [11:0] imm;
  wire [23:0] bit_extender_1_out, bit_extender_2_out, jalr_output, multiplexer_1_out, pc_plus4, pcout,
       pcout_chuyi4;
  wire [31:0] adder_output, bit_extender_3_out, bit_extender_4_out, data_write, rd_read_result,
       rs1_read_result, x0, x1, x2, x3, x4, x5, x6, x7, x8, x9, x10, x11, x12, x13, x14, x15;

  Divider #(.width(24)) divider_1 (.a(pcout), .b(24'h4), .out(pcout_chuyi4));  // open: upper, rem
  Adder #(.width(24)) adder_1 (.a(pcout), .b(24'h4), .out(pc_plus4));  // open: cin, cout
  ROM #(.addrWidth(24), .dataWidth(32)) rom_1 (.addr(pcout_chuyi4), .data({imm, rs1, funct3, rd, opcode}));
  Multiplexer #(.width(24)) multiplexer_1 (
    .in0(pc_plus4), .in1(jalr_output), .out(multiplexer_1_out), .sel(jalrchengli));
  Register #(.width(24)) register_1 (.D(multiplexer_1_out), .en(1'b1), .clk(CLK), .Q(pcout));  // open: clr
  Bit_Extender #(.in_width(32), .out_width(24), .\type ("zero")) bit_extender_1 (
    .in(rs1_read_result), .out(bit_extender_1_out));
  assign bit_extender_2_out = {{12{imm[11]}}, imm};  // Bit_Extender bit_extender_2
  Comparator #(.width(5)) comparator_1 (.a(rd), .b({5{1'b0}}), .eq(rd_is_x0));  // open: gt, lt
  not not_1 (not_1_out, funct3[0]);
  not not_2 (not_2_out, funct3[1]);
  not not_3 (not_3_out, funct3[2]);
  not not_4 (not_4_out, opcode[2]);
  not not_5 (not_5_out, opcode[3]);
  not not_6 (not_6_out, opcode[5]);
  not not_7 (not_7_out, opcode[6]);
  not not_8 (not_8_out, opcode[3]);
  not not_9 (not_9_out, opcode[4]);
  and and_1 (funct3is000, not_1_out, not_2_out, not_3_out);
  and and_2 (addichengli, opcode[0], opcode[1], not_4_out, not_5_out, opcode[4], not_6_out, not_7_out, funct3is000);
  and and_3 (jalrchengli, opcode[0], opcode[1], opcode[2], not_8_out, not_9_out, opcode[5], opcode[6], funct3is000);
  Adder #(.width(24)) adder_2 (.a(bit_extender_1_out), .b(bit_extender_2_out), .out(jalr_output));  // open: cin, cout
  assign bit_extender_3_out = {{20{1'b0}}, imm};  // Bit_Extender bit_extender_3
  Adder #(.width(32)) adder_3 (.a(rs1_read_result), .b(bit_extender_3_out), .out(adder_output));  // open: cin, cout
  and and_4 (and_4_out, jalrchengli, not_10_out);
  not not_10 (not_10_out, rd_is_x0);
  assign bit_extender_4_out = {{8{1'b0}}, pc_plus4};  // Bit_Extender bit_extender_4
  Multiplexer multiplexer_2 (.in0(addichengli), .in1(and_4_out), .out(multiplexer_2_out), .sel(jalrchengli));
  Decoder #(.enable("false"), .select(5)) decoder_1 (
    .out0(GPR0_3[0]), .out1(GPR0_3[1]), .out2(GPR0_3[2]), .out3(GPR0_3[3]), .out4(GPR4_7[0]),
    .out5(GPR4_7[1]), .out6(GPR4_7[2]), .out7(GPR4_7[3]), .out8(GPR8_11[0]), .out9(GPR8_11[1]),
    .out10(GPR8_11[2]), .out11(GPR8_11[3]), .out12(GPR12_15[0]), .out13(GPR12_15[1]), .out14(GPR12_15[2]),
    .out15(GPR12_15[3]), .sel(rd));  // open: out16, out17, out18, out19, out20, out21, out22, out23, out24, out25, out26, out27, out28, out29, out30, out31
  Multiplexer #(.select(2), .width(32)) multiplexer_3 (
    .in1(adder_output), .in2(bit_extender_4_out), .out(data_write), .sel({jalrchengli, addichengli}));  // open: in0, in3
  Register #(.width(32)) u_x0 (.D(data_write), .en(1'b0), .clk(CLK), .Q(x0));  // open: clr
  Register #(.width(32)) u_x4 (.D(data_write), .en(GPR4_7[0]), .clk(CLK), .Q(x4));  // open: clr
  Register #(.width(32)) u_x8 (.D(data_write), .en(GPR8_11[0]), .clk(CLK), .Q(x8));  // open: clr
  Register #(.width(32)) u_x12 (.D(data_write), .en(GPR12_15[0]), .clk(CLK), .Q(x12));  // open: clr
  Register #(.width(32)) u_x1 (.D(data_write), .en(GPR0_3[1]), .clk(CLK), .Q(x1));  // open: clr
  Register #(.width(32)) u_x5 (.D(data_write), .en(GPR4_7[1]), .clk(CLK), .Q(x5));  // open: clr
  Register #(.width(32)) u_x9 (.D(data_write), .en(GPR8_11[1]), .clk(CLK), .Q(x9));  // open: clr
  Register #(.width(32)) u_x13 (.D(data_write), .en(GPR12_15[1]), .clk(CLK), .Q(x13));  // open: clr
  Register #(.width(32)) u_x2 (.D(data_write), .en(GPR0_3[2]), .clk(CLK), .Q(x2));  // open: clr
  Register #(.width(32)) u_x6 (.D(data_write), .en(GPR4_7[2]), .clk(CLK), .Q(x6));  // open: clr
  Register #(.width(32)) u_x10 (.D(data_write), .en(GPR8_11[2]), .clk(CLK), .Q(x10));  // open: clr
  Register #(.width(32)) u_x14 (.D(data_write), .en(GPR12_15[2]), .clk(CLK), .Q(x14));  // open: clr
  Register #(.width(32)) u_x3 (.D(data_write), .en(GPR0_3[3]), .clk(CLK), .Q(x3));  // open: clr
  Register #(.width(32)) u_x7 (.D(data_write), .en(GPR4_7[3]), .clk(CLK), .Q(x7));  // open: clr
  Register #(.width(32)) u_x11 (.D(data_write), .en(GPR8_11[3]), .clk(CLK), .Q(x11));  // open: clr
  Register #(.width(32)) u_x15 (.D(data_write), .en(GPR12_15[3]), .clk(CLK), .Q(x15));  // open: clr
  Clock clock_1 (.out(CLK));
  Multiplexer #(.select(5), .width(32)) multiplexer_4 (
    .in0(x0), .in1(x1), .in2(x2), .in3(x3), .in4(x4), .in5(x5), .in6(x6), .in7(x7), .in8(x8), .in9(x9),
    .in10(x10), .in11(x11), .in12(x12), .in13(x13), .in14(x14), .in15(x15), .out(rs1_read_result), .sel(rs1));  // open: in16, in17, in18, in19, in20, in21, in22, in23, in24, in25, in26, in27, in28, in29, in30, in31
  Multiplexer #(.select(5), .width(32)) multiplexer_5 (
    .in0(x0), .in1(x1), .in2(x2), .in3(x3), .in4(x4), .in5(x5), .in6(x6), .in7(x7), .in8(x8), .in9(x9),
    .in10(x10), .in11(x11), .in12(x12), .in13(x13), .in14(x14), .in15(x15), .out(rd_read_result), .sel(rd));  // open: in16, in17, in18, in19, in20, in21, in22, in23, in24, in25, in26, in27, in28, in29, in30, in31

  // Other names for the same wires on the sheet: zhuangtai[1:0] = {jalrchengli, addichengli}

  // Notes on the sheet:
  //   contents of rom_1 (hex, n*v repeats v):
  //   1400513 10000e7 c000e7 c00067 a50513 8067
  //   PC寄存器
  //   判断rd是否为x0
  //   是否为addi指令判断：is_addi = (inst[6:0] == 0010011) && (inst[14:12] == 000)
  //   此条件下addi指令成立并执行
  //   此条件下jalr指令成立并执行
  //   计算jalr指令要跳转的指令地址
  //   addi执行过程，Imm被拓展到32位进行加
  //   rd为x0时，禁止写入，x0恒为0
  //   GPR
  //   GPR
  //   GPR
  //   GPR
endmodule

module minirv_addijalraddlui (
);

  wire addchengli, addichengli, and_7_out, CLK, funct3is000, funct7is000, jalrchengli, luichengli,
       multiplexer_3_out, not_1_out, not_2_out, not_3_out, not_4_out, not_5_out, not_6_out, not_7_out,
       not_8_out, not_9_out, not_10_out, not_11_out, not_12_out, not_13_out, not_14_out, not_15_out,
       not_16_out, not_17_out, not_18_out, not_19_out, not_20_out, not_21_out, rd_is_x0;
  wire [2:0] funct3, zhuangtai;
  wire [3:0] GPR0_3, GPR4_7, GPR8_11, GPR12_15;
  wire [4:0] rd;
  wire [6:0] opcode;
  wire [19:15] lui_imm;
  wire [23:0] bit_extender_1_out, bit_extender_2_out, jalr_output, multiplexer_1_out, pc_plus4, pcout,
       pcout_chuyi4;
  wire [31:0] adder_output, addiimm_for_fushuyunsuan, addzhilin_output, bit_extender_3_out, data_write,
       rd_read_result, rs1_read_result, rs2_read_result, x0, x1, x2, x3, x4, x5, x6, x7, x8, x9, x10, x11,
       x12, x13, x14, x15;

  Divider #(.width(24)) divider_1 (.a(pcout), .b(24'h4), .out(pcout_chuyi4));  // open: upper, rem
  Adder #(.width(24)) adder_1 (.a(pcout), .b(24'h4), .out(pc_plus4));  // open: cin, cout
  ROM #(.addrWidth(24), .dataWidth(32)) rom_1 (
    .addr(pcout_chuyi4), .data({addiimm_for_fushuyunsuan[11:0], lui_imm, funct3, rd, opcode}));
  Multiplexer #(.width(24)) multiplexer_1 (
    .in0(pc_plus4), .in1(jalr_output), .out(multiplexer_1_out), .sel(jalrchengli));
  Register #(.width(24)) register_1 (.D(multiplexer_1_out), .en(1'b1), .clk(CLK), .Q(pcout));  // open: clr
  Bit_Extender #(.in_width(32), .out_width(24), .\type ("zero")) bit_extender_1 (
    .in(rs1_read_result), .out(bit_extender_1_out));
  assign bit_extender_2_out = {{12{addiimm_for_fushuyunsuan[11]}}, addiimm_for_fushuyunsuan[11:0]};  // Bit_Extender bit_extender_2
  Comparator #(.width(5)) comparator_1 (.a(rd), .b({5{1'b0}}), .eq(rd_is_x0));  // open: gt, lt
  not not_1 (not_1_out, addiimm_for_fushuyunsuan[6]);
  not not_2 (not_2_out, addiimm_for_fushuyunsuan[7]);
  not not_3 (not_3_out, addiimm_for_fushuyunsuan[8]);
  not not_4 (not_4_out, addiimm_for_fushuyunsuan[9]);
  not not_5 (not_5_out, addiimm_for_fushuyunsuan[10]);
  not not_6 (not_6_out, addiimm_for_fushuyunsuan[11]);
  not not_7 (not_7_out, opcode[3]);
  not not_8 (not_8_out, opcode[6]);
  not not_9 (not_9_out, funct3[0]);
  not not_10 (not_10_out, funct3[1]);
  not not_11 (not_11_out, funct3[2]);
  not not_12 (not_12_out, opcode[2]);
  not not_13 (not_13_out, opcode[3]);
  not not_14 (not_14_out, opcode[5]);
  not not_15 (not_15_out, opcode[6]);
  not not_16 (not_16_out, opcode[3]);
  not not_17 (not_17_out, opcode[4]);
  and and_1 (funct7is000, not_1_out, not_2_out, not_3_out, not_4_out, not_5_out, not_6_out);
  not not_18 (not_18_out, opcode[2]);
  not not_19 (not_19_out, opcode[3]);
  not not_20 (not_20_out, opcode[6]);
  and and_2 (luichengli, opcode[0], opcode[1], opcode[2], not_7_out, opcode[4], opcode[5], not_8_out);
  and and_3 (funct3is000, not_9_out, not_10_out, not_11_out);
  and and_4 (addichengli, opcode[0], opcode[1], not_12_out, not_13_out, opcode[4], not_14_out, not_15_out, funct3is000);
  Multiplexer #(.width(20)) multiplexer_2 (
    .in0({20{1'b0}}), .in1({20{1'b1}}), .out(addiimm_for_fushuyunsuan[31:12]),
    .sel(addiimm_for_fushuyunsuan[11]));
  and and_5 (jalrchengli, opcode[0], opcode[1], opcode[2], not_16_out, not_17_out, opcode[5], opcode[6], funct3is000);
  Adder #(.width(24)) adder_2 (.a(bit_extender_1_out), .b(bit_extender_2_out), .out(jalr_output));  // open: cin, cout
  and and_6 (addchengli, opcode[1], not_18_out, not_19_out, opcode[4], opcode[0], opcode[5], not_20_out, funct3is000, funct7is000);
  Adder #(.width(32)) adder_3 (.a(rs1_read_result), .b(rs2_read_result), .out(addzhilin_output));  // open: cin, cout
  // Probe on addzhilin_output
  not not_21 (not_21_out, rd_is_x0);
  ROM #(.addrWidth(24), .dataWidth(32)) rom_2 ();  // open: addr, data
  and and_7 (and_7_out, jalrchengli, not_21_out);
  Adder #(.width(32)) adder_4 (
    .a(rs1_read_result), .b(addiimm_for_fushuyunsuan), .out(adder_output));  // open: cin, cout
  Multiplexer multiplexer_3 (.in0(addichengli), .in1(and_7_out), .out(multiplexer_3_out), .sel(jalrchengli));
  Decoder #(.enable("false"), .select(5)) decoder_1 (
    .out0(GPR0_3[0]), .out1(GPR0_3[1]), .out2(GPR0_3[2]), .out3(GPR0_3[3]), .out4(GPR4_7[0]),
    .out5(GPR4_7[1]), .out6(GPR4_7[2]), .out7(GPR4_7[3]), .out8(GPR8_11[0]), .out9(GPR8_11[1]),
    .out10(GPR8_11[2]), .out11(GPR8_11[3]), .out12(GPR12_15[0]), .out13(GPR12_15[1]), .out14(GPR12_15[2]),
    .out15(GPR12_15[3]), .sel(rd));  // open: out16, out17, out18, out19, out20, out21, out22, out23, out24, out25, out26, out27, out28, out29, out30, out31
  assign bit_extender_3_out = {{8{1'b0}}, pc_plus4};  // Bit_Extender bit_extender_3
  RAM #(.addrWidth(20), .asyncread("true"), .byteenables("byteEnables"), .dataWidth(32), .\type ("nonvolatile")) ram_1 ();  // open: addr, we, oe, clk, din, dout, be3, be2, be1, be0
  bianmaqi_zidianlu bianmaqi_zidianlu_1 (
    .I3(luichengli), .I2(addchengli), .I1(jalrchengli), .I0(addichengli), .Y2(zhuangtai[2]),
    .Y1(zhuangtai[1]), .Y0(zhuangtai[0]));  // open: I15, I14, I13, I12, I11, I10, I9, I8, I7, I6, I5, I4, Y3
  Multiplexer #(.select(3), .width(32)) multiplexer_4 (
    .in0(adder_output), .in1(bit_extender_3_out), .in2(addzhilin_output),
    .in3({addiimm_for_fushuyunsuan[11:0], lui_imm, funct3, {12{1'b0}}}), .out(data_write), .sel(zhuangtai));  // open: in4, in5, in6, in7
  Register #(.width(32)) u_x0 (.D({32{1'b0}}), .en(1'b0), .clk(CLK), .Q(x0));  // open: clr
  Register #(.width(32)) u_x4 (.D(data_write), .en(GPR4_7[0]), .clk(CLK), .Q(x4));  // open: clr
  Register #(.width(32)) u_x8 (.D(data_write), .en(GPR8_11[0]), .clk(CLK), .Q(x8));  // open: clr
  Register #(.width(32)) u_x12 (.D(data_write), .en(GPR12_15[0]), .clk(CLK), .Q(x12));  // open: clr
  Register #(.width(32)) u_x1 (.D(data_write), .en(GPR0_3[1]), .clk(CLK), .Q(x1));  // open: clr
  Register #(.width(32)) u_x5 (.D(data_write), .en(GPR4_7[1]), .clk(CLK), .Q(x5));  // open: clr
  Register #(.width(32)) u_x9 (.D(data_write), .en(GPR8_11[1]), .clk(CLK), .Q(x9));  // open: clr
  Register #(.width(32)) u_x13 (.D(data_write), .en(GPR12_15[1]), .clk(CLK), .Q(x13));  // open: clr
  Register #(.width(32)) u_x2 (.D(data_write), .en(GPR0_3[2]), .clk(CLK), .Q(x2));  // open: clr
  Register #(.width(32)) u_x6 (.D(data_write), .en(GPR4_7[2]), .clk(CLK), .Q(x6));  // open: clr
  Register #(.width(32)) u_x10 (.D(data_write), .en(GPR8_11[2]), .clk(CLK), .Q(x10));  // open: clr
  Register #(.width(32)) u_x14 (.D(data_write), .en(GPR12_15[2]), .clk(CLK), .Q(x14));  // open: clr
  Register #(.width(32)) u_x3 (.D(data_write), .en(GPR0_3[3]), .clk(CLK), .Q(x3));  // open: clr
  Register #(.width(32)) u_x7 (.D(data_write), .en(GPR4_7[3]), .clk(CLK), .Q(x7));  // open: clr
  Register #(.width(32)) u_x11 (.D(data_write), .en(GPR8_11[3]), .clk(CLK), .Q(x11));  // open: clr
  Register #(.width(32)) u_x15 (.D(data_write), .en(GPR12_15[3]), .clk(CLK), .Q(x15));  // open: clr
  Clock clock_1 (.out(CLK));
  Multiplexer #(.select(5), .width(32)) multiplexer_5 (
    .in0(x0), .in1(x1), .in2(x2), .in3(x3), .in4(x4), .in5(x5), .in6(x6), .in7(x7), .in8(x8), .in9(x9),
    .in10(x10), .in11(x11), .in12(x12), .in13(x13), .in14(x14), .in15(x15), .out(rs1_read_result),
    .sel(lui_imm));  // open: in16, in17, in18, in19, in20, in21, in22, in23, in24, in25, in26, in27, in28, in29, in30, in31
  Multiplexer #(.select(5), .width(32)) multiplexer_6 (
    .in0(x0), .in1(x1), .in2(x2), .in3(x3), .in4(x4), .in5(x5), .in6(x6), .in7(x7), .in8(x8), .in9(x9),
    .in10(x10), .in11(x11), .in12(x12), .in13(x13), .in14(x14), .in15(x15), .out(rd_read_result), .sel(rd));  // open: in16, in17, in18, in19, in20, in21, in22, in23, in24, in25, in26, in27, in28, in29, in30, in31
  Multiplexer #(.select(6), .width(32)) multiplexer_7 (
    .in0(x0), .in1(x1), .in2(x2), .in3(x3), .in4(x4), .in5(x5), .in6(x6), .in7(x7), .in8(x8), .in9(x9),
    .in10(x10), .in11(x11), .in12(x12), .in13(x13), .in14(x14), .in15(x15), .out(rs2_read_result),
    .sel(addiimm_for_fushuyunsuan[5:0]));  // open: in16, in17, in18, in19, in20, in21, in22, in23, in24, in25, in26, in27, in28, in29, in30, in31, in32, in33, in34, in35, in36, in37, in38, in39, in40, in41, in42, in43, in44, in45, in46, in47, in48, in49, in50, in51, in52, in53, in54, in55, in56, in57, in58, in59, in60, in61, in62, in63

  // Other names for the same wires on the sheet: imm[11:0] = addiimm_for_fushuyunsuan[11:0];
  //   lui_imm (some bits) = {addiimm_for_fushuyunsuan[11:0], funct3};
  //   lui_imm_20[19:0] = {addiimm_for_fushuyunsuan[11:0], lui_imm, funct3}; rs2[5:0] = addiimm_for_fushuyunsuan[5:0];
  //   funct7[5:0] = addiimm_for_fushuyunsuan[11:6]; rs1[4:0] = lui_imm

  // Notes on the sheet:
  //   PC寄存器
  //   先把imm拆成add指令格式所需
  //   判断rd是否为x0
  //   拼凑lui_imm的格式
  //   是否为addi指令判断：is_addi = (inst[6:0] == 0010011) && (inst[14:12] == 000)
  //   此条件下addi指令成立并执行
  //   负数扩展
  //   此条件下jalr指令成立并执行
  //   计算jalr指令要跳转的指令地址
  //   此条件下add指令成立并执行
  //   add执行过程
  //   此条件下lui指令成立并执行
  //   根据立即数的最高位来决定最高位补0还是1
  //   目前暂定让x0的WE接地保证始终为0
  //   rd为x0时，禁止写入，x0恒为0
  //   addi执行过程，Imm被拓展到32位进行加
  //   contents of rom_2 (hex, n*v repeats v):
  //   fe010113 123437 45640413 abcd2b7 23428293 542023 42303 ef00393 740223 444303 10000513 20000593
  //   b50633 10000e7 10060693 8067 67
  //   GPR写入逻辑
  //   目前暂定让x0的WE接地保证始终为0
  //   GPR
  //   GPR
  //   GPR
  //   GPR
endmodule

module MINIRV_Final (
);

  wire addchengli, addichengli, and_12_out, BE0, BE1, BE2, BE3, button_1_out, CLK, comparator_1_gt,
       comparator_2_lt, decoder_1_out0, decoder_1_out1, decoder_1_out2, decoder_1_out3, funct3is000,
       funct7is000, ismem, isvga, jalrchengli, lbuchengli, luichengli, lwchengli, not_1_out, not_2_out,
       not_3_out, not_4_out, not_5_out, not_6_out, not_7_out, not_8_out, not_9_out, not_10_out, not_11_out,
       not_12_out, not_13_out, not_14_out, not_15_out, not_16_out, not_17_out, not_18_out, not_19_out,
       not_20_out, not_21_out, not_22_out, not_23_out, not_24_out, not_25_out, not_26_out, not_27_out,
       not_28_out, not_29_out, not_30_out, not_31_out, not_32_out, not_33_out, not_34_out, not_35_out,
       not_36_out, not_37_out, not_38_out, not_39_out, not_40_out, not_41_out, not_42_out, not_43_out,
       not_44_out, not_45_out, not_46_out, not_47_out, not_48_out, or_1_out, or_2_out, sbchengli, swchengli;
  wire [0:0] adder_7_out;
  wire [1:0] four_2youxianbianmaqi_1_y0, four_2youxianbianmaqi_2_y0, sb_choose;
  wire [2:0] funct3, zhuangtai;
  wire [3:0] GPR0_3, GPR4_7, GPR8_11, GPR12_15;
  wire [4:0] imm, imm4_0;
  wire [6:0] funct7, opcode;
  wire [7:0] lbu_after_boarden;
  wire [19:15] lui_imm;
  wire [23:0] bit_extender_5_out, bit_extender_6_out, multiplexer_1_out, pc_plus4, pcout, pcout_chuyi4;
  wire [23:1] jalr_output;
  wire [31:0] adder_output, addzhilin_output, bit_extender_1_out, bit_extender_2_out, bit_extender_3_out,
       bit_extender_4_out, bit_extender_8_out, data_write, imm_foraddi, lbu_youxiaodizhi, lw_youxiaodizhi,
       multiplexer_3_out, multiplexer_4_out, RAM_read_result, rd_read_result, rs1_read_result,
       rs2_read_result, sw_youxiaodizhi, x0, x2, x4, x6, x8, x10, x12, x14;
  wire [31:2] sb_youxiaodizhi;
  wire [63:32] x0_1, x2_3, x4_5, x6_7, x8_9, x10_11, x12_13, x14_15;

  Adder #(.width(24)) adder_1 (.a(pcout), .b(24'h4), .out(pc_plus4));  // open: cin, cout
  Divider #(.width(24)) divider_1 (.a(pcout), .b(24'h4), .out(pcout_chuyi4));  // open: upper, rem
  not not_1 (not_1_out, opcode[2]);
  not not_2 (not_2_out, opcode[3]);
  not not_3 (not_3_out, opcode[4]);
  not not_4 (not_4_out, opcode[5]);
  not not_5 (not_5_out, opcode[6]);
  not not_6 (not_6_out, funct3[0]);
  not not_7 (not_7_out, funct3[2]);
  assign bit_extender_1_out = {{20{funct7[6]}}, {funct7, imm}};  // Bit_Extender bit_extender_1
  not not_8 (not_8_out, opcode[2]);
  not not_9 (not_9_out, opcode[3]);
  not not_10 (not_10_out, opcode[4]);
  not not_11 (not_11_out, opcode[6]);
  not not_12 (not_12_out, funct3[0]);
  not not_13 (not_13_out, funct3[2]);
  assign bit_extender_2_out = {{20{funct7[6]}}, {funct7, imm4_0}};  // Bit_Extender bit_extender_2
  and and_1 (lwchengli, opcode[0], opcode[1], not_1_out, not_2_out, not_3_out, not_4_out, not_5_out, not_6_out, funct3[1], not_7_out);
  and and_2 (swchengli, opcode[0], opcode[1], not_8_out, not_9_out, not_10_out, opcode[5], not_11_out, not_12_out, funct3[1], not_13_out);
  not not_14 (not_14_out, opcode[2]);
  not not_15 (not_15_out, opcode[3]);
  not not_16 (not_16_out, opcode[4]);
  not not_17 (not_17_out, opcode[5]);
  not not_18 (not_18_out, opcode[6]);
  not not_19 (not_19_out, funct3[0]);
  not not_20 (not_20_out, funct3[1]);
  assign bit_extender_3_out = {{20{funct7[6]}}, {funct7, imm}};  // Bit_Extender bit_extender_3
  ROM #(.addrWidth(24), .dataWidth(32)) rom_1 (
    .addr(pcout_chuyi4), .data({funct7, imm, lui_imm, funct3, imm4_0, opcode}));
  Adder #(.width(32)) adder_2 (.a(rs1_read_result), .b(bit_extender_1_out), .out(lw_youxiaodizhi));  // open: cin, cout
  Adder #(.width(32)) adder_3 (.a(rs1_read_result), .b(bit_extender_2_out), .out(sw_youxiaodizhi));  // open: cin, cout
  and and_3 (lbuchengli, opcode[0], opcode[1], not_14_out, not_15_out, not_16_out, not_17_out, not_18_out, not_19_out, not_20_out, funct3[2]);
  Adder #(.width(32)) adder_4 (.a(bit_extender_3_out), .b(rs1_read_result), .out(lbu_youxiaodizhi));  // open: cin, cout
  Multiplexer #(.width(24)) multiplexer_1 (
    .in0(pc_plus4), .in1({jalr_output, 1'b0}), .out(multiplexer_1_out), .sel(jalrchengli));
  Multiplexer #(.select(2), .width(8)) multiplexer_2 (
    .in0(RAM_read_result[7:0]), .in1(RAM_read_result[15:8]), .in2(RAM_read_result[23:16]),
    .in3(RAM_read_result[31:24]), .out(lbu_after_boarden), .sel(lbu_youxiaodizhi[1:0]));
  Register #(.width(24)) register_1 (.D(multiplexer_1_out), .en(1'b1), .clk(CLK), .Q(pcout), .clr(button_1_out));
  Clock clock_1 (.out(CLK));
  Button button_1 (.out(button_1_out));
  assign bit_extender_4_out = {{20{funct7[6]}}, {funct7, imm4_0}};  // Bit_Extender bit_extender_4
  not not_21 (not_21_out, funct7[0]);
  not not_22 (not_22_out, funct7[1]);
  not not_23 (not_23_out, funct7[2]);
  not not_24 (not_24_out, funct7[3]);
  not not_25 (not_25_out, funct7[4]);
  not not_26 (not_26_out, funct7[5]);
  not not_27 (not_27_out, funct7[6]);
  not not_28 (not_28_out, opcode[3]);
  not not_29 (not_29_out, opcode[6]);
  Comparator #(.width(32)) comparator_1 (.a(32'h20040000), .b(sw_youxiaodizhi), .gt(comparator_1_gt));  // open: eq, lt
  Comparator #(.width(32)) comparator_2 (.a(32'h20000000), .b(sw_youxiaodizhi), .lt(comparator_2_lt));  // open: gt, eq
  not not_30 (not_30_out, opcode[2]);
  not not_31 (not_31_out, opcode[3]);
  not not_32 (not_32_out, opcode[4]);
  not not_33 (not_33_out, opcode[6]);
  not not_34 (not_34_out, funct3[0]);
  not not_35 (not_35_out, funct3[1]);
  not not_36 (not_36_out, funct3[2]);
  not not_37 (not_37_out, funct3[0]);
  not not_38 (not_38_out, funct3[1]);
  not not_39 (not_39_out, funct3[2]);
  not not_40 (not_40_out, opcode[2]);
  not not_41 (not_41_out, opcode[3]);
  not not_42 (not_42_out, opcode[5]);
  not not_43 (not_43_out, opcode[6]);
  not not_44 (not_44_out, opcode[3]);
  not not_45 (not_45_out, opcode[4]);
  Bit_Extender #(.in_width(32), .out_width(24), .\type ("zero")) bit_extender_5 (
    .in(rs1_read_result), .out(bit_extender_5_out));
  assign bit_extender_6_out = {{12{funct7[6]}}, {funct7, imm}};  // Bit_Extender bit_extender_6
  and and_4 (funct7is000, not_22_out, not_23_out, not_24_out, not_21_out, not_25_out, not_26_out, not_27_out);
  not not_46 (not_46_out, opcode[2]);
  not not_47 (not_47_out, opcode[3]);
  not not_48 (not_48_out, opcode[6]);
  and and_5 (luichengli, opcode[0], opcode[1], opcode[2], not_28_out, opcode[4], opcode[5], not_29_out);
  and and_6 (sbchengli, opcode[0], opcode[1], not_30_out, not_31_out, not_32_out, opcode[5], not_33_out, not_34_out, not_35_out, not_36_out);
  Adder #(.width(32)) adder_5 (
    .a(rs1_read_result), .b(bit_extender_4_out), .out({sb_youxiaodizhi, sb_choose}));  // open: cin, cout
  and and_7 (funct3is000, not_37_out, not_38_out, not_39_out);
  and and_8 (addichengli, opcode[0], opcode[1], not_40_out, not_41_out, opcode[4], not_42_out, not_43_out, funct3is000);
  assign imm_foraddi = {{20{funct7[6]}}, {funct7, imm}};  // Bit_Extender bit_extender_7
  Adder #(.width(32)) adder_6 (.a(rs1_read_result), .b(imm_foraddi), .out(adder_output));  // open: cin, cout
  and and_9 (jalrchengli, opcode[0], opcode[1], opcode[2], not_44_out, not_45_out, opcode[5], opcode[6], funct3is000);
  Adder #(.width(24)) adder_7 (
    .a(bit_extender_5_out), .b(bit_extender_6_out), .out({jalr_output, adder_7_out[0]}));  // open: cin, cout
  Adder #(.width(32)) adder_8 (.a(rs1_read_result), .b(rs2_read_result), .out(addzhilin_output));  // open: cin, cout
  and and_10 (isvga, comparator_1_gt, comparator_2_lt);
  and and_11 (addchengli, opcode[0], opcode[1], not_46_out, not_47_out, opcode[4], opcode[5], not_48_out, funct3is000, funct7is000);
  not not_49 (ismem, isvga);
  Decoder #(.enable("false"), .select(2)) decoder_1 (
    .out0(decoder_1_out0), .out1(decoder_1_out1), .out2(decoder_1_out2), .out3(decoder_1_out3),
    .sel(sb_choose));
  // RGB_Video #(.cursor("No Cursor"), .height(256), .width(256)) rgb_video_1: pin names not known; wires that end beside it: CLK, isvga, sw_youxiaodizhi[9:2], sw_youxiaodizhi[17:10], rs2_read_result[23:0]
  or or_1 (or_1_out, addichengli, jalrchengli, addchengli, luichengli, lwchengli, lbuchengli);
  or or_2 (or_2_out, swchengli, sbchengli);
  or or_3 (BE3, swchengli, decoder_1_out3);
  or or_4 (BE2, swchengli, decoder_1_out2);
  or or_5 (BE1, swchengli, decoder_1_out1);
  or or_6 (BE0, swchengli, decoder_1_out0);
  Decoder #(.select(4)) decoder_2 (
    .out0(GPR0_3[0]), .out1(GPR0_3[1]), .out2(GPR0_3[2]), .out3(GPR0_3[3]), .out4(GPR4_7[0]),
    .out5(GPR4_7[1]), .out6(GPR4_7[2]), .out7(GPR4_7[3]), .out8(GPR8_11[0]), .out9(GPR8_11[1]),
    .out10(GPR8_11[2]), .out11(GPR8_11[3]), .out12(GPR12_15[0]), .out13(GPR12_15[1]), .out14(GPR12_15[2]),
    .out15(GPR12_15[3]), .sel(imm4_0[3:0]), .en(or_1_out));
  and and_12 (and_12_out, ismem, or_2_out);
  assign bit_extender_8_out = {{8{1'b0}}, pc_plus4};  // Bit_Extender bit_extender_8
  four_2youxianbianmaqi four_2youxianbianmaqi_1 (
    .A2(sbchengli), .A0(swchengli), .Y1(four_2youxianbianmaqi_1_y0[1]), .Y0(four_2youxianbianmaqi_1_y0[0]));  // open: A3, A1, GS
  bianmaqi_zidianlu bianmaqi_zidianlu_1 (
    .I5(lbuchengli), .I4(lwchengli), .I3(luichengli), .I2(addchengli), .I1(jalrchengli), .I0(addichengli),
    .Y2(zhuangtai[2]), .Y1(zhuangtai[1]), .Y0(zhuangtai[0]));  // open: I15, I14, I13, I12, I11, I10, I9, I8, I7, I6, Y3
  four_2youxianbianmaqi four_2youxianbianmaqi_2 (
    .A3(addichengli), .A2(lbuchengli), .A1(lwchengli), .A0(swchengli), .Y1(four_2youxianbianmaqi_2_y0[1]),
    .Y0(four_2youxianbianmaqi_2_y0[0]));  // open: GS
  Multiplexer #(.select(2), .width(32)) multiplexer_3 (
    .in0(rs2_read_result),
    .in2({rs2_read_result[7:0], rs2_read_result[7:0], rs2_read_result[7:0], rs2_read_result[7:0]}),
    .out(multiplexer_3_out), .sel(four_2youxianbianmaqi_1_y0));  // open: in1, in3
  Multiplexer #(.select(2), .width(32)) multiplexer_4 (
    .in0(sw_youxiaodizhi), .in1(lw_youxiaodizhi), .in2(lbu_youxiaodizhi), .in3(adder_output),
    .out(multiplexer_4_out), .sel(four_2youxianbianmaqi_2_y0));
  RAM #(.addrWidth(24), .asyncread("true"), .byteenables("byteEnables"), .dataWidth(32), .\type ("nonvolatile")) ram_1 (
    .addr(multiplexer_4_out[25:2]), .we(and_12_out), .oe(1'b1), .clk(CLK), .din(multiplexer_3_out),
    .dout(RAM_read_result), .be3(BE3), .be2(BE2), .be1(BE1), .be0(BE0));
  Multiplexer #(.select(3), .width(32)) multiplexer_5 (
    .in0(adder_output), .in1(bit_extender_8_out), .in2(addzhilin_output),
    .in3({funct7, imm, lui_imm, funct3, {12{1'b0}}}), .in4(RAM_read_result),
    .in5({{24{1'b0}}, lbu_after_boarden}), .out(data_write), .sel(zhuangtai));  // open: in6, in7
  Register #(.width(32)) u_x0 (.D({32{1'b0}}), .en(1'b0), .clk(CLK), .Q(x0));  // open: clr
  Register #(.width(32)) tp (.D(data_write), .en(GPR4_7[0]), .clk(CLK), .Q(x4));  // open: clr
  Register #(.width(32)) s0_fp (.D(data_write), .en(GPR8_11[0]), .clk(CLK), .Q(x8));  // open: clr
  Register #(.width(32)) a2 (.D(data_write), .en(GPR12_15[0]), .clk(CLK), .Q(x12));  // open: clr
  Register #(.width(32)) ra (.D(data_write), .en(GPR0_3[1]), .clk(CLK), .Q(x0_1));  // open: clr
  Register #(.width(32)) t0 (.D(data_write), .en(GPR4_7[1]), .clk(CLK), .Q(x4_5));  // open: clr
  Register #(.width(32)) s1 (.D(data_write), .en(GPR8_11[1]), .clk(CLK), .Q(x8_9));  // open: clr
  Register #(.width(32)) a3 (.D(data_write), .en(GPR12_15[1]), .clk(CLK), .Q(x12_13));  // open: clr
  Register #(.width(32)) sp (.D(data_write), .en(GPR0_3[2]), .clk(CLK), .Q(x2));  // open: clr
  Register #(.width(32)) t1 (.D(data_write), .en(GPR4_7[2]), .clk(CLK), .Q(x6));  // open: clr
  Register #(.width(32)) a0 (.D(data_write), .en(GPR8_11[2]), .clk(CLK), .Q(x10));  // open: clr
  Register #(.width(32)) a4 (.D(data_write), .en(GPR12_15[2]), .clk(CLK), .Q(x14));  // open: clr
  Register #(.width(32)) gp (.D(data_write), .en(GPR0_3[3]), .clk(CLK), .Q(x2_3));  // open: clr
  Register #(.width(32)) t2 (.D(data_write), .en(GPR4_7[3]), .clk(CLK), .Q(x6_7));  // open: clr
  Register #(.width(32)) a1 (.D(data_write), .en(GPR8_11[3]), .clk(CLK), .Q(x10_11));  // open: clr
  Register #(.width(32)) a5 (.D(data_write), .en(GPR12_15[3]), .clk(CLK), .Q(x14_15));  // open: clr
  Multiplexer #(.select(4), .width(32)) multiplexer_6 (
    .in0(x0), .in1(x0_1), .in2(x2), .in3(x2_3), .in4(x4), .in5(x4_5), .in6(x6), .in7(x6_7), .in8(x8),
    .in9(x8_9), .in10(x10), .in11(x10_11), .in12(x12), .in13(x12_13), .in14(x14), .in15(x14_15),
    .out(rs1_read_result), .sel(lui_imm[18:15]));
  Multiplexer #(.select(4), .width(32)) multiplexer_7 (
    .in0(x0), .in1(x0_1), .in2(x2), .in3(x2_3), .in4(x4), .in5(x4_5), .in6(x6), .in7(x6_7), .in8(x8),
    .in9(x8_9), .in10(x10), .in11(x10_11), .in12(x12), .in13(x12_13), .in14(x14), .in15(x14_15),
    .out(rd_read_result), .sel(imm4_0[3:0]));
  Multiplexer #(.select(4), .width(32)) multiplexer_8 (
    .in0(x0), .in1(x0_1), .in2(x2), .in3(x2_3), .in4(x4), .in5(x4_5), .in6(x6), .in7(x6_7), .in8(x8),
    .in9(x8_9), .in10(x10), .in11(x10_11), .in12(x12), .in13(x12_13), .in14(x14), .in15(x14_15),
    .out(rs2_read_result), .sel(imm[3:0]));

  // Other names for the same wires on the sheet: rs2dibawei_write[7:0] = rs2_read_result[7:0];
  //   lbu_word_readresult[7:0] = lbu_after_boarden; word_choose[1:0] = lbu_youxiaodizhi[1:0];
  //   lui_imm (some bits) = {funct7, imm, funct3}; lui_imm_20[19:0] = {funct7, imm, lui_imm, funct3};
  //   rs1[4:0] = lui_imm; rd[4:0] = imm4_0; sb_imm[11:0] = {funct7, imm4_0}; sw_imm[11:0] = {funct7, imm4_0};
  //   imm[11:5] = funct7; imm_11_5[6:0] = funct7; rs2[4:0] = imm; sb_rs2[4:0] = imm; sb_youxiaodizhi[1:0] = sb_choose;
  //   x0_1[31:0] = x0; x1[31:0] = x0_1; x2_3[31:0] = x2; x3[31:0] = x2_3; x4_5[31:0] = x4; x5[31:0] = x4_5;
  //   x6_7[31:0] = x6; x7[31:0] = x6_7; x8_9[31:0] = x8; x9[31:0] = x8_9; x10_11[31:0] = x10; x11[31:0] = x10_11;
  //   x12_13[31:0] = x12; x13[31:0] = x12_13; x14_15[31:0] = x14; x15[31:0] = x14_15

  // Notes on the sheet:
  //   对lbu读到的结果进行零拓展
  //   此条件下lw指令成立并执行
  //   此条件下sw指令成立并执行
  //   此条件下lbu指令成立并执行
  //   选择读到哪个字
  //   contents of rom_1 (hex, n*v repeats v):
  //   413 93137 10113 10b7 dbc08093 80e7 fe012823 fea10923 fea12423 fe914203 fe4109a3 ff012783 f787b3
  //   f787b3 4b6b7 af868693 fdc10113 d787b3 10000713 f12423 10593 100793 b00513 2112023 12023 12223 e12623
  //   e12823 f10a23 10b7 a8408093 80e7 2012083 2410113 8067 ff410113 112423 10b7 a7c08093 80e7 513 1800093
  //   80e7 812083 513 c10113 8067 852583 feb12823 fe812e23 3437 80840413 ff014183 3401b3 1c183 ff114203
  //   440233 24203 4181b3 ff214203 440233 24203 4181b3 ff314203 440233 24203 4181b3 3237 80020213 320233
  //   24203 ffc12403 420233 420233 410233 11b7 86418193 fe312823 14800193 fe312623 fec22203 20067 1052703
  //   52683 452783 fe810113 e12423 112a23 812823 912623 fed12823 fef12623 13737 a0070713 fe012223 ff314203
  //   fe4102a3 fef14203 fe410223 fe412203 470233 24203 fe4105a3 ff214203 fe4102a3 fee14203 fe410223
  //   fe412203 470233 24203 fe410523 ff114203 fe4102a3 fed14203 fe410223 fe412203 470233 24203 fe4104a3
  //   ff014203 fe4102a3 fec14203 fe410223 fe412203 470233 24203 fe410423 fe812703 c52603 fee12823 fe812e23
  //   3437 80840413 ff014183 3401b3 1c183 ff114203 440233 24203 4181b3 ff214203 440233 24203 4181b3
  //   ff314203 440233 24203 4181b3 3237 80020213 320233 24203 ffc12403 420233 420233 410233 66800193
  //   fe312823 28800193 fe312623 fec22203 20067 c68733 10000513 fe812e23 fe912c23 fee12823 50413 ff012483
  //   fe812423 feb14183 3181b3 fe312423 fe914183 3181b3 fe912423 feb14203 420233 fe412423 fe914203 4181b3
  //   3181b3 fe312a23 fe912423 33237 90020213 feb14183 4181b3 1c183 fe3103a3 fea14183 4181b3 1c183
  //   fe310323 fe914183 4181b3 1c183 fe3102a3 fe814183 4181b3 1c183 fe310223 ff412183 fe412203 440233
  //   120213 fe412423 feb14203 420233 fe412423 fe914203 4181b3 3237 90820213 320233 ff812483 ffc12403
  //   24203 420233 420233 410233 11b7 86818193 fe312823 39000193 fe312623 fec22203 20067 812703 10000513
  //   e78733 fe812e23 fe912c23 fee12823 50413 ff012483 fe812423 feb14183 3181b3 fe312423 fe914183 3181b3
  //   fe912423 feb14203 420233 fe412423 fe914203 4181b3 3181b3 fe312a23 fe912423 33237 90020213 feb14183
  //   4181b3 1c183 fe3103a3 fea14183 4181b3 1c183 fe310323 fe914183 4181b3 1c183 fe3102a3 fe814183 4181b3
  //   1c183 fe310223 ff412183 fe412203 440233 120213 fe412423 feb14203 420233 fe412423 fe914203 4181b3
  //   3237 90820213 320233 ff812483 ffc12403 24203 420233 420233 410233 11b7 86818193 fe312823 49c00193
  //   fe312623 fec22203 20067 8*f787b3 d787b3 f787b3 f787b3 20000437 f40433 812783 c60633 c60633 fef12423
  //   feb14183 3181b3 fe312423 fe914183 fff78213 fe412423 feb14203 420233 fe412423 fe914203 4181b3 3237
  //   91820213 418233 24203 420233 420233 410233 65400193 fe312823 54000193 fe312623 fec22203 20067 493
  //   40513 b12223 c12023 10b7 de008093 80e7 12603 412583 812783 148493 40040413 c585b3 fef12823 fe912623
  //   fe812e23 fe912c23 2437 70040413 ff014183 340233 100193 320023 fec14183 3401b3 18023 24183 ff114483
  //   940233 100493 920023 fed14483 9404b3 48023 24483 9181b3 ff214483 940233 100493 920023 fee14483
  //   9404b3 48023 24483 9181b3 ff314483 940233 100493 920023 fef14483 9404b3 48023 24483 9181b3 3237
  //   80020213 320233 24203 ff812483 ffc12403 420233 420233 410233 65400193 fe312823 54400193 fe312623
  //   fec22203 20067 1412083 1012403 c12483 1810113 8067 10000713 fec12823 fee12623 fe812e23 fe912c23 2437
  //   70040413 ff014183 340233 100193 320023 fec14183 3401b3 18023 24183 ff114483 940233 100493 920023
  //   fed14483 9404b3 48023 24483 9181b3 ff214483 940233 100493 920023 fee14483 9404b3 48023 24483 9181b3
  //   ff314483 940233 100493 920023 fef14483 9404b3 48023 24483 9181b3 3237 80020213 320233 24203 ff812483
  //   ffc12403 420233 420233 410233 74c00193 fe312823 28800193 fe312623 fec22203 20067 812703 fee12823
  //   fec12623 fe812e23 fe912c23 2437 70040413 ff014183 340233 100193 320023 fec14183 3401b3 18023 24183
  //   ff114483 940233 100493 920023 fed14483 9404b3 48023 24483 9181b3 ff214483 940233 100493 920023
  //   fee14483 9404b3 48023 24483 9181b3 ff314483 940233 100493 920023 fef14483 9404b3 48023 24483 9181b3
  //   3237 80020213 320233 24203 ff812483 ffc12403 420233 420233 410233 11b7 83418193 fe312823 39000193
  //   fe312623 fec22203 20067 1012403 1412083 c12483 40637 20000537 1810113 1237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
  //   PC寄存器
  //   先把imm拆成add指令格式所需
  //   拼凑lui_imm的格式
  //   取rs2的低八位写入RAM对应位置
  //   此条件下lui指令成立并执行
  //   此条件下sb指令成立并执行
  //   此条件下addi指令成立并执行
  //   addi执行过程，Imm被拓展到32位进行加
  //   此条件下jalr指令成立并执行
  //   计算jalr指令要跳转的指令地址
  //   此条件下add指令成立并执行
  //   add执行过程
  //   将sb指令得到的低八位复制四份然后选择性写入
  //   lbu零拓展后的结果
  //   GPR写入逻辑
  //   目前暂定让x0的WE接地保证始终为0
  //   GPR
  //   GPR
  //   GPR
  //   GPR
endmodule
